// Logisim project transistor.circ as structural Verilog
module NAND2x1x1 (
  input  a,
  input  b,
  output out
);

  wire transistor_4_out;

  Transistor transistor_1 (.in(1'b1), .out(out), .gate(a));
  Transistor transistor_2 (.in(1'b1), .out(out), .gate(b));
  Transistor #(.\type ("n")) transistor_3 (.in(transistor_4_out), .out(out), .gate(a));
  Transistor #(.\type ("n")) transistor_4 (.in(1'b0), .out(transistor_4_out), .gate(b));
endmodule

module NAND3x1x1 (
  input  a,
  input  b,
  input  c,
  output out
);

  wire transistor_5_out, transistor_6_out;

  Transistor transistor_1 (.in(1'b1), .out(out), .gate(a));
  Transistor transistor_2 (.in(1'b1), .out(out), .gate(c));
  Transistor transistor_3 (.in(1'b1), .out(out), .gate(b));
  Transistor #(.\type ("n")) transistor_4 (.in(transistor_5_out), .out(out), .gate(a));
  Transistor #(.\type ("n")) transistor_5 (.in(transistor_6_out), .out(transistor_5_out), .gate(b));
  Transistor #(.\type ("n")) transistor_6 (.in(1'b0), .out(transistor_6_out), .gate(c));
endmodule

module NOR2x1x1 (
  input  a,
  input  b,
  output out
);

  wire transistor_1_out;

  Transistor transistor_1 (.in(1'b1), .out(transistor_1_out), .gate(a));
  Transistor transistor_2 (.in(transistor_1_out), .out(out), .gate(b));
  Transistor #(.\type ("n")) transistor_3 (.in(1'b0), .out(out), .gate(b));
  Transistor #(.\type ("n")) transistor_4 (.in(1'b0), .out(out), .gate(a));
endmodule

module NOR3x1x1 (
  input  a,
  input  b,
  input  c,
  output out
);

  wire transistor_3_out, transistor_4_out;

  Transistor #(.\type ("n")) transistor_1 (.in(1'b0), .out(out), .gate(b));
  Transistor #(.\type ("n")) transistor_2 (.in(1'b0), .out(out), .gate(a));
  Transistor transistor_3 (.in(1'b1), .out(transistor_3_out), .gate(a));
  Transistor transistor_4 (.in(transistor_3_out), .out(transistor_4_out), .gate(b));
  Transistor transistor_5 (.in(transistor_4_out), .out(out), .gate(c));
  Transistor #(.\type ("n")) transistor_6 (.in(1'b0), .out(out), .gate(c));
endmodule

module XOR2x1x1 (
  input  a,
  input  b,
  output out
);

  wire transistor_1_out, transistor_4_out, transistor_5_out, transistor_6_out, transistor_9_out,
       transistor_13_out, transistor_16_out;

  Transistor transistor_1 (.in(1'b1), .out(transistor_1_out), .gate(b));
  Transistor transistor_2 (.in(1'b1), .out(transistor_1_out), .gate(a));
  Transistor #(.\type ("n")) transistor_3 (.in(transistor_4_out), .out(transistor_1_out), .gate(a));
  Transistor #(.\type ("n")) transistor_4 (.in(1'b0), .out(transistor_4_out), .gate(b));
  Transistor transistor_5 (.in(1'b1), .out(transistor_5_out), .gate(a));
  Transistor transistor_6 (.in(1'b1), .out(transistor_6_out), .gate(transistor_1_out));
  Transistor transistor_7 (.in(1'b1), .out(transistor_5_out), .gate(transistor_1_out));
  Transistor #(.\type ("n")) transistor_8 (.in(transistor_9_out), .out(transistor_5_out), .gate(a));
  Transistor #(.\type ("n")) transistor_9 (.in(1'b0), .out(transistor_9_out), .gate(transistor_1_out));
  Transistor transistor_10 (.in(1'b1), .out(out), .gate(transistor_5_out));
  Transistor transistor_11 (.in(1'b1), .out(transistor_6_out), .gate(b));
  Transistor #(.\type ("n")) transistor_12 (.in(transistor_13_out), .out(transistor_6_out), .gate(transistor_1_out));
  Transistor #(.\type ("n")) transistor_13 (.in(1'b0), .out(transistor_13_out), .gate(b));
  Transistor transistor_14 (.in(1'b1), .out(out), .gate(transistor_6_out));
  Transistor #(.\type ("n")) transistor_15 (.in(transistor_16_out), .out(out), .gate(transistor_5_out));
  Transistor #(.\type ("n")) transistor_16 (.in(1'b0), .out(transistor_16_out), .gate(transistor_6_out));
endmodule

module NOT1x1x1 (
  input  in,
  output out
);

  Transistor transistor_1 (.in(1'b1), .out(out), .gate(in));
  Transistor #(.\type ("n")) transistor_2 (.in(1'b0), .out(out), .gate(in));
endmodule

module EN1x1x1 (
  input  in,
  input  en,
  output out
);

  wire transistor_1_out;

  Transistor #(.gate("br")) transistor_1 (.in(1'b1), .out(transistor_1_out), .gate(en));
  Transistor #(.\type ("n")) transistor_2 (.in(in), .out(out), .gate(en));
  Transistor #(.gate("br")) transistor_3 (.in(in), .out(out), .gate(transistor_1_out));
  Transistor #(.\type ("n"), .gate("br")) transistor_4 (.in(1'b0), .out(transistor_1_out), .gate(en));
endmodule

module MUX2x1x1 (
  input  a,
  input  sel,
  input  b,
  output out
);

  wire transistor_1_out;

  Transistor transistor_1 (.in(1'b1), .out(transistor_1_out), .gate(sel));
  Transistor #(.\type ("n")) transistor_2 (.in(1'b0), .out(transistor_1_out), .gate(sel));
  Transistor transistor_3 (.in(a), .out(out), .gate(sel));
  Transistor #(.\type ("n"), .gate("br")) transistor_4 (.in(a), .out(out), .gate(transistor_1_out));
  Transistor transistor_5 (.in(b), .out(out), .gate(transistor_1_out));
  Transistor #(.\type ("n"), .gate("br")) transistor_6 (.in(b), .out(out), .gate(sel));
endmodule

module MUX4x1x1 (
  input  a,
  input  b,
  input  c,
  input  d,
  input  sel0,
  input  sel1,
  output out
);

  wire transistor_1_out, transistor_3_out, transistor_5_out, transistor_9_out, transistor_15_out;

  Transistor transistor_1 (.in(1'b1), .out(transistor_1_out), .gate(sel0));
  Transistor #(.\type ("n")) transistor_2 (.in(1'b0), .out(transistor_1_out), .gate(sel0));
  Transistor transistor_3 (.in(1'b1), .out(transistor_3_out), .gate(sel0));
  Transistor #(.\type ("n")) transistor_4 (.in(1'b0), .out(transistor_3_out), .gate(sel0));
  Transistor transistor_5 (.in(a), .out(transistor_5_out), .gate(sel0));
  Transistor #(.\type ("n"), .gate("br")) transistor_6 (.in(a), .out(transistor_5_out), .gate(transistor_1_out));
  Transistor transistor_7 (.in(b), .out(transistor_5_out), .gate(transistor_1_out));
  Transistor #(.\type ("n"), .gate("br")) transistor_8 (.in(b), .out(transistor_5_out), .gate(sel0));
  Transistor transistor_9 (.in(c), .out(transistor_9_out), .gate(sel0));
  Transistor #(.\type ("n"), .gate("br")) transistor_10 (.in(c), .out(transistor_9_out), .gate(transistor_3_out));
  Transistor transistor_11 (.in(d), .out(transistor_9_out), .gate(transistor_3_out));
  Transistor #(.\type ("n"), .gate("br")) transistor_12 (.in(d), .out(transistor_9_out), .gate(sel0));
  Transistor transistor_13 (.in(transistor_5_out), .out(out), .gate(sel1));
  Transistor #(.\type ("n"), .gate("br")) transistor_14 (.in(transistor_5_out), .out(out), .gate(transistor_15_out));
  Transistor transistor_15 (.in(1'b1), .out(transistor_15_out), .gate(sel1));
  Transistor #(.\type ("n")) transistor_16 (.in(1'b0), .out(transistor_15_out), .gate(sel1));
  Transistor transistor_17 (.in(transistor_9_out), .out(out), .gate(transistor_15_out));
  Transistor #(.\type ("n"), .gate("br")) transistor_18 (.in(transistor_9_out), .out(out), .gate(sel1));
endmodule

module MUX8x1x1 (
  input  a,
  input  b,
  input  c,
  input  d,
  input  e,
  input  f,
  input  g,
  input  h,
  input  sel0,
  input  sel1,
  input  sel2,
  output out
);

  wire transistor_1_out, transistor_3_out, transistor_5_out, transistor_7_out, transistor_9_out,
       transistor_13_out, transistor_17_out, transistor_21_out, transistor_25_out, transistor_27_out,
       transistor_31_out, transistor_33_out, transistor_37_out;

  Transistor transistor_1 (.in(1'b1), .out(transistor_1_out), .gate(sel0));
  Transistor #(.\type ("n")) transistor_2 (.in(1'b0), .out(transistor_1_out), .gate(sel0));
  Transistor transistor_3 (.in(1'b1), .out(transistor_3_out), .gate(sel0));
  Transistor #(.\type ("n")) transistor_4 (.in(1'b0), .out(transistor_3_out), .gate(sel0));
  Transistor transistor_5 (.in(1'b1), .out(transistor_5_out), .gate(sel0));
  Transistor #(.\type ("n")) transistor_6 (.in(1'b0), .out(transistor_5_out), .gate(sel0));
  Transistor transistor_7 (.in(1'b1), .out(transistor_7_out), .gate(sel0));
  Transistor #(.\type ("n")) transistor_8 (.in(1'b0), .out(transistor_7_out), .gate(sel0));
  Transistor transistor_9 (.in(a), .out(transistor_9_out), .gate(sel0));
  Transistor #(.\type ("n"), .gate("br")) transistor_10 (.in(a), .out(transistor_9_out), .gate(transistor_1_out));
  Transistor transistor_11 (.in(b), .out(transistor_9_out), .gate(transistor_1_out));
  Transistor #(.\type ("n"), .gate("br")) transistor_12 (.in(b), .out(transistor_9_out), .gate(sel0));
  Transistor transistor_13 (.in(c), .out(transistor_13_out), .gate(sel0));
  Transistor #(.\type ("n"), .gate("br")) transistor_14 (.in(c), .out(transistor_13_out), .gate(transistor_3_out));
  Transistor transistor_15 (.in(d), .out(transistor_13_out), .gate(transistor_3_out));
  Transistor #(.\type ("n"), .gate("br")) transistor_16 (.in(d), .out(transistor_13_out), .gate(sel0));
  Transistor transistor_17 (.in(e), .out(transistor_17_out), .gate(sel0));
  Transistor #(.\type ("n"), .gate("br")) transistor_18 (.in(e), .out(transistor_17_out), .gate(transistor_5_out));
  Transistor transistor_19 (.in(f), .out(transistor_17_out), .gate(transistor_5_out));
  Transistor #(.\type ("n"), .gate("br")) transistor_20 (.in(f), .out(transistor_17_out), .gate(sel0));
  Transistor transistor_21 (.in(g), .out(transistor_21_out), .gate(sel0));
  Transistor #(.\type ("n"), .gate("br")) transistor_22 (.in(g), .out(transistor_21_out), .gate(transistor_7_out));
  Transistor transistor_23 (.in(h), .out(transistor_21_out), .gate(transistor_7_out));
  Transistor #(.\type ("n"), .gate("br")) transistor_24 (.in(h), .out(transistor_21_out), .gate(sel0));
  Transistor transistor_25 (.in(transistor_9_out), .out(transistor_25_out), .gate(sel1));
  Transistor #(.\type ("n"), .gate("br")) transistor_26 (
    .in(transistor_9_out), .out(transistor_25_out), .gate(transistor_27_out));
  Transistor transistor_27 (.in(1'b1), .out(transistor_27_out), .gate(sel1));
  Transistor #(.\type ("n")) transistor_28 (.in(1'b0), .out(transistor_27_out), .gate(sel1));
  Transistor transistor_29 (.in(transistor_13_out), .out(transistor_25_out), .gate(transistor_27_out));
  Transistor #(.\type ("n"), .gate("br")) transistor_30 (.in(transistor_13_out), .out(transistor_25_out), .gate(sel1));
  Transistor transistor_31 (.in(transistor_17_out), .out(transistor_31_out), .gate(sel1));
  Transistor #(.\type ("n"), .gate("br")) transistor_32 (
    .in(transistor_17_out), .out(transistor_31_out), .gate(transistor_33_out));
  Transistor transistor_33 (.in(1'b1), .out(transistor_33_out), .gate(sel1));
  Transistor #(.\type ("n")) transistor_34 (.in(1'b0), .out(transistor_33_out), .gate(sel1));
  Transistor transistor_35 (.in(transistor_21_out), .out(transistor_31_out), .gate(transistor_33_out));
  Transistor #(.\type ("n"), .gate("br")) transistor_36 (.in(transistor_21_out), .out(transistor_31_out), .gate(sel1));
  Transistor transistor_37 (.in(1'b1), .out(transistor_37_out), .gate(sel2));
  Transistor #(.\type ("n")) transistor_38 (.in(1'b0), .out(transistor_37_out), .gate(sel2));
  Transistor transistor_39 (.in(transistor_25_out), .out(out), .gate(sel2));
  Transistor #(.\type ("n"), .gate("br")) transistor_40 (.in(transistor_25_out), .out(out), .gate(transistor_37_out));
  Transistor transistor_41 (.in(transistor_31_out), .out(out), .gate(transistor_37_out));
  Transistor #(.\type ("n"), .gate("br")) transistor_42 (.in(transistor_31_out), .out(out), .gate(sel2));
endmodule

module DEC1x2x4 (
  input  in1,
  input  in0,
  output _00,
  output _01,
  output _10,
  output _11
);

  wire transistor_1_out, transistor_3_out, transistor_5_out, transistor_7_out, transistor_9_out,
       transistor_12_out, transistor_13_out, transistor_16_out, transistor_17_out, transistor_20_out,
       transistor_21_out, transistor_24_out;

  Transistor #(.\type ("n")) transistor_1 (.in(1'b0), .out(transistor_1_out), .gate(in0));
  Transistor transistor_2 (.in(1'b1), .out(transistor_1_out), .gate(in0));
  Transistor transistor_3 (.in(1'b1), .out(transistor_3_out), .gate(in1));
  Transistor #(.\type ("n")) transistor_4 (.in(1'b0), .out(transistor_3_out), .gate(in1));
  Transistor transistor_5 (.in(1'b1), .out(transistor_5_out), .gate(in1));
  Transistor #(.\type ("n")) transistor_6 (.in(1'b0), .out(transistor_5_out), .gate(in1));
  Transistor #(.\type ("n")) transistor_7 (.in(1'b0), .out(transistor_7_out), .gate(in0));
  Transistor transistor_8 (.in(1'b1), .out(transistor_7_out), .gate(in0));
  Transistor transistor_9 (.in(1'b1), .out(transistor_9_out), .gate(transistor_1_out));
  Transistor transistor_10 (.in(1'b1), .out(transistor_9_out), .gate(transistor_3_out));
  Transistor #(.\type ("n")) transistor_11 (.in(transistor_12_out), .out(transistor_9_out), .gate(transistor_1_out));
  Transistor #(.\type ("n")) transistor_12 (.in(1'b0), .out(transistor_12_out), .gate(transistor_3_out));
  Transistor transistor_13 (.in(1'b1), .out(transistor_13_out), .gate(transistor_5_out));
  Transistor transistor_14 (.in(1'b1), .out(transistor_13_out), .gate(in0));
  Transistor #(.\type ("n")) transistor_15 (.in(transistor_16_out), .out(transistor_13_out), .gate(in0));
  Transistor #(.\type ("n")) transistor_16 (.in(1'b0), .out(transistor_16_out), .gate(transistor_5_out));
  Transistor transistor_17 (.in(1'b1), .out(transistor_17_out), .gate(transistor_7_out));
  Transistor transistor_18 (.in(1'b1), .out(transistor_17_out), .gate(in1));
  Transistor #(.\type ("n")) transistor_19 (.in(transistor_20_out), .out(transistor_17_out), .gate(transistor_7_out));
  Transistor #(.\type ("n")) transistor_20 (.in(1'b0), .out(transistor_20_out), .gate(in1));
  Transistor transistor_21 (.in(1'b1), .out(transistor_21_out), .gate(in1));
  Transistor transistor_22 (.in(1'b1), .out(transistor_21_out), .gate(in0));
  Transistor #(.\type ("n")) transistor_23 (.in(transistor_24_out), .out(transistor_21_out), .gate(in0));
  Transistor #(.\type ("n")) transistor_24 (.in(1'b0), .out(transistor_24_out), .gate(in1));
  Transistor transistor_25 (.in(1'b1), .out(_00), .gate(transistor_9_out));
  Transistor #(.\type ("n")) transistor_26 (.in(1'b0), .out(_00), .gate(transistor_9_out));
  Transistor transistor_27 (.in(1'b1), .out(_01), .gate(transistor_13_out));
  Transistor #(.\type ("n")) transistor_28 (.in(1'b0), .out(_01), .gate(transistor_13_out));
  Transistor transistor_29 (.in(1'b1), .out(_10), .gate(transistor_17_out));
  Transistor #(.\type ("n")) transistor_30 (.in(1'b0), .out(_10), .gate(transistor_17_out));
  Transistor transistor_31 (.in(1'b1), .out(_11), .gate(transistor_21_out));
  Transistor #(.\type ("n")) transistor_32 (.in(1'b0), .out(_11), .gate(transistor_21_out));
endmodule

module DEC1x3x8 (
  input  in2,
  input  in1,
  input  in0,
  output _000,
  output _001,
  output _010,
  output _011,
  output _100,
  output _101,
  output _110,
  output _111
);

  wire transistor_1_out, transistor_2_out, transistor_3_out, transistor_4_out, transistor_5_out,
       transistor_6_out, transistor_7_out, transistor_8_out, transistor_9_out, transistor_10_out,
       transistor_11_out, transistor_12_out, transistor_25_out, transistor_27_out, transistor_29_out,
       transistor_31_out, transistor_33_out, transistor_35_out, transistor_37_out, transistor_39_out,
       transistor_43_out, transistor_44_out, transistor_47_out, transistor_48_out, transistor_51_out,
       transistor_52_out, transistor_55_out, transistor_56_out, transistor_59_out, transistor_60_out,
       transistor_63_out, transistor_64_out, transistor_67_out, transistor_68_out, transistor_71_out,
       transistor_72_out;

  Transistor transistor_1 (.in(1'b1), .out(transistor_1_out), .gate(in0));
  Transistor transistor_2 (.in(1'b1), .out(transistor_2_out), .gate(in1));
  Transistor transistor_3 (.in(1'b1), .out(transistor_3_out), .gate(in2));
  Transistor transistor_4 (.in(1'b1), .out(transistor_4_out), .gate(in1));
  Transistor transistor_5 (.in(1'b1), .out(transistor_5_out), .gate(in2));
  Transistor transistor_6 (.in(1'b1), .out(transistor_6_out), .gate(in0));
  Transistor transistor_7 (.in(1'b1), .out(transistor_7_out), .gate(in2));
  Transistor transistor_8 (.in(1'b1), .out(transistor_8_out), .gate(in2));
  Transistor transistor_9 (.in(1'b1), .out(transistor_9_out), .gate(in0));
  Transistor transistor_10 (.in(1'b1), .out(transistor_10_out), .gate(in1));
  Transistor transistor_11 (.in(1'b1), .out(transistor_11_out), .gate(in1));
  Transistor transistor_12 (.in(1'b1), .out(transistor_12_out), .gate(in0));
  Transistor #(.\type ("n")) transistor_13 (.in(1'b0), .out(transistor_1_out), .gate(in0));
  Transistor #(.\type ("n")) transistor_14 (.in(1'b0), .out(transistor_2_out), .gate(in1));
  Transistor #(.\type ("n")) transistor_15 (.in(1'b0), .out(transistor_3_out), .gate(in2));
  Transistor #(.\type ("n")) transistor_16 (.in(1'b0), .out(transistor_4_out), .gate(in1));
  Transistor #(.\type ("n")) transistor_17 (.in(1'b0), .out(transistor_5_out), .gate(in2));
  Transistor #(.\type ("n")) transistor_18 (.in(1'b0), .out(transistor_6_out), .gate(in0));
  Transistor #(.\type ("n")) transistor_19 (.in(1'b0), .out(transistor_7_out), .gate(in2));
  Transistor #(.\type ("n")) transistor_20 (.in(1'b0), .out(transistor_8_out), .gate(in2));
  Transistor #(.\type ("n")) transistor_21 (.in(1'b0), .out(transistor_9_out), .gate(in0));
  Transistor #(.\type ("n")) transistor_22 (.in(1'b0), .out(transistor_10_out), .gate(in1));
  Transistor #(.\type ("n")) transistor_23 (.in(1'b0), .out(transistor_11_out), .gate(in1));
  Transistor #(.\type ("n")) transistor_24 (.in(1'b0), .out(transistor_12_out), .gate(in0));
  Transistor transistor_25 (.in(1'b1), .out(transistor_25_out), .gate(transistor_1_out));
  Transistor transistor_26 (.in(1'b1), .out(transistor_25_out), .gate(transistor_2_out));
  Transistor transistor_27 (.in(1'b1), .out(transistor_27_out), .gate(transistor_4_out));
  Transistor transistor_28 (.in(1'b1), .out(transistor_27_out), .gate(in0));
  Transistor transistor_29 (.in(1'b1), .out(transistor_29_out), .gate(transistor_6_out));
  Transistor transistor_30 (.in(1'b1), .out(transistor_29_out), .gate(in1));
  Transistor transistor_31 (.in(1'b1), .out(transistor_31_out), .gate(in0));
  Transistor transistor_32 (.in(1'b1), .out(transistor_31_out), .gate(in1));
  Transistor transistor_33 (.in(1'b1), .out(transistor_33_out), .gate(transistor_9_out));
  Transistor transistor_34 (.in(1'b1), .out(transistor_33_out), .gate(transistor_10_out));
  Transistor transistor_35 (.in(1'b1), .out(transistor_35_out), .gate(in0));
  Transistor transistor_36 (.in(1'b1), .out(transistor_35_out), .gate(transistor_11_out));
  Transistor transistor_37 (.in(1'b1), .out(transistor_37_out), .gate(in1));
  Transistor transistor_38 (.in(1'b1), .out(transistor_37_out), .gate(transistor_12_out));
  Transistor transistor_39 (.in(1'b1), .out(transistor_39_out), .gate(in0));
  Transistor transistor_40 (.in(1'b1), .out(transistor_39_out), .gate(in1));
  Transistor transistor_41 (.in(1'b1), .out(transistor_25_out), .gate(transistor_3_out));
  Transistor #(.\type ("n")) transistor_42 (.in(transistor_43_out), .out(transistor_25_out), .gate(transistor_1_out));
  Transistor #(.\type ("n")) transistor_43 (.in(transistor_44_out), .out(transistor_43_out), .gate(transistor_2_out));
  Transistor #(.\type ("n")) transistor_44 (.in(1'b0), .out(transistor_44_out), .gate(transistor_3_out));
  Transistor transistor_45 (.in(1'b1), .out(transistor_27_out), .gate(transistor_5_out));
  Transistor #(.\type ("n")) transistor_46 (.in(transistor_47_out), .out(transistor_27_out), .gate(in0));
  Transistor #(.\type ("n")) transistor_47 (.in(transistor_48_out), .out(transistor_47_out), .gate(transistor_4_out));
  Transistor #(.\type ("n")) transistor_48 (.in(1'b0), .out(transistor_48_out), .gate(transistor_5_out));
  Transistor transistor_49 (.in(1'b1), .out(transistor_29_out), .gate(transistor_7_out));
  Transistor #(.\type ("n")) transistor_50 (.in(transistor_51_out), .out(transistor_29_out), .gate(transistor_6_out));
  Transistor #(.\type ("n")) transistor_51 (.in(transistor_52_out), .out(transistor_51_out), .gate(in1));
  Transistor #(.\type ("n")) transistor_52 (.in(1'b0), .out(transistor_52_out), .gate(transistor_7_out));
  Transistor transistor_53 (.in(1'b1), .out(transistor_31_out), .gate(transistor_8_out));
  Transistor #(.\type ("n")) transistor_54 (.in(transistor_55_out), .out(transistor_31_out), .gate(in0));
  Transistor #(.\type ("n")) transistor_55 (.in(transistor_56_out), .out(transistor_55_out), .gate(in1));
  Transistor #(.\type ("n")) transistor_56 (.in(1'b0), .out(transistor_56_out), .gate(transistor_8_out));
  Transistor transistor_57 (.in(1'b1), .out(transistor_33_out), .gate(in2));
  Transistor #(.\type ("n")) transistor_58 (.in(transistor_59_out), .out(transistor_33_out), .gate(transistor_9_out));
  Transistor #(.\type ("n")) transistor_59 (.in(transistor_60_out), .out(transistor_59_out), .gate(transistor_10_out));
  Transistor #(.\type ("n")) transistor_60 (.in(1'b0), .out(transistor_60_out), .gate(in2));
  Transistor transistor_61 (.in(1'b1), .out(transistor_35_out), .gate(in2));
  Transistor #(.\type ("n")) transistor_62 (.in(transistor_63_out), .out(transistor_35_out), .gate(in0));
  Transistor #(.\type ("n")) transistor_63 (.in(transistor_64_out), .out(transistor_63_out), .gate(transistor_11_out));
  Transistor #(.\type ("n")) transistor_64 (.in(1'b0), .out(transistor_64_out), .gate(in2));
  Transistor transistor_65 (.in(1'b1), .out(transistor_37_out), .gate(in2));
  Transistor #(.\type ("n")) transistor_66 (.in(transistor_67_out), .out(transistor_37_out), .gate(transistor_12_out));
  Transistor #(.\type ("n")) transistor_67 (.in(transistor_68_out), .out(transistor_67_out), .gate(in1));
  Transistor #(.\type ("n")) transistor_68 (.in(1'b0), .out(transistor_68_out), .gate(in2));
  Transistor transistor_69 (.in(1'b1), .out(transistor_39_out), .gate(in2));
  Transistor #(.\type ("n")) transistor_70 (.in(transistor_71_out), .out(transistor_39_out), .gate(in0));
  Transistor #(.\type ("n")) transistor_71 (.in(transistor_72_out), .out(transistor_71_out), .gate(in1));
  Transistor #(.\type ("n")) transistor_72 (.in(1'b0), .out(transistor_72_out), .gate(in2));
  Transistor transistor_73 (.in(1'b1), .out(_000), .gate(transistor_25_out));
  Transistor #(.\type ("n")) transistor_74 (.in(1'b0), .out(_000), .gate(transistor_25_out));
  Transistor transistor_75 (.in(1'b1), .out(_001), .gate(transistor_27_out));
  Transistor #(.\type ("n")) transistor_76 (.in(1'b0), .out(_001), .gate(transistor_27_out));
  Transistor transistor_77 (.in(1'b1), .out(_010), .gate(transistor_29_out));
  Transistor #(.\type ("n")) transistor_78 (.in(1'b0), .out(_010), .gate(transistor_29_out));
  Transistor transistor_79 (.in(1'b1), .out(_011), .gate(transistor_31_out));
  Transistor #(.\type ("n")) transistor_80 (.in(1'b0), .out(_011), .gate(transistor_31_out));
  Transistor transistor_81 (.in(1'b1), .out(_100), .gate(transistor_33_out));
  Transistor #(.\type ("n")) transistor_82 (.in(1'b0), .out(_100), .gate(transistor_33_out));
  Transistor transistor_83 (.in(1'b1), .out(_101), .gate(transistor_35_out));
  Transistor #(.\type ("n")) transistor_84 (.in(1'b0), .out(_101), .gate(transistor_35_out));
  Transistor transistor_85 (.in(1'b1), .out(_110), .gate(transistor_37_out));
  Transistor #(.\type ("n")) transistor_86 (.in(1'b0), .out(_110), .gate(transistor_37_out));
  Transistor transistor_87 (.in(1'b1), .out(_111), .gate(transistor_39_out));
  Transistor #(.\type ("n")) transistor_88 (.in(1'b0), .out(_111), .gate(transistor_39_out));
endmodule

module DLATCH (
  input  in,
  input  w,
  input  rst,
  input  r,
  input  in_2,
  input  w_2,
  input  rst_2,
  output out,
  output out_2
);

  wire transistor_1_out, transistor_3_out, transistor_9_out, transistor_13_out, transistor_15_out,
       transistor_19_out, transistor_21_out, transistor_25_out;

  Transistor transistor_1 (.in(1'b1), .out(transistor_1_out), .gate(w_2));
  Transistor #(.\type ("n")) transistor_2 (.in(1'b0), .out(transistor_1_out), .gate(w_2));
  Transistor #(.\type ("n")) transistor_3 (.in(in), .out(transistor_3_out), .gate(w_2));
  Transistor #(.gate("br")) transistor_4 (.in(in), .out(transistor_3_out), .gate(transistor_1_out));
  Transistor #(.\type ("n")) transistor_5 (.in(out), .out(transistor_3_out), .gate(transistor_1_out));
  Transistor #(.gate("br")) transistor_6 (.in(out), .out(transistor_3_out), .gate(w_2));
  Transistor #(.\type ("n")) transistor_7 (.in(1'b0), .out(out), .gate(rst_2));
  Transistor #(.gate("br")) transistor_8 (.in(1'b0), .out(out), .gate(transistor_9_out));
  Transistor transistor_9 (.in(1'b1), .out(transistor_9_out), .gate(rst_2));
  Transistor #(.\type ("n")) transistor_10 (.in(1'b0), .out(transistor_9_out), .gate(rst_2));
  Transistor #(.\type ("n")) transistor_11 (.in(transistor_3_out), .out(out), .gate(transistor_9_out));
  Transistor #(.gate("br")) transistor_12 (.in(transistor_3_out), .out(out), .gate(rst_2));
  Transistor transistor_13 (.in(1'b1), .out(transistor_13_out), .gate(w));
  Transistor #(.\type ("n")) transistor_14 (.in(1'b0), .out(transistor_13_out), .gate(w));
  Transistor #(.\type ("n")) transistor_15 (.in(in_2), .out(transistor_15_out), .gate(w));
  Transistor #(.gate("br")) transistor_16 (.in(in_2), .out(transistor_15_out), .gate(transistor_13_out));
  Transistor #(.\type ("n")) transistor_17 (.in(transistor_21_out), .out(transistor_15_out), .gate(transistor_13_out));
  Transistor #(.gate("br")) transistor_18 (.in(transistor_21_out), .out(transistor_15_out), .gate(w));
  Transistor transistor_19 (.in(1'b1), .out(transistor_19_out), .gate(rst));
  Transistor #(.\type ("n")) transistor_20 (.in(1'b0), .out(transistor_19_out), .gate(rst));
  Transistor #(.\type ("n")) transistor_21 (.in(1'b0), .out(transistor_21_out), .gate(rst));
  Transistor #(.gate("br")) transistor_22 (.in(1'b0), .out(transistor_21_out), .gate(transistor_19_out));
  Transistor #(.\type ("n")) transistor_23 (.in(transistor_15_out), .out(transistor_21_out), .gate(transistor_19_out));
  Transistor #(.gate("br")) transistor_24 (.in(transistor_15_out), .out(transistor_21_out), .gate(rst));
  Transistor transistor_25 (.in(1'b1), .out(transistor_25_out), .gate(r));
  Transistor #(.\type ("n")) transistor_26 (.in(1'b0), .out(transistor_25_out), .gate(r));
  Transistor transistor_27 (.in(transistor_21_out), .out(out_2), .gate(transistor_25_out));
  Transistor #(.\type ("n"), .gate("br")) transistor_28 (.in(transistor_21_out), .out(out_2), .gate(r));
endmodule

module EN8x1x8 (
  input  in0,
  input  in1,
  input  in2,
  input  in3,
  input  in4,
  input  in5,
  input  in6,
  input  in7,
  input  en,
  output out0,
  output out1,
  output out2,
  output out3,
  output out4,
  output out6,
  output out6_2,
  output out7
);

  wire transistor_1_out, transistor_2_out, transistor_3_out, transistor_4_out, transistor_5_out,
       transistor_6_out, transistor_7_out, transistor_8_out;

  Transistor #(.gate("br")) transistor_1 (.in(1'b1), .out(transistor_1_out), .gate(en));
  Transistor #(.gate("br")) transistor_2 (.in(1'b1), .out(transistor_2_out), .gate(en));
  Transistor #(.gate("br")) transistor_3 (.in(1'b1), .out(transistor_3_out), .gate(en));
  Transistor #(.gate("br")) transistor_4 (.in(1'b1), .out(transistor_4_out), .gate(en));
  Transistor #(.gate("br")) transistor_5 (.in(1'b1), .out(transistor_5_out), .gate(en));
  Transistor #(.gate("br")) transistor_6 (.in(1'b1), .out(transistor_6_out), .gate(en));
  Transistor #(.gate("br")) transistor_7 (.in(1'b1), .out(transistor_7_out), .gate(en));
  Transistor #(.gate("br")) transistor_8 (.in(1'b1), .out(transistor_8_out), .gate(en));
  Transistor #(.\type ("n")) transistor_9 (.in(in0), .out(out0), .gate(en));
  Transistor #(.gate("br")) transistor_10 (.in(in0), .out(out0), .gate(transistor_1_out));
  Transistor #(.\type ("n"), .gate("br")) transistor_11 (.in(1'b0), .out(transistor_1_out), .gate(en));
  Transistor #(.\type ("n")) transistor_12 (.in(in1), .out(out1), .gate(en));
  Transistor #(.gate("br")) transistor_13 (.in(in1), .out(out1), .gate(transistor_2_out));
  Transistor #(.\type ("n"), .gate("br")) transistor_14 (.in(1'b0), .out(transistor_2_out), .gate(en));
  Transistor #(.\type ("n")) transistor_15 (.in(in2), .out(out2), .gate(en));
  Transistor #(.gate("br")) transistor_16 (.in(in2), .out(out2), .gate(transistor_3_out));
  Transistor #(.\type ("n"), .gate("br")) transistor_17 (.in(1'b0), .out(transistor_3_out), .gate(en));
  Transistor #(.\type ("n")) transistor_18 (.in(in3), .out(out3), .gate(en));
  Transistor #(.gate("br")) transistor_19 (.in(in3), .out(out3), .gate(transistor_4_out));
  Transistor #(.\type ("n"), .gate("br")) transistor_20 (.in(1'b0), .out(transistor_4_out), .gate(en));
  Transistor #(.\type ("n")) transistor_21 (.in(in4), .out(out4), .gate(en));
  Transistor #(.gate("br")) transistor_22 (.in(in4), .out(out4), .gate(transistor_5_out));
  Transistor #(.\type ("n"), .gate("br")) transistor_23 (.in(1'b0), .out(transistor_5_out), .gate(en));
  Transistor #(.\type ("n")) transistor_24 (.in(in5), .out(out6), .gate(en));
  Transistor #(.gate("br")) transistor_25 (.in(in5), .out(out6), .gate(transistor_6_out));
  Transistor #(.\type ("n"), .gate("br")) transistor_26 (.in(1'b0), .out(transistor_6_out), .gate(en));
  Transistor #(.\type ("n")) transistor_27 (.in(in6), .out(out6_2), .gate(en));
  Transistor #(.gate("br")) transistor_28 (.in(in6), .out(out6_2), .gate(transistor_7_out));
  Transistor #(.\type ("n"), .gate("br")) transistor_29 (.in(1'b0), .out(transistor_7_out), .gate(en));
  Transistor #(.\type ("n")) transistor_30 (.in(in7), .out(out7), .gate(en));
  Transistor #(.gate("br")) transistor_31 (.in(in7), .out(out7), .gate(transistor_8_out));
  Transistor #(.\type ("n"), .gate("br")) transistor_32 (.in(1'b0), .out(transistor_8_out), .gate(en));
endmodule

module REG1x4x1 (
  input  in0,
  input  in1,
  input  in2,
  input  in3,
  input  r,
  input  w,
  input  rst,
  output out0,
  output out1,
  output out2,
  output out3
);

  wire transistor_1_out, transistor_3_out, transistor_5_out, transistor_7_out, transistor_9_out,
       transistor_11_out, transistor_15_out, transistor_17_out, transistor_21_out, transistor_23_out,
       transistor_27_out, transistor_29_out, transistor_33_out, transistor_37_out, transistor_41_out,
       transistor_45_out, transistor_49_out, transistor_50_out, transistor_51_out, transistor_52_out;

  Transistor transistor_1 (.in(1'b1), .out(transistor_1_out), .gate(w));
  Transistor #(.\type ("n")) transistor_2 (.in(1'b0), .out(transistor_1_out), .gate(w));
  Transistor transistor_3 (.in(1'b1), .out(transistor_3_out), .gate(w));
  Transistor #(.\type ("n")) transistor_4 (.in(1'b0), .out(transistor_3_out), .gate(w));
  Transistor transistor_5 (.in(1'b1), .out(transistor_5_out), .gate(w));
  Transistor #(.\type ("n")) transistor_6 (.in(1'b0), .out(transistor_5_out), .gate(w));
  Transistor transistor_7 (.in(1'b1), .out(transistor_7_out), .gate(w));
  Transistor #(.\type ("n")) transistor_8 (.in(1'b0), .out(transistor_7_out), .gate(w));
  Transistor #(.\type ("n")) transistor_9 (.in(in0), .out(transistor_9_out), .gate(w));
  Transistor #(.gate("br")) transistor_10 (.in(in0), .out(transistor_9_out), .gate(transistor_1_out));
  Transistor transistor_11 (.in(1'b1), .out(transistor_11_out), .gate(rst));
  Transistor #(.\type ("n")) transistor_12 (.in(1'b0), .out(transistor_11_out), .gate(rst));
  Transistor #(.\type ("n")) transistor_13 (.in(transistor_33_out), .out(transistor_9_out), .gate(transistor_1_out));
  Transistor #(.gate("br")) transistor_14 (.in(transistor_33_out), .out(transistor_9_out), .gate(w));
  Transistor #(.\type ("n")) transistor_15 (.in(in1), .out(transistor_15_out), .gate(w));
  Transistor #(.gate("br")) transistor_16 (.in(in1), .out(transistor_15_out), .gate(transistor_3_out));
  Transistor transistor_17 (.in(1'b1), .out(transistor_17_out), .gate(rst));
  Transistor #(.\type ("n")) transistor_18 (.in(1'b0), .out(transistor_17_out), .gate(rst));
  Transistor #(.\type ("n")) transistor_19 (.in(transistor_37_out), .out(transistor_15_out), .gate(transistor_3_out));
  Transistor #(.gate("br")) transistor_20 (.in(transistor_37_out), .out(transistor_15_out), .gate(w));
  Transistor #(.\type ("n")) transistor_21 (.in(in2), .out(transistor_21_out), .gate(w));
  Transistor #(.gate("br")) transistor_22 (.in(in2), .out(transistor_21_out), .gate(transistor_5_out));
  Transistor transistor_23 (.in(1'b1), .out(transistor_23_out), .gate(rst));
  Transistor #(.\type ("n")) transistor_24 (.in(1'b0), .out(transistor_23_out), .gate(rst));
  Transistor #(.\type ("n")) transistor_25 (.in(transistor_41_out), .out(transistor_21_out), .gate(transistor_5_out));
  Transistor #(.gate("br")) transistor_26 (.in(transistor_41_out), .out(transistor_21_out), .gate(w));
  Transistor #(.\type ("n")) transistor_27 (.in(in3), .out(transistor_27_out), .gate(w));
  Transistor #(.gate("br")) transistor_28 (.in(in3), .out(transistor_27_out), .gate(transistor_7_out));
  Transistor transistor_29 (.in(1'b1), .out(transistor_29_out), .gate(rst));
  Transistor #(.\type ("n")) transistor_30 (.in(1'b0), .out(transistor_29_out), .gate(rst));
  Transistor #(.\type ("n")) transistor_31 (.in(transistor_45_out), .out(transistor_27_out), .gate(transistor_7_out));
  Transistor #(.gate("br")) transistor_32 (.in(transistor_45_out), .out(transistor_27_out), .gate(w));
  Transistor #(.\type ("n")) transistor_33 (.in(1'b0), .out(transistor_33_out), .gate(rst));
  Transistor #(.gate("br")) transistor_34 (.in(1'b0), .out(transistor_33_out), .gate(transistor_11_out));
  Transistor #(.\type ("n")) transistor_35 (.in(transistor_9_out), .out(transistor_33_out), .gate(transistor_11_out));
  Transistor #(.gate("br")) transistor_36 (.in(transistor_9_out), .out(transistor_33_out), .gate(rst));
  Transistor #(.\type ("n")) transistor_37 (.in(1'b0), .out(transistor_37_out), .gate(rst));
  Transistor #(.gate("br")) transistor_38 (.in(1'b0), .out(transistor_37_out), .gate(transistor_17_out));
  Transistor #(.\type ("n")) transistor_39 (.in(transistor_15_out), .out(transistor_37_out), .gate(transistor_17_out));
  Transistor #(.gate("br")) transistor_40 (.in(transistor_15_out), .out(transistor_37_out), .gate(rst));
  Transistor #(.\type ("n")) transistor_41 (.in(1'b0), .out(transistor_41_out), .gate(rst));
  Transistor #(.gate("br")) transistor_42 (.in(1'b0), .out(transistor_41_out), .gate(transistor_23_out));
  Transistor #(.\type ("n")) transistor_43 (.in(transistor_21_out), .out(transistor_41_out), .gate(transistor_23_out));
  Transistor #(.gate("br")) transistor_44 (.in(transistor_21_out), .out(transistor_41_out), .gate(rst));
  Transistor #(.\type ("n")) transistor_45 (.in(1'b0), .out(transistor_45_out), .gate(rst));
  Transistor #(.gate("br")) transistor_46 (.in(1'b0), .out(transistor_45_out), .gate(transistor_29_out));
  Transistor #(.\type ("n")) transistor_47 (.in(transistor_27_out), .out(transistor_45_out), .gate(transistor_29_out));
  Transistor #(.gate("br")) transistor_48 (.in(transistor_27_out), .out(transistor_45_out), .gate(rst));
  Transistor #(.gate("br")) transistor_49 (.in(1'b1), .out(transistor_49_out), .gate(r));
  Transistor #(.gate("br")) transistor_50 (.in(1'b1), .out(transistor_50_out), .gate(r));
  Transistor #(.gate("br")) transistor_51 (.in(1'b1), .out(transistor_51_out), .gate(r));
  Transistor #(.gate("br")) transistor_52 (.in(1'b1), .out(transistor_52_out), .gate(r));
  Transistor #(.\type ("n")) transistor_53 (.in(transistor_33_out), .out(out0), .gate(r));
  Transistor #(.gate("br")) transistor_54 (.in(transistor_33_out), .out(out0), .gate(transistor_49_out));
  Transistor #(.\type ("n"), .gate("br")) transistor_55 (.in(1'b0), .out(transistor_49_out), .gate(r));
  Transistor #(.\type ("n")) transistor_56 (.in(transistor_37_out), .out(out1), .gate(r));
  Transistor #(.gate("br")) transistor_57 (.in(transistor_37_out), .out(out1), .gate(transistor_50_out));
  Transistor #(.\type ("n"), .gate("br")) transistor_58 (.in(1'b0), .out(transistor_50_out), .gate(r));
  Transistor #(.\type ("n")) transistor_59 (.in(transistor_41_out), .out(out2), .gate(r));
  Transistor #(.gate("br")) transistor_60 (.in(transistor_41_out), .out(out2), .gate(transistor_51_out));
  Transistor #(.\type ("n"), .gate("br")) transistor_61 (.in(1'b0), .out(transistor_51_out), .gate(r));
  Transistor #(.\type ("n")) transistor_62 (.in(transistor_45_out), .out(out3), .gate(r));
  Transistor #(.gate("br")) transistor_63 (.in(transistor_45_out), .out(out3), .gate(transistor_52_out));
  Transistor #(.\type ("n"), .gate("br")) transistor_64 (.in(1'b0), .out(transistor_52_out), .gate(r));
endmodule

module REG1x8x1 (
  input  in0,
  input  in1,
  input  in2,
  input  in3,
  input  in4,
  input  in5,
  input  in6,
  input  in7,
  input  r,
  input  w,
  input  rst,
  output out0,
  output out1,
  output out2,
  output out3,
  output out4,
  output out5,
  output out6,
  output out7
);

  wire transistor_1_out, transistor_3_out, transistor_5_out, transistor_7_out, transistor_9_out,
       transistor_11_out, transistor_13_out, transistor_15_out, transistor_17_out, transistor_19_out,
       transistor_23_out, transistor_25_out, transistor_29_out, transistor_31_out, transistor_35_out,
       transistor_37_out, transistor_41_out, transistor_43_out, transistor_47_out, transistor_49_out,
       transistor_53_out, transistor_55_out, transistor_59_out, transistor_61_out, transistor_65_out,
       transistor_69_out, transistor_73_out, transistor_77_out, transistor_81_out, transistor_85_out,
       transistor_89_out, transistor_93_out, transistor_97_out, transistor_98_out, transistor_99_out,
       transistor_100_out, transistor_101_out, transistor_102_out, transistor_103_out, transistor_104_out;

  Transistor transistor_1 (.in(1'b1), .out(transistor_1_out), .gate(w));
  Transistor #(.\type ("n")) transistor_2 (.in(1'b0), .out(transistor_1_out), .gate(w));
  Transistor transistor_3 (.in(1'b1), .out(transistor_3_out), .gate(w));
  Transistor #(.\type ("n")) transistor_4 (.in(1'b0), .out(transistor_3_out), .gate(w));
  Transistor transistor_5 (.in(1'b1), .out(transistor_5_out), .gate(w));
  Transistor #(.\type ("n")) transistor_6 (.in(1'b0), .out(transistor_5_out), .gate(w));
  Transistor transistor_7 (.in(1'b1), .out(transistor_7_out), .gate(w));
  Transistor #(.\type ("n")) transistor_8 (.in(1'b0), .out(transistor_7_out), .gate(w));
  Transistor transistor_9 (.in(1'b1), .out(transistor_9_out), .gate(w));
  Transistor #(.\type ("n")) transistor_10 (.in(1'b0), .out(transistor_9_out), .gate(w));
  Transistor transistor_11 (.in(1'b1), .out(transistor_11_out), .gate(w));
  Transistor #(.\type ("n")) transistor_12 (.in(1'b0), .out(transistor_11_out), .gate(w));
  Transistor transistor_13 (.in(1'b1), .out(transistor_13_out), .gate(w));
  Transistor #(.\type ("n")) transistor_14 (.in(1'b0), .out(transistor_13_out), .gate(w));
  Transistor transistor_15 (.in(1'b1), .out(transistor_15_out), .gate(w));
  Transistor #(.\type ("n")) transistor_16 (.in(1'b0), .out(transistor_15_out), .gate(w));
  Transistor #(.\type ("n")) transistor_17 (.in(in0), .out(transistor_17_out), .gate(w));
  Transistor #(.gate("br")) transistor_18 (.in(in0), .out(transistor_17_out), .gate(transistor_1_out));
  Transistor transistor_19 (.in(1'b1), .out(transistor_19_out), .gate(rst));
  Transistor #(.\type ("n")) transistor_20 (.in(1'b0), .out(transistor_19_out), .gate(rst));
  Transistor #(.\type ("n")) transistor_21 (.in(transistor_65_out), .out(transistor_17_out), .gate(transistor_1_out));
  Transistor #(.gate("br")) transistor_22 (.in(transistor_65_out), .out(transistor_17_out), .gate(w));
  Transistor #(.\type ("n")) transistor_23 (.in(in1), .out(transistor_23_out), .gate(w));
  Transistor #(.gate("br")) transistor_24 (.in(in1), .out(transistor_23_out), .gate(transistor_3_out));
  Transistor transistor_25 (.in(1'b1), .out(transistor_25_out), .gate(rst));
  Transistor #(.\type ("n")) transistor_26 (.in(1'b0), .out(transistor_25_out), .gate(rst));
  Transistor #(.\type ("n")) transistor_27 (.in(transistor_69_out), .out(transistor_23_out), .gate(transistor_3_out));
  Transistor #(.gate("br")) transistor_28 (.in(transistor_69_out), .out(transistor_23_out), .gate(w));
  Transistor #(.\type ("n")) transistor_29 (.in(in2), .out(transistor_29_out), .gate(w));
  Transistor #(.gate("br")) transistor_30 (.in(in2), .out(transistor_29_out), .gate(transistor_5_out));
  Transistor transistor_31 (.in(1'b1), .out(transistor_31_out), .gate(rst));
  Transistor #(.\type ("n")) transistor_32 (.in(1'b0), .out(transistor_31_out), .gate(rst));
  Transistor #(.\type ("n")) transistor_33 (.in(transistor_73_out), .out(transistor_29_out), .gate(transistor_5_out));
  Transistor #(.gate("br")) transistor_34 (.in(transistor_73_out), .out(transistor_29_out), .gate(w));
  Transistor #(.\type ("n")) transistor_35 (.in(in3), .out(transistor_35_out), .gate(w));
  Transistor #(.gate("br")) transistor_36 (.in(in3), .out(transistor_35_out), .gate(transistor_7_out));
  Transistor transistor_37 (.in(1'b1), .out(transistor_37_out), .gate(rst));
  Transistor #(.\type ("n")) transistor_38 (.in(1'b0), .out(transistor_37_out), .gate(rst));
  Transistor #(.\type ("n")) transistor_39 (.in(transistor_77_out), .out(transistor_35_out), .gate(transistor_7_out));
  Transistor #(.gate("br")) transistor_40 (.in(transistor_77_out), .out(transistor_35_out), .gate(w));
  Transistor #(.\type ("n")) transistor_41 (.in(in4), .out(transistor_41_out), .gate(w));
  Transistor #(.gate("br")) transistor_42 (.in(in4), .out(transistor_41_out), .gate(transistor_9_out));
  Transistor transistor_43 (.in(1'b1), .out(transistor_43_out), .gate(rst));
  Transistor #(.\type ("n")) transistor_44 (.in(1'b0), .out(transistor_43_out), .gate(rst));
  Transistor #(.\type ("n")) transistor_45 (.in(transistor_81_out), .out(transistor_41_out), .gate(transistor_9_out));
  Transistor #(.gate("br")) transistor_46 (.in(transistor_81_out), .out(transistor_41_out), .gate(w));
  Transistor #(.\type ("n")) transistor_47 (.in(in5), .out(transistor_47_out), .gate(w));
  Transistor #(.gate("br")) transistor_48 (.in(in5), .out(transistor_47_out), .gate(transistor_11_out));
  Transistor transistor_49 (.in(1'b1), .out(transistor_49_out), .gate(rst));
  Transistor #(.\type ("n")) transistor_50 (.in(1'b0), .out(transistor_49_out), .gate(rst));
  Transistor #(.\type ("n")) transistor_51 (.in(transistor_85_out), .out(transistor_47_out), .gate(transistor_11_out));
  Transistor #(.gate("br")) transistor_52 (.in(transistor_85_out), .out(transistor_47_out), .gate(w));
  Transistor #(.\type ("n")) transistor_53 (.in(in6), .out(transistor_53_out), .gate(w));
  Transistor #(.gate("br")) transistor_54 (.in(in6), .out(transistor_53_out), .gate(transistor_13_out));
  Transistor transistor_55 (.in(1'b1), .out(transistor_55_out), .gate(rst));
  Transistor #(.\type ("n")) transistor_56 (.in(1'b0), .out(transistor_55_out), .gate(rst));
  Transistor #(.\type ("n")) transistor_57 (.in(transistor_89_out), .out(transistor_53_out), .gate(transistor_13_out));
  Transistor #(.gate("br")) transistor_58 (.in(transistor_89_out), .out(transistor_53_out), .gate(w));
  Transistor #(.\type ("n")) transistor_59 (.in(in7), .out(transistor_59_out), .gate(w));
  Transistor #(.gate("br")) transistor_60 (.in(in7), .out(transistor_59_out), .gate(transistor_15_out));
  Transistor transistor_61 (.in(1'b1), .out(transistor_61_out), .gate(rst));
  Transistor #(.\type ("n")) transistor_62 (.in(1'b0), .out(transistor_61_out), .gate(rst));
  Transistor #(.\type ("n")) transistor_63 (.in(transistor_93_out), .out(transistor_59_out), .gate(transistor_15_out));
  Transistor #(.gate("br")) transistor_64 (.in(transistor_93_out), .out(transistor_59_out), .gate(w));
  Transistor #(.\type ("n")) transistor_65 (.in(1'b0), .out(transistor_65_out), .gate(rst));
  Transistor #(.gate("br")) transistor_66 (.in(1'b0), .out(transistor_65_out), .gate(transistor_19_out));
  Transistor #(.\type ("n")) transistor_67 (.in(transistor_17_out), .out(transistor_65_out), .gate(transistor_19_out));
  Transistor #(.gate("br")) transistor_68 (.in(transistor_17_out), .out(transistor_65_out), .gate(rst));
  Transistor #(.\type ("n")) transistor_69 (.in(1'b0), .out(transistor_69_out), .gate(rst));
  Transistor #(.gate("br")) transistor_70 (.in(1'b0), .out(transistor_69_out), .gate(transistor_25_out));
  Transistor #(.\type ("n")) transistor_71 (.in(transistor_23_out), .out(transistor_69_out), .gate(transistor_25_out));
  Transistor #(.gate("br")) transistor_72 (.in(transistor_23_out), .out(transistor_69_out), .gate(rst));
  Transistor #(.\type ("n")) transistor_73 (.in(1'b0), .out(transistor_73_out), .gate(rst));
  Transistor #(.gate("br")) transistor_74 (.in(1'b0), .out(transistor_73_out), .gate(transistor_31_out));
  Transistor #(.\type ("n")) transistor_75 (.in(transistor_29_out), .out(transistor_73_out), .gate(transistor_31_out));
  Transistor #(.gate("br")) transistor_76 (.in(transistor_29_out), .out(transistor_73_out), .gate(rst));
  Transistor #(.\type ("n")) transistor_77 (.in(1'b0), .out(transistor_77_out), .gate(rst));
  Transistor #(.gate("br")) transistor_78 (.in(1'b0), .out(transistor_77_out), .gate(transistor_37_out));
  Transistor #(.\type ("n")) transistor_79 (.in(transistor_35_out), .out(transistor_77_out), .gate(transistor_37_out));
  Transistor #(.gate("br")) transistor_80 (.in(transistor_35_out), .out(transistor_77_out), .gate(rst));
  Transistor #(.\type ("n")) transistor_81 (.in(1'b0), .out(transistor_81_out), .gate(rst));
  Transistor #(.gate("br")) transistor_82 (.in(1'b0), .out(transistor_81_out), .gate(transistor_43_out));
  Transistor #(.\type ("n")) transistor_83 (.in(transistor_41_out), .out(transistor_81_out), .gate(transistor_43_out));
  Transistor #(.gate("br")) transistor_84 (.in(transistor_41_out), .out(transistor_81_out), .gate(rst));
  Transistor #(.\type ("n")) transistor_85 (.in(1'b0), .out(transistor_85_out), .gate(rst));
  Transistor #(.gate("br")) transistor_86 (.in(1'b0), .out(transistor_85_out), .gate(transistor_49_out));
  Transistor #(.\type ("n")) transistor_87 (.in(transistor_47_out), .out(transistor_85_out), .gate(transistor_49_out));
  Transistor #(.gate("br")) transistor_88 (.in(transistor_47_out), .out(transistor_85_out), .gate(rst));
  Transistor #(.\type ("n")) transistor_89 (.in(1'b0), .out(transistor_89_out), .gate(rst));
  Transistor #(.gate("br")) transistor_90 (.in(1'b0), .out(transistor_89_out), .gate(transistor_55_out));
  Transistor #(.\type ("n")) transistor_91 (.in(transistor_53_out), .out(transistor_89_out), .gate(transistor_55_out));
  Transistor #(.gate("br")) transistor_92 (.in(transistor_53_out), .out(transistor_89_out), .gate(rst));
  Transistor #(.\type ("n")) transistor_93 (.in(1'b0), .out(transistor_93_out), .gate(rst));
  Transistor #(.gate("br")) transistor_94 (.in(1'b0), .out(transistor_93_out), .gate(transistor_61_out));
  Transistor #(.\type ("n")) transistor_95 (.in(transistor_59_out), .out(transistor_93_out), .gate(transistor_61_out));
  Transistor #(.gate("br")) transistor_96 (.in(transistor_59_out), .out(transistor_93_out), .gate(rst));
  Transistor #(.gate("br")) transistor_97 (.in(1'b1), .out(transistor_97_out), .gate(r));
  Transistor #(.gate("br")) transistor_98 (.in(1'b1), .out(transistor_98_out), .gate(r));
  Transistor #(.gate("br")) transistor_99 (.in(1'b1), .out(transistor_99_out), .gate(r));
  Transistor #(.gate("br")) transistor_100 (.in(1'b1), .out(transistor_100_out), .gate(r));
  Transistor #(.gate("br")) transistor_101 (.in(1'b1), .out(transistor_101_out), .gate(r));
  Transistor #(.gate("br")) transistor_102 (.in(1'b1), .out(transistor_102_out), .gate(r));
  Transistor #(.gate("br")) transistor_103 (.in(1'b1), .out(transistor_103_out), .gate(r));
  Transistor #(.gate("br")) transistor_104 (.in(1'b1), .out(transistor_104_out), .gate(r));
  Transistor #(.\type ("n")) transistor_105 (.in(transistor_65_out), .out(out0), .gate(r));
  Transistor #(.gate("br")) transistor_106 (.in(transistor_65_out), .out(out0), .gate(transistor_97_out));
  Transistor #(.\type ("n"), .gate("br")) transistor_107 (.in(1'b0), .out(transistor_97_out), .gate(r));
  Transistor #(.\type ("n")) transistor_108 (.in(transistor_69_out), .out(out1), .gate(r));
  Transistor #(.gate("br")) transistor_109 (.in(transistor_69_out), .out(out1), .gate(transistor_98_out));
  Transistor #(.\type ("n"), .gate("br")) transistor_110 (.in(1'b0), .out(transistor_98_out), .gate(r));
  Transistor #(.\type ("n")) transistor_111 (.in(transistor_73_out), .out(out2), .gate(r));
  Transistor #(.gate("br")) transistor_112 (.in(transistor_73_out), .out(out2), .gate(transistor_99_out));
  Transistor #(.\type ("n"), .gate("br")) transistor_113 (.in(1'b0), .out(transistor_99_out), .gate(r));
  Transistor #(.\type ("n")) transistor_114 (.in(transistor_77_out), .out(out3), .gate(r));
  Transistor #(.gate("br")) transistor_115 (.in(transistor_77_out), .out(out3), .gate(transistor_100_out));
  Transistor #(.\type ("n"), .gate("br")) transistor_116 (.in(1'b0), .out(transistor_100_out), .gate(r));
  Transistor #(.\type ("n")) transistor_117 (.in(transistor_81_out), .out(out4), .gate(r));
  Transistor #(.gate("br")) transistor_118 (.in(transistor_81_out), .out(out4), .gate(transistor_101_out));
  Transistor #(.\type ("n"), .gate("br")) transistor_119 (.in(1'b0), .out(transistor_101_out), .gate(r));
  Transistor #(.\type ("n")) transistor_120 (.in(transistor_85_out), .out(out5), .gate(r));
  Transistor #(.gate("br")) transistor_121 (.in(transistor_85_out), .out(out5), .gate(transistor_102_out));
  Transistor #(.\type ("n"), .gate("br")) transistor_122 (.in(1'b0), .out(transistor_102_out), .gate(r));
  Transistor #(.\type ("n")) transistor_123 (.in(transistor_89_out), .out(out6), .gate(r));
  Transistor #(.gate("br")) transistor_124 (.in(transistor_89_out), .out(out6), .gate(transistor_103_out));
  Transistor #(.\type ("n"), .gate("br")) transistor_125 (.in(1'b0), .out(transistor_103_out), .gate(r));
  Transistor #(.\type ("n")) transistor_126 (.in(transistor_93_out), .out(out7), .gate(r));
  Transistor #(.gate("br")) transistor_127 (.in(transistor_93_out), .out(out7), .gate(transistor_104_out));
  Transistor #(.\type ("n"), .gate("br")) transistor_128 (.in(1'b0), .out(transistor_104_out), .gate(r));
endmodule

module SHL1x8x1 (
  input  cin,
  input  in0,
  input  in1,
  input  in2,
  input  in3,
  input  in4,
  input  in5,
  input  in6,
  input  in7,
  output out0,
  output out1,
  output out2,
  output out3,
  output out4,
  output out6,
  output out6_2,
  output out7,
  output cout
);


  assign cout = in7;
  assign out0 = cin;
  assign out1 = in0;
  assign out2 = in1;
  assign out3 = in2;
  assign out4 = in3;
  assign out6 = in4;
  assign out6_2 = in5;
  assign out7 = in6;
endmodule

module SHR1x8x1 (
  input  in0,
  input  in1,
  input  in2,
  input  in3,
  input  in4,
  input  in5,
  input  in6,
  input  in7,
  input  cin,
  output cout,
  output out0,
  output out1,
  output out2,
  output out3,
  output out4,
  output out6,
  output out6_2,
  output out7
);


  assign cout = in0;
  assign out0 = in1;
  assign out1 = in2;
  assign out2 = in3;
  assign out3 = in4;
  assign out4 = in5;
  assign out6 = in6;
  assign out6_2 = in7;
  assign out7 = cin;
endmodule

module AND2x8x1 (
  input  a0,
  input  b0,
  input  a1,
  input  b1,
  input  a2,
  input  b2,
  input  a3,
  input  b3,
  input  a4,
  input  b4,
  input  a5,
  input  b5,
  input  a6,
  input  b6,
  input  a7,
  input  b7,
  output out0,
  output out1,
  output out2,
  output out3,
  output out4,
  output out5,
  output out6,
  output out7
);

  wire transistor_1_out, transistor_2_out, transistor_3_out, transistor_4_out, transistor_5_out,
       transistor_6_out, transistor_7_out, transistor_8_out, transistor_13_out, transistor_18_out,
       transistor_23_out, transistor_28_out, transistor_33_out, transistor_38_out, transistor_43_out,
       transistor_48_out;

  Transistor transistor_1 (.in(1'b1), .out(transistor_1_out), .gate(a0));
  Transistor transistor_2 (.in(1'b1), .out(transistor_2_out), .gate(a1));
  Transistor transistor_3 (.in(1'b1), .out(transistor_3_out), .gate(a2));
  Transistor transistor_4 (.in(1'b1), .out(transistor_4_out), .gate(a3));
  Transistor transistor_5 (.in(1'b1), .out(transistor_5_out), .gate(a4));
  Transistor transistor_6 (.in(1'b1), .out(transistor_6_out), .gate(a5));
  Transistor transistor_7 (.in(1'b1), .out(transistor_7_out), .gate(a6));
  Transistor transistor_8 (.in(1'b1), .out(transistor_8_out), .gate(a7));
  Transistor transistor_9 (.in(1'b1), .out(transistor_1_out), .gate(b0));
  Transistor transistor_10 (.in(1'b1), .out(out0), .gate(transistor_1_out));
  Transistor #(.\type ("n")) transistor_11 (.in(transistor_13_out), .out(transistor_1_out), .gate(a0));
  Transistor #(.\type ("n")) transistor_12 (.in(1'b0), .out(out0), .gate(transistor_1_out));
  Transistor #(.\type ("n")) transistor_13 (.in(1'b0), .out(transistor_13_out), .gate(b0));
  Transistor transistor_14 (.in(1'b1), .out(out1), .gate(transistor_2_out));
  Transistor transistor_15 (.in(1'b1), .out(transistor_2_out), .gate(b1));
  Transistor #(.\type ("n")) transistor_16 (.in(1'b0), .out(out1), .gate(transistor_2_out));
  Transistor #(.\type ("n")) transistor_17 (.in(transistor_18_out), .out(transistor_2_out), .gate(a1));
  Transistor #(.\type ("n")) transistor_18 (.in(1'b0), .out(transistor_18_out), .gate(b1));
  Transistor transistor_19 (.in(1'b1), .out(out2), .gate(transistor_3_out));
  Transistor transistor_20 (.in(1'b1), .out(transistor_3_out), .gate(b2));
  Transistor #(.\type ("n")) transistor_21 (.in(1'b0), .out(out2), .gate(transistor_3_out));
  Transistor #(.\type ("n")) transistor_22 (.in(transistor_23_out), .out(transistor_3_out), .gate(a2));
  Transistor #(.\type ("n")) transistor_23 (.in(1'b0), .out(transistor_23_out), .gate(b2));
  Transistor transistor_24 (.in(1'b1), .out(out3), .gate(transistor_4_out));
  Transistor transistor_25 (.in(1'b1), .out(transistor_4_out), .gate(b3));
  Transistor #(.\type ("n")) transistor_26 (.in(1'b0), .out(out3), .gate(transistor_4_out));
  Transistor #(.\type ("n")) transistor_27 (.in(transistor_28_out), .out(transistor_4_out), .gate(a3));
  Transistor #(.\type ("n")) transistor_28 (.in(1'b0), .out(transistor_28_out), .gate(b3));
  Transistor transistor_29 (.in(1'b1), .out(out4), .gate(transistor_5_out));
  Transistor transistor_30 (.in(1'b1), .out(transistor_5_out), .gate(b4));
  Transistor #(.\type ("n")) transistor_31 (.in(transistor_33_out), .out(transistor_5_out), .gate(a4));
  Transistor #(.\type ("n")) transistor_32 (.in(1'b0), .out(out4), .gate(transistor_5_out));
  Transistor #(.\type ("n")) transistor_33 (.in(1'b0), .out(transistor_33_out), .gate(b4));
  Transistor transistor_34 (.in(1'b1), .out(out5), .gate(transistor_6_out));
  Transistor transistor_35 (.in(1'b1), .out(transistor_6_out), .gate(b5));
  Transistor #(.\type ("n")) transistor_36 (.in(1'b0), .out(out5), .gate(transistor_6_out));
  Transistor #(.\type ("n")) transistor_37 (.in(transistor_38_out), .out(transistor_6_out), .gate(a5));
  Transistor #(.\type ("n")) transistor_38 (.in(1'b0), .out(transistor_38_out), .gate(b5));
  Transistor transistor_39 (.in(1'b1), .out(out6), .gate(transistor_7_out));
  Transistor transistor_40 (.in(1'b1), .out(transistor_7_out), .gate(b6));
  Transistor #(.\type ("n")) transistor_41 (.in(transistor_43_out), .out(transistor_7_out), .gate(a6));
  Transistor #(.\type ("n")) transistor_42 (.in(1'b0), .out(out6), .gate(transistor_7_out));
  Transistor #(.\type ("n")) transistor_43 (.in(1'b0), .out(transistor_43_out), .gate(b6));
  Transistor transistor_44 (.in(1'b1), .out(out7), .gate(transistor_8_out));
  Transistor transistor_45 (.in(1'b1), .out(transistor_8_out), .gate(b7));
  Transistor #(.\type ("n")) transistor_46 (.in(1'b0), .out(out7), .gate(transistor_8_out));
  Transistor #(.\type ("n")) transistor_47 (.in(transistor_48_out), .out(transistor_8_out), .gate(a7));
  Transistor #(.\type ("n")) transistor_48 (.in(1'b0), .out(transistor_48_out), .gate(b7));
endmodule

module FULLADDER (
  input  a,
  input  b,
  input  cin,
  output sum,
  output cout
);

  wire transistor_1_out, transistor_2_out, transistor_4_out, transistor_6_out, transistor_9_out,
       transistor_10_out, transistor_13_out, transistor_14_out, transistor_17_out, transistor_20_out,
       transistor_21_out, transistor_23_out, transistor_26_out, transistor_27_out, transistor_30_out,
       transistor_31_out, transistor_32_out, transistor_33_out, transistor_37_out, transistor_41_out,
       transistor_42_out, transistor_43_out, transistor_48_out;

  Transistor transistor_1 (.in(1'b1), .out(transistor_1_out), .gate(a));
  Transistor transistor_2 (.in(1'b1), .out(transistor_2_out), .gate(a));
  Transistor transistor_3 (.in(1'b1), .out(transistor_1_out), .gate(b));
  Transistor transistor_4 (.in(1'b1), .out(transistor_4_out), .gate(transistor_1_out));
  Transistor #(.\type ("n")) transistor_5 (.in(transistor_6_out), .out(transistor_1_out), .gate(a));
  Transistor #(.\type ("n")) transistor_6 (.in(1'b0), .out(transistor_6_out), .gate(b));
  Transistor transistor_7 (.in(1'b1), .out(transistor_2_out), .gate(transistor_1_out));
  Transistor #(.\type ("n")) transistor_8 (.in(transistor_9_out), .out(transistor_2_out), .gate(a));
  Transistor #(.\type ("n")) transistor_9 (.in(1'b0), .out(transistor_9_out), .gate(transistor_1_out));
  Transistor transistor_10 (.in(1'b1), .out(transistor_10_out), .gate(transistor_2_out));
  Transistor transistor_11 (.in(1'b1), .out(transistor_4_out), .gate(b));
  Transistor #(.\type ("n")) transistor_12 (.in(transistor_13_out), .out(transistor_4_out), .gate(transistor_1_out));
  Transistor #(.\type ("n")) transistor_13 (.in(1'b0), .out(transistor_13_out), .gate(b));
  Transistor transistor_14 (.in(1'b1), .out(transistor_14_out), .gate(transistor_10_out));
  Transistor transistor_15 (.in(1'b1), .out(transistor_14_out), .gate(cin));
  Transistor #(.\type ("n")) transistor_16 (.in(transistor_17_out), .out(transistor_14_out), .gate(transistor_10_out));
  Transistor #(.\type ("n")) transistor_17 (.in(1'b0), .out(transistor_17_out), .gate(cin));
  Transistor transistor_18 (.in(1'b1), .out(transistor_10_out), .gate(transistor_4_out));
  Transistor #(.\type ("n")) transistor_19 (.in(transistor_20_out), .out(transistor_10_out), .gate(transistor_2_out));
  Transistor #(.\type ("n")) transistor_20 (.in(1'b0), .out(transistor_20_out), .gate(transistor_4_out));
  Transistor transistor_21 (.in(1'b1), .out(transistor_21_out), .gate(transistor_14_out));
  Transistor #(.\type ("n")) transistor_22 (.in(1'b0), .out(transistor_21_out), .gate(transistor_14_out));
  Transistor transistor_23 (.in(1'b1), .out(transistor_23_out), .gate(transistor_10_out));
  Transistor transistor_24 (.in(1'b1), .out(transistor_23_out), .gate(cin));
  Transistor #(.\type ("n")) transistor_25 (.in(transistor_26_out), .out(transistor_23_out), .gate(transistor_10_out));
  Transistor #(.\type ("n")) transistor_26 (.in(1'b0), .out(transistor_26_out), .gate(cin));
  Transistor transistor_27 (.in(1'b1), .out(transistor_27_out), .gate(b));
  Transistor transistor_28 (.in(1'b1), .out(transistor_27_out), .gate(a));
  Transistor #(.\type ("n")) transistor_29 (.in(transistor_30_out), .out(transistor_27_out), .gate(a));
  Transistor #(.\type ("n")) transistor_30 (.in(1'b0), .out(transistor_30_out), .gate(b));
  Transistor transistor_31 (.in(1'b1), .out(transistor_31_out), .gate(transistor_10_out));
  Transistor transistor_32 (.in(1'b1), .out(transistor_32_out), .gate(transistor_23_out));
  Transistor transistor_33 (.in(1'b1), .out(transistor_33_out), .gate(transistor_27_out));
  Transistor #(.\type ("n")) transistor_34 (.in(1'b0), .out(transistor_33_out), .gate(transistor_27_out));
  Transistor transistor_35 (.in(1'b1), .out(transistor_31_out), .gate(transistor_23_out));
  Transistor #(.\type ("n")) transistor_36 (.in(transistor_37_out), .out(transistor_31_out), .gate(transistor_10_out));
  Transistor #(.\type ("n")) transistor_37 (.in(1'b0), .out(transistor_37_out), .gate(transistor_23_out));
  Transistor transistor_38 (.in(1'b1), .out(sum), .gate(transistor_31_out));
  Transistor transistor_39 (.in(1'b1), .out(transistor_32_out), .gate(cin));
  Transistor #(.\type ("n")) transistor_40 (.in(transistor_41_out), .out(transistor_32_out), .gate(transistor_23_out));
  Transistor #(.\type ("n")) transistor_41 (.in(1'b0), .out(transistor_41_out), .gate(cin));
  Transistor transistor_42 (.in(1'b1), .out(transistor_42_out), .gate(transistor_21_out));
  Transistor transistor_43 (.in(transistor_42_out), .out(transistor_43_out), .gate(transistor_33_out));
  Transistor #(.\type ("n")) transistor_44 (.in(1'b0), .out(transistor_43_out), .gate(transistor_21_out));
  Transistor #(.\type ("n")) transistor_45 (.in(1'b0), .out(transistor_43_out), .gate(transistor_33_out));
  Transistor transistor_46 (.in(1'b1), .out(sum), .gate(transistor_32_out));
  Transistor #(.\type ("n")) transistor_47 (.in(transistor_48_out), .out(sum), .gate(transistor_31_out));
  Transistor #(.\type ("n")) transistor_48 (.in(1'b0), .out(transistor_48_out), .gate(transistor_32_out));
  Transistor transistor_49 (.in(1'b1), .out(cout), .gate(transistor_43_out));
  Transistor #(.\type ("n")) transistor_50 (.in(1'b0), .out(cout), .gate(transistor_43_out));
endmodule

module ADDSUB (
  input  sub,
  input  cin,
  input  a,
  input  b,
  output sum,
  output cout
);

  wire transistor_1_out, transistor_4_out, transistor_5_out, transistor_8_out, transistor_9_out,
       transistor_12_out, transistor_13_out, transistor_16_out, transistor_17_out, transistor_18_out,
       transistor_22_out, transistor_23_out, transistor_26_out, transistor_27_out, transistor_30_out,
       transistor_31_out, transistor_33_out, transistor_35_out, transistor_38_out, transistor_39_out,
       transistor_41_out, transistor_44_out, transistor_45_out, transistor_48_out, transistor_49_out,
       transistor_52_out, transistor_53_out, transistor_57_out, transistor_60_out;

  Transistor transistor_1 (.in(1'b1), .out(transistor_1_out), .gate(b));
  Transistor transistor_2 (.in(1'b1), .out(transistor_1_out), .gate(sub));
  Transistor #(.\type ("n")) transistor_3 (.in(transistor_4_out), .out(transistor_1_out), .gate(sub));
  Transistor #(.\type ("n")) transistor_4 (.in(1'b0), .out(transistor_4_out), .gate(b));
  Transistor transistor_5 (.in(1'b1), .out(transistor_5_out), .gate(transistor_1_out));
  Transistor transistor_6 (.in(1'b1), .out(transistor_5_out), .gate(b));
  Transistor #(.\type ("n")) transistor_7 (.in(transistor_8_out), .out(transistor_5_out), .gate(transistor_1_out));
  Transistor #(.\type ("n")) transistor_8 (.in(1'b0), .out(transistor_8_out), .gate(b));
  Transistor transistor_9 (.in(1'b1), .out(transistor_9_out), .gate(sub));
  Transistor transistor_10 (.in(1'b1), .out(transistor_9_out), .gate(transistor_1_out));
  Transistor #(.\type ("n")) transistor_11 (.in(transistor_12_out), .out(transistor_9_out), .gate(transistor_1_out));
  Transistor #(.\type ("n")) transistor_12 (.in(1'b0), .out(transistor_12_out), .gate(sub));
  Transistor transistor_13 (.in(1'b1), .out(transistor_13_out), .gate(transistor_9_out));
  Transistor transistor_14 (.in(1'b1), .out(transistor_13_out), .gate(transistor_5_out));
  Transistor #(.\type ("n")) transistor_15 (.in(transistor_16_out), .out(transistor_13_out), .gate(transistor_9_out));
  Transistor #(.\type ("n")) transistor_16 (.in(1'b0), .out(transistor_16_out), .gate(transistor_5_out));
  Transistor transistor_17 (.in(1'b1), .out(transistor_17_out), .gate(a));
  Transistor transistor_18 (.in(1'b1), .out(transistor_18_out), .gate(transistor_17_out));
  Transistor transistor_19 (.in(1'b1), .out(transistor_17_out), .gate(transistor_13_out));
  Transistor #(.\type ("n")) transistor_20 (.in(1'b0), .out(transistor_18_out), .gate(transistor_17_out));
  Transistor #(.\type ("n")) transistor_21 (.in(transistor_22_out), .out(transistor_17_out), .gate(a));
  Transistor #(.\type ("n")) transistor_22 (.in(1'b0), .out(transistor_22_out), .gate(transistor_13_out));
  Transistor transistor_23 (.in(1'b1), .out(transistor_23_out), .gate(a));
  Transistor transistor_24 (.in(1'b1), .out(transistor_23_out), .gate(transistor_13_out));
  Transistor #(.\type ("n")) transistor_25 (.in(transistor_26_out), .out(transistor_23_out), .gate(a));
  Transistor #(.\type ("n")) transistor_26 (.in(1'b0), .out(transistor_26_out), .gate(transistor_13_out));
  Transistor transistor_27 (.in(1'b1), .out(transistor_27_out), .gate(transistor_13_out));
  Transistor transistor_28 (.in(1'b1), .out(transistor_27_out), .gate(transistor_23_out));
  Transistor #(.\type ("n")) transistor_29 (.in(transistor_30_out), .out(transistor_27_out), .gate(transistor_23_out));
  Transistor #(.\type ("n")) transistor_30 (.in(1'b0), .out(transistor_30_out), .gate(transistor_13_out));
  Transistor transistor_31 (.in(1'b1), .out(transistor_31_out), .gate(a));
  Transistor transistor_32 (.in(1'b1), .out(transistor_31_out), .gate(transistor_23_out));
  Transistor transistor_33 (.in(1'b1), .out(transistor_33_out), .gate(transistor_31_out));
  Transistor #(.\type ("n")) transistor_34 (.in(transistor_35_out), .out(transistor_31_out), .gate(transistor_23_out));
  Transistor #(.\type ("n")) transistor_35 (.in(1'b0), .out(transistor_35_out), .gate(a));
  Transistor transistor_36 (.in(1'b1), .out(transistor_33_out), .gate(transistor_27_out));
  Transistor #(.\type ("n")) transistor_37 (.in(transistor_38_out), .out(transistor_33_out), .gate(transistor_31_out));
  Transistor #(.\type ("n")) transistor_38 (.in(1'b0), .out(transistor_38_out), .gate(transistor_27_out));
  Transistor transistor_39 (.in(1'b1), .out(transistor_39_out), .gate(cin));
  Transistor transistor_40 (.in(1'b1), .out(transistor_39_out), .gate(transistor_33_out));
  Transistor transistor_41 (.in(1'b1), .out(transistor_41_out), .gate(transistor_39_out));
  Transistor #(.\type ("n")) transistor_42 (.in(1'b0), .out(transistor_41_out), .gate(transistor_39_out));
  Transistor #(.\type ("n")) transistor_43 (.in(transistor_44_out), .out(transistor_39_out), .gate(cin));
  Transistor #(.\type ("n")) transistor_44 (.in(1'b0), .out(transistor_44_out), .gate(transistor_33_out));
  Transistor transistor_45 (.in(1'b1), .out(transistor_45_out), .gate(transistor_33_out));
  Transistor transistor_46 (.in(1'b1), .out(transistor_45_out), .gate(cin));
  Transistor #(.\type ("n")) transistor_47 (.in(transistor_48_out), .out(transistor_45_out), .gate(transistor_33_out));
  Transistor #(.\type ("n")) transistor_48 (.in(1'b0), .out(transistor_48_out), .gate(cin));
  Transistor transistor_49 (.in(1'b1), .out(transistor_49_out), .gate(transistor_45_out));
  Transistor transistor_50 (.in(1'b1), .out(transistor_49_out), .gate(cin));
  Transistor #(.\type ("n")) transistor_51 (.in(transistor_52_out), .out(transistor_49_out), .gate(transistor_45_out));
  Transistor #(.\type ("n")) transistor_52 (.in(1'b0), .out(transistor_52_out), .gate(cin));
  Transistor transistor_53 (.in(1'b1), .out(transistor_53_out), .gate(transistor_33_out));
  Transistor transistor_54 (.in(1'b1), .out(sum), .gate(transistor_53_out));
  Transistor transistor_55 (.in(1'b1), .out(transistor_53_out), .gate(transistor_45_out));
  Transistor #(.\type ("n")) transistor_56 (.in(transistor_57_out), .out(transistor_53_out), .gate(transistor_45_out));
  Transistor #(.\type ("n")) transistor_57 (.in(1'b0), .out(transistor_57_out), .gate(transistor_33_out));
  Transistor transistor_58 (.in(1'b1), .out(sum), .gate(transistor_49_out));
  Transistor #(.\type ("n")) transistor_59 (.in(transistor_60_out), .out(sum), .gate(transistor_53_out));
  Transistor #(.\type ("n")) transistor_60 (.in(1'b0), .out(transistor_60_out), .gate(transistor_49_out));
endmodule
module ADDSUB2x8x1 (
  input  sub,
  input  cin,
  input  a0,
  input  b0,
  input  a1,
  input  b1,
  input  a2,
  input  b2,
  input  a3,
  input  b3,
  input  a4,
  input  b4,
  input  a5,
  input  b5,
  input  a6,
  input  b6,
  input  a7,
  input  b7,
  output sum0,
  output sum1,
  output sum2,
  output sum3,
  output sum4,
  output sum5,
  output sum6,
  output sum7,
  output cout,
  output overflow
);

  wire transistor_1_out, transistor_2_out, transistor_3_out, transistor_4_out, transistor_5_out,
       transistor_6_out, transistor_7_out, transistor_8_out, transistor_9_out, transistor_10_out,
       transistor_11_out, transistor_12_out, transistor_15_out, transistor_16_out, transistor_17_out,
       transistor_20_out, transistor_21_out, transistor_22_out, transistor_25_out, transistor_26_out,
       transistor_27_out, transistor_30_out, transistor_31_out, transistor_32_out, transistor_35_out,
       transistor_36_out, transistor_37_out, transistor_40_out, transistor_41_out, transistor_42_out,
       transistor_45_out, transistor_46_out, transistor_48_out, transistor_50_out, transistor_51_out,
       transistor_53_out, transistor_55_out, transistor_58_out, transistor_61_out, transistor_64_out,
       transistor_67_out, transistor_70_out, transistor_73_out, transistor_76_out, transistor_79_out,
       transistor_82_out, transistor_85_out, transistor_88_out, transistor_91_out, transistor_94_out,
       transistor_97_out, transistor_100_out, transistor_103_out, transistor_106_out, transistor_109_out,
       transistor_112_out, transistor_113_out, transistor_116_out, transistor_117_out, transistor_120_out,
       transistor_121_out, transistor_124_out, transistor_125_out, transistor_128_out, transistor_129_out,
       transistor_132_out, transistor_133_out, transistor_136_out, transistor_137_out, transistor_140_out,
       transistor_141_out, transistor_144_out, transistor_145_out, transistor_148_out, transistor_149_out,
       transistor_152_out, transistor_153_out, transistor_156_out, transistor_160_out, transistor_161_out,
       transistor_162_out, transistor_163_out, transistor_164_out, transistor_165_out, transistor_166_out,
       transistor_167_out, transistor_168_out, transistor_171_out, transistor_174_out, transistor_177_out,
       transistor_180_out, transistor_183_out, transistor_186_out, transistor_189_out, transistor_192_out,
       transistor_193_out, transistor_196_out, transistor_197_out, transistor_200_out, transistor_201_out,
       transistor_202_out, transistor_205_out, transistor_206_out, transistor_209_out, transistor_210_out,
       transistor_211_out, transistor_214_out, transistor_215_out, transistor_218_out, transistor_219_out,
       transistor_220_out, transistor_223_out, transistor_224_out, transistor_227_out, transistor_228_out,
       transistor_229_out, transistor_232_out, transistor_233_out, transistor_236_out, transistor_237_out,
       transistor_238_out, transistor_241_out, transistor_242_out, transistor_245_out, transistor_246_out,
       transistor_247_out, transistor_250_out, transistor_251_out, transistor_254_out, transistor_255_out,
       transistor_256_out, transistor_259_out, transistor_260_out, transistor_263_out, transistor_264_out,
       transistor_265_out, transistor_268_out, transistor_270_out, transistor_273_out, transistor_274_out,
       transistor_277_out, transistor_278_out, transistor_282_out, transistor_283_out, transistor_286_out,
       transistor_287_out, transistor_291_out, transistor_292_out, transistor_295_out, transistor_296_out,
       transistor_300_out, transistor_301_out, transistor_304_out, transistor_306_out, transistor_309_out,
       transistor_310_out, transistor_313_out, transistor_314_out, transistor_318_out, transistor_319_out,
       transistor_322_out, transistor_323_out, transistor_327_out, transistor_328_out, transistor_331_out,
       transistor_333_out, transistor_336_out, transistor_337_out, transistor_340_out, transistor_341_out,
       transistor_342_out, transistor_343_out, transistor_344_out, transistor_345_out, transistor_346_out,
       transistor_347_out, transistor_348_out, transistor_349_out, transistor_350_out, transistor_351_out,
       transistor_352_out, transistor_353_out, transistor_354_out, transistor_355_out, transistor_356_out,
       transistor_357_out, transistor_358_out, transistor_359_out, transistor_361_out, transistor_363_out,
       transistor_364_out, transistor_368_out, transistor_369_out, transistor_370_out, transistor_373_out,
       transistor_375_out, transistor_378_out, transistor_379_out, transistor_381_out, transistor_383_out,
       transistor_385_out, transistor_388_out, transistor_389_out, transistor_391_out, transistor_393_out,
       transistor_394_out, transistor_398_out, transistor_399_out, transistor_400_out, transistor_403_out,
       transistor_404_out, transistor_408_out, transistor_409_out, transistor_411_out, transistor_413_out,
       transistor_415_out, transistor_418_out, transistor_419_out, transistor_421_out, transistor_423_out,
       transistor_424_out, transistor_428_out, transistor_429_out, transistor_431_out, transistor_433_out,
       transistor_435_out, transistor_438_out, transistor_441_out, transistor_445_out, transistor_448_out,
       transistor_451_out, transistor_452_out, transistor_455_out, transistor_458_out, transistor_459_out,
       transistor_462_out, transistor_465_out, transistor_466_out, transistor_469_out, transistor_472_out,
       transistor_473_out, transistor_476_out, transistor_479_out, transistor_480_out, transistor_483_out,
       transistor_486_out, transistor_487_out, transistor_490_out, transistor_493_out, transistor_494_out,
       transistor_497_out, transistor_500_out, transistor_501_out, transistor_504_out, transistor_508_out,
       transistor_509_out, transistor_510_out, transistor_517_out, transistor_518_out, transistor_519_out,
       transistor_526_out, transistor_527_out, transistor_529_out, transistor_535_out, transistor_536_out,
       transistor_538_out, transistor_544_out, transistor_545_out, transistor_547_out, transistor_553_out,
       transistor_554_out, transistor_555_out, transistor_562_out, transistor_563_out, transistor_565_out,
       transistor_571_out, transistor_572_out, transistor_574_out;

  Transistor transistor_1 (.in(1'b1), .out(transistor_1_out), .gate(sub));
  Transistor transistor_2 (.in(1'b1), .out(transistor_2_out), .gate(sub));
  Transistor transistor_3 (.in(1'b1), .out(transistor_3_out), .gate(sub));
  Transistor transistor_4 (.in(1'b1), .out(transistor_4_out), .gate(sub));
  Transistor transistor_5 (.in(1'b1), .out(transistor_5_out), .gate(sub));
  Transistor transistor_6 (.in(1'b1), .out(transistor_6_out), .gate(sub));
  Transistor transistor_7 (.in(1'b1), .out(transistor_7_out), .gate(sub));
  Transistor transistor_8 (.in(1'b1), .out(transistor_8_out), .gate(sub));
  Transistor transistor_9 (.in(1'b1), .out(transistor_9_out), .gate(sub));
  Transistor transistor_10 (.in(1'b1), .out(transistor_10_out), .gate(transistor_574_out));
  Transistor transistor_11 (.in(1'b1), .out(transistor_11_out), .gate(sub));
  Transistor transistor_12 (.in(1'b1), .out(transistor_12_out), .gate(transistor_1_out));
  Transistor transistor_13 (.in(1'b1), .out(transistor_1_out), .gate(cin));
  Transistor #(.\type ("n")) transistor_14 (.in(transistor_15_out), .out(transistor_1_out), .gate(sub));
  Transistor #(.\type ("n")) transistor_15 (.in(1'b0), .out(transistor_15_out), .gate(cin));
  Transistor transistor_16 (.in(1'b1), .out(transistor_16_out), .gate(sub));
  Transistor transistor_17 (.in(1'b1), .out(transistor_17_out), .gate(transistor_2_out));
  Transistor transistor_18 (.in(1'b1), .out(transistor_2_out), .gate(b0));
  Transistor #(.\type ("n")) transistor_19 (.in(transistor_20_out), .out(transistor_2_out), .gate(sub));
  Transistor #(.\type ("n")) transistor_20 (.in(1'b0), .out(transistor_20_out), .gate(b0));
  Transistor transistor_21 (.in(1'b1), .out(transistor_21_out), .gate(sub));
  Transistor transistor_22 (.in(1'b1), .out(transistor_22_out), .gate(transistor_3_out));
  Transistor transistor_23 (.in(1'b1), .out(transistor_3_out), .gate(b1));
  Transistor #(.\type ("n")) transistor_24 (.in(transistor_25_out), .out(transistor_3_out), .gate(sub));
  Transistor #(.\type ("n")) transistor_25 (.in(1'b0), .out(transistor_25_out), .gate(b1));
  Transistor transistor_26 (.in(1'b1), .out(transistor_26_out), .gate(sub));
  Transistor transistor_27 (.in(1'b1), .out(transistor_27_out), .gate(transistor_4_out));
  Transistor transistor_28 (.in(1'b1), .out(transistor_4_out), .gate(b2));
  Transistor #(.\type ("n")) transistor_29 (.in(transistor_30_out), .out(transistor_4_out), .gate(sub));
  Transistor #(.\type ("n")) transistor_30 (.in(1'b0), .out(transistor_30_out), .gate(b2));
  Transistor transistor_31 (.in(1'b1), .out(transistor_31_out), .gate(sub));
  Transistor transistor_32 (.in(1'b1), .out(transistor_32_out), .gate(transistor_5_out));
  Transistor transistor_33 (.in(1'b1), .out(transistor_5_out), .gate(b3));
  Transistor #(.\type ("n")) transistor_34 (.in(transistor_35_out), .out(transistor_5_out), .gate(sub));
  Transistor #(.\type ("n")) transistor_35 (.in(1'b0), .out(transistor_35_out), .gate(b3));
  Transistor transistor_36 (.in(1'b1), .out(transistor_36_out), .gate(sub));
  Transistor transistor_37 (.in(1'b1), .out(transistor_37_out), .gate(transistor_6_out));
  Transistor transistor_38 (.in(1'b1), .out(transistor_6_out), .gate(b4));
  Transistor #(.\type ("n")) transistor_39 (.in(transistor_40_out), .out(transistor_6_out), .gate(sub));
  Transistor #(.\type ("n")) transistor_40 (.in(1'b0), .out(transistor_40_out), .gate(b4));
  Transistor transistor_41 (.in(1'b1), .out(transistor_41_out), .gate(sub));
  Transistor transistor_42 (.in(1'b1), .out(transistor_42_out), .gate(transistor_7_out));
  Transistor transistor_43 (.in(1'b1), .out(transistor_7_out), .gate(b5));
  Transistor #(.\type ("n")) transistor_44 (.in(transistor_45_out), .out(transistor_7_out), .gate(sub));
  Transistor #(.\type ("n")) transistor_45 (.in(1'b0), .out(transistor_45_out), .gate(b5));
  Transistor transistor_46 (.in(1'b1), .out(transistor_46_out), .gate(sub));
  Transistor transistor_47 (.in(1'b1), .out(transistor_8_out), .gate(b6));
  Transistor transistor_48 (.in(1'b1), .out(transistor_48_out), .gate(transistor_8_out));
  Transistor #(.\type ("n")) transistor_49 (.in(transistor_50_out), .out(transistor_8_out), .gate(sub));
  Transistor #(.\type ("n")) transistor_50 (.in(1'b0), .out(transistor_50_out), .gate(b6));
  Transistor transistor_51 (.in(1'b1), .out(transistor_51_out), .gate(sub));
  Transistor transistor_52 (.in(1'b1), .out(transistor_9_out), .gate(b7));
  Transistor transistor_53 (.in(1'b1), .out(transistor_53_out), .gate(transistor_9_out));
  Transistor #(.\type ("n")) transistor_54 (.in(transistor_55_out), .out(transistor_9_out), .gate(sub));
  Transistor #(.\type ("n")) transistor_55 (.in(1'b0), .out(transistor_55_out), .gate(b7));
  Transistor transistor_56 (.in(1'b1), .out(transistor_10_out), .gate(sub));
  Transistor #(.\type ("n")) transistor_57 (.in(transistor_58_out), .out(transistor_10_out), .gate(transistor_574_out));
  Transistor #(.\type ("n")) transistor_58 (.in(1'b0), .out(transistor_58_out), .gate(sub));
  Transistor transistor_59 (.in(1'b1), .out(transistor_11_out), .gate(transistor_1_out));
  Transistor #(.\type ("n")) transistor_60 (.in(transistor_61_out), .out(transistor_11_out), .gate(sub));
  Transistor #(.\type ("n")) transistor_61 (.in(1'b0), .out(transistor_61_out), .gate(transistor_1_out));
  Transistor transistor_62 (.in(1'b1), .out(transistor_12_out), .gate(cin));
  Transistor #(.\type ("n")) transistor_63 (.in(transistor_64_out), .out(transistor_12_out), .gate(transistor_1_out));
  Transistor #(.\type ("n")) transistor_64 (.in(1'b0), .out(transistor_64_out), .gate(cin));
  Transistor transistor_65 (.in(1'b1), .out(transistor_16_out), .gate(transistor_2_out));
  Transistor #(.\type ("n")) transistor_66 (.in(transistor_67_out), .out(transistor_16_out), .gate(sub));
  Transistor #(.\type ("n")) transistor_67 (.in(1'b0), .out(transistor_67_out), .gate(transistor_2_out));
  Transistor transistor_68 (.in(1'b1), .out(transistor_17_out), .gate(b0));
  Transistor #(.\type ("n")) transistor_69 (.in(transistor_70_out), .out(transistor_17_out), .gate(transistor_2_out));
  Transistor #(.\type ("n")) transistor_70 (.in(1'b0), .out(transistor_70_out), .gate(b0));
  Transistor transistor_71 (.in(1'b1), .out(transistor_21_out), .gate(transistor_3_out));
  Transistor #(.\type ("n")) transistor_72 (.in(transistor_73_out), .out(transistor_21_out), .gate(sub));
  Transistor #(.\type ("n")) transistor_73 (.in(1'b0), .out(transistor_73_out), .gate(transistor_3_out));
  Transistor transistor_74 (.in(1'b1), .out(transistor_22_out), .gate(b1));
  Transistor #(.\type ("n")) transistor_75 (.in(transistor_76_out), .out(transistor_22_out), .gate(transistor_3_out));
  Transistor #(.\type ("n")) transistor_76 (.in(1'b0), .out(transistor_76_out), .gate(b1));
  Transistor transistor_77 (.in(1'b1), .out(transistor_26_out), .gate(transistor_4_out));
  Transistor #(.\type ("n")) transistor_78 (.in(transistor_79_out), .out(transistor_26_out), .gate(sub));
  Transistor #(.\type ("n")) transistor_79 (.in(1'b0), .out(transistor_79_out), .gate(transistor_4_out));
  Transistor transistor_80 (.in(1'b1), .out(transistor_27_out), .gate(b2));
  Transistor #(.\type ("n")) transistor_81 (.in(transistor_82_out), .out(transistor_27_out), .gate(transistor_4_out));
  Transistor #(.\type ("n")) transistor_82 (.in(1'b0), .out(transistor_82_out), .gate(b2));
  Transistor transistor_83 (.in(1'b1), .out(transistor_31_out), .gate(transistor_5_out));
  Transistor #(.\type ("n")) transistor_84 (.in(transistor_85_out), .out(transistor_31_out), .gate(sub));
  Transistor #(.\type ("n")) transistor_85 (.in(1'b0), .out(transistor_85_out), .gate(transistor_5_out));
  Transistor transistor_86 (.in(1'b1), .out(transistor_32_out), .gate(b3));
  Transistor #(.\type ("n")) transistor_87 (.in(transistor_88_out), .out(transistor_32_out), .gate(transistor_5_out));
  Transistor #(.\type ("n")) transistor_88 (.in(1'b0), .out(transistor_88_out), .gate(b3));
  Transistor transistor_89 (.in(1'b1), .out(transistor_36_out), .gate(transistor_6_out));
  Transistor #(.\type ("n")) transistor_90 (.in(transistor_91_out), .out(transistor_36_out), .gate(sub));
  Transistor #(.\type ("n")) transistor_91 (.in(1'b0), .out(transistor_91_out), .gate(transistor_6_out));
  Transistor transistor_92 (.in(1'b1), .out(transistor_37_out), .gate(b4));
  Transistor #(.\type ("n")) transistor_93 (.in(transistor_94_out), .out(transistor_37_out), .gate(transistor_6_out));
  Transistor #(.\type ("n")) transistor_94 (.in(1'b0), .out(transistor_94_out), .gate(b4));
  Transistor transistor_95 (.in(1'b1), .out(transistor_41_out), .gate(transistor_7_out));
  Transistor #(.\type ("n")) transistor_96 (.in(transistor_97_out), .out(transistor_41_out), .gate(sub));
  Transistor #(.\type ("n")) transistor_97 (.in(1'b0), .out(transistor_97_out), .gate(transistor_7_out));
  Transistor transistor_98 (.in(1'b1), .out(transistor_42_out), .gate(b5));
  Transistor #(.\type ("n")) transistor_99 (.in(transistor_100_out), .out(transistor_42_out), .gate(transistor_7_out));
  Transistor #(.\type ("n")) transistor_100 (.in(1'b0), .out(transistor_100_out), .gate(b5));
  Transistor transistor_101 (.in(1'b1), .out(transistor_46_out), .gate(transistor_8_out));
  Transistor #(.\type ("n")) transistor_102 (.in(transistor_103_out), .out(transistor_46_out), .gate(sub));
  Transistor #(.\type ("n")) transistor_103 (.in(1'b0), .out(transistor_103_out), .gate(transistor_8_out));
  Transistor transistor_104 (.in(1'b1), .out(transistor_48_out), .gate(b6));
  Transistor #(.\type ("n")) transistor_105 (.in(transistor_106_out), .out(transistor_48_out), .gate(transistor_8_out));
  Transistor #(.\type ("n")) transistor_106 (.in(1'b0), .out(transistor_106_out), .gate(b6));
  Transistor transistor_107 (.in(1'b1), .out(transistor_51_out), .gate(transistor_9_out));
  Transistor #(.\type ("n")) transistor_108 (.in(transistor_109_out), .out(transistor_51_out), .gate(sub));
  Transistor #(.\type ("n")) transistor_109 (.in(1'b0), .out(transistor_109_out), .gate(transistor_9_out));
  Transistor transistor_110 (.in(1'b1), .out(transistor_53_out), .gate(b7));
  Transistor #(.\type ("n")) transistor_111 (.in(transistor_112_out), .out(transistor_53_out), .gate(transistor_9_out));
  Transistor #(.\type ("n")) transistor_112 (.in(1'b0), .out(transistor_112_out), .gate(b7));
  Transistor transistor_113 (.in(1'b1), .out(transistor_113_out), .gate(transistor_10_out));
  Transistor transistor_114 (.in(1'b1), .out(transistor_113_out), .gate(transistor_574_out));
  Transistor #(.\type ("n")) transistor_115 (
    .in(transistor_116_out), .out(transistor_113_out), .gate(transistor_574_out));
  Transistor #(.\type ("n")) transistor_116 (.in(1'b0), .out(transistor_116_out), .gate(transistor_10_out));
  Transistor transistor_117 (.in(1'b1), .out(transistor_117_out), .gate(transistor_10_out));
  Transistor transistor_118 (.in(1'b1), .out(transistor_117_out), .gate(sub));
  Transistor #(.\type ("n")) transistor_119 (
    .in(transistor_120_out), .out(transistor_117_out), .gate(transistor_10_out));
  Transistor #(.\type ("n")) transistor_120 (.in(1'b0), .out(transistor_120_out), .gate(sub));
  Transistor transistor_121 (.in(1'b1), .out(transistor_121_out), .gate(transistor_12_out));
  Transistor transistor_122 (.in(1'b1), .out(transistor_121_out), .gate(transistor_11_out));
  Transistor #(.\type ("n")) transistor_123 (
    .in(transistor_124_out), .out(transistor_121_out), .gate(transistor_11_out));
  Transistor #(.\type ("n")) transistor_124 (.in(1'b0), .out(transistor_124_out), .gate(transistor_12_out));
  Transistor transistor_125 (.in(1'b1), .out(transistor_125_out), .gate(transistor_17_out));
  Transistor transistor_126 (.in(1'b1), .out(transistor_125_out), .gate(transistor_16_out));
  Transistor #(.\type ("n")) transistor_127 (
    .in(transistor_128_out), .out(transistor_125_out), .gate(transistor_16_out));
  Transistor #(.\type ("n")) transistor_128 (.in(1'b0), .out(transistor_128_out), .gate(transistor_17_out));
  Transistor transistor_129 (.in(1'b1), .out(transistor_129_out), .gate(transistor_21_out));
  Transistor transistor_130 (.in(1'b1), .out(transistor_129_out), .gate(transistor_22_out));
  Transistor #(.\type ("n")) transistor_131 (
    .in(transistor_132_out), .out(transistor_129_out), .gate(transistor_21_out));
  Transistor #(.\type ("n")) transistor_132 (.in(1'b0), .out(transistor_132_out), .gate(transistor_22_out));
  Transistor transistor_133 (.in(1'b1), .out(transistor_133_out), .gate(transistor_26_out));
  Transistor transistor_134 (.in(1'b1), .out(transistor_133_out), .gate(transistor_27_out));
  Transistor #(.\type ("n")) transistor_135 (
    .in(transistor_136_out), .out(transistor_133_out), .gate(transistor_26_out));
  Transistor #(.\type ("n")) transistor_136 (.in(1'b0), .out(transistor_136_out), .gate(transistor_27_out));
  Transistor transistor_137 (.in(1'b1), .out(transistor_137_out), .gate(transistor_31_out));
  Transistor transistor_138 (.in(1'b1), .out(transistor_137_out), .gate(transistor_32_out));
  Transistor #(.\type ("n")) transistor_139 (
    .in(transistor_140_out), .out(transistor_137_out), .gate(transistor_31_out));
  Transistor #(.\type ("n")) transistor_140 (.in(1'b0), .out(transistor_140_out), .gate(transistor_32_out));
  Transistor transistor_141 (.in(1'b1), .out(transistor_141_out), .gate(transistor_36_out));
  Transistor transistor_142 (.in(1'b1), .out(transistor_141_out), .gate(transistor_37_out));
  Transistor #(.\type ("n")) transistor_143 (
    .in(transistor_144_out), .out(transistor_141_out), .gate(transistor_36_out));
  Transistor #(.\type ("n")) transistor_144 (.in(1'b0), .out(transistor_144_out), .gate(transistor_37_out));
  Transistor transistor_145 (.in(1'b1), .out(transistor_145_out), .gate(transistor_41_out));
  Transistor transistor_146 (.in(1'b1), .out(transistor_145_out), .gate(transistor_42_out));
  Transistor #(.\type ("n")) transistor_147 (
    .in(transistor_148_out), .out(transistor_145_out), .gate(transistor_41_out));
  Transistor #(.\type ("n")) transistor_148 (.in(1'b0), .out(transistor_148_out), .gate(transistor_42_out));
  Transistor transistor_149 (.in(1'b1), .out(transistor_149_out), .gate(transistor_48_out));
  Transistor transistor_150 (.in(1'b1), .out(transistor_149_out), .gate(transistor_46_out));
  Transistor #(.\type ("n")) transistor_151 (
    .in(transistor_152_out), .out(transistor_149_out), .gate(transistor_46_out));
  Transistor #(.\type ("n")) transistor_152 (.in(1'b0), .out(transistor_152_out), .gate(transistor_48_out));
  Transistor transistor_153 (.in(1'b1), .out(transistor_153_out), .gate(transistor_53_out));
  Transistor transistor_154 (.in(1'b1), .out(transistor_153_out), .gate(transistor_51_out));
  Transistor #(.\type ("n")) transistor_155 (
    .in(transistor_156_out), .out(transistor_153_out), .gate(transistor_51_out));
  Transistor #(.\type ("n")) transistor_156 (.in(1'b0), .out(transistor_156_out), .gate(transistor_53_out));
  Transistor transistor_157 (.in(1'b1), .out(cout), .gate(transistor_117_out));
  Transistor transistor_158 (.in(1'b1), .out(cout), .gate(transistor_113_out));
  Transistor #(.\type ("n")) transistor_159 (.in(transistor_160_out), .out(cout), .gate(transistor_113_out));
  Transistor #(.\type ("n")) transistor_160 (.in(1'b0), .out(transistor_160_out), .gate(transistor_117_out));
  Transistor transistor_161 (.in(1'b1), .out(transistor_161_out), .gate(a0));
  Transistor transistor_162 (.in(1'b1), .out(transistor_162_out), .gate(a1));
  Transistor transistor_163 (.in(1'b1), .out(transistor_163_out), .gate(a2));
  Transistor transistor_164 (.in(1'b1), .out(transistor_164_out), .gate(a3));
  Transistor transistor_165 (.in(1'b1), .out(transistor_165_out), .gate(a4));
  Transistor transistor_166 (.in(1'b1), .out(transistor_166_out), .gate(a5));
  Transistor transistor_167 (.in(1'b1), .out(transistor_167_out), .gate(a6));
  Transistor transistor_168 (.in(1'b1), .out(transistor_168_out), .gate(a7));
  Transistor transistor_169 (.in(1'b1), .out(transistor_161_out), .gate(transistor_125_out));
  Transistor #(.\type ("n")) transistor_170 (.in(transistor_171_out), .out(transistor_161_out), .gate(a0));
  Transistor #(.\type ("n")) transistor_171 (.in(1'b0), .out(transistor_171_out), .gate(transistor_125_out));
  Transistor transistor_172 (.in(1'b1), .out(transistor_162_out), .gate(transistor_129_out));
  Transistor #(.\type ("n")) transistor_173 (.in(transistor_174_out), .out(transistor_162_out), .gate(a1));
  Transistor #(.\type ("n")) transistor_174 (.in(1'b0), .out(transistor_174_out), .gate(transistor_129_out));
  Transistor transistor_175 (.in(1'b1), .out(transistor_163_out), .gate(transistor_133_out));
  Transistor #(.\type ("n")) transistor_176 (.in(transistor_177_out), .out(transistor_163_out), .gate(a2));
  Transistor #(.\type ("n")) transistor_177 (.in(1'b0), .out(transistor_177_out), .gate(transistor_133_out));
  Transistor transistor_178 (.in(1'b1), .out(transistor_164_out), .gate(transistor_137_out));
  Transistor #(.\type ("n")) transistor_179 (.in(transistor_180_out), .out(transistor_164_out), .gate(a3));
  Transistor #(.\type ("n")) transistor_180 (.in(1'b0), .out(transistor_180_out), .gate(transistor_137_out));
  Transistor transistor_181 (.in(1'b1), .out(transistor_165_out), .gate(transistor_141_out));
  Transistor #(.\type ("n")) transistor_182 (.in(transistor_183_out), .out(transistor_165_out), .gate(a4));
  Transistor #(.\type ("n")) transistor_183 (.in(1'b0), .out(transistor_183_out), .gate(transistor_141_out));
  Transistor transistor_184 (.in(1'b1), .out(transistor_166_out), .gate(transistor_145_out));
  Transistor #(.\type ("n")) transistor_185 (.in(transistor_186_out), .out(transistor_166_out), .gate(a5));
  Transistor #(.\type ("n")) transistor_186 (.in(1'b0), .out(transistor_186_out), .gate(transistor_145_out));
  Transistor transistor_187 (.in(1'b1), .out(transistor_167_out), .gate(transistor_149_out));
  Transistor #(.\type ("n")) transistor_188 (.in(transistor_189_out), .out(transistor_167_out), .gate(a6));
  Transistor #(.\type ("n")) transistor_189 (.in(1'b0), .out(transistor_189_out), .gate(transistor_149_out));
  Transistor transistor_190 (.in(1'b1), .out(transistor_168_out), .gate(transistor_153_out));
  Transistor #(.\type ("n")) transistor_191 (.in(transistor_192_out), .out(transistor_168_out), .gate(a7));
  Transistor #(.\type ("n")) transistor_192 (.in(1'b0), .out(transistor_192_out), .gate(transistor_153_out));
  Transistor transistor_193 (.in(1'b1), .out(transistor_193_out), .gate(transistor_161_out));
  Transistor transistor_194 (.in(1'b1), .out(transistor_193_out), .gate(a0));
  Transistor #(.\type ("n")) transistor_195 (.in(transistor_196_out), .out(transistor_193_out), .gate(a0));
  Transistor #(.\type ("n")) transistor_196 (.in(1'b0), .out(transistor_196_out), .gate(transistor_161_out));
  Transistor transistor_197 (.in(1'b1), .out(transistor_197_out), .gate(transistor_161_out));
  Transistor transistor_198 (.in(1'b1), .out(transistor_197_out), .gate(transistor_125_out));
  Transistor #(.\type ("n")) transistor_199 (
    .in(transistor_200_out), .out(transistor_197_out), .gate(transistor_161_out));
  Transistor #(.\type ("n")) transistor_200 (.in(1'b0), .out(transistor_200_out), .gate(transistor_125_out));
  Transistor transistor_201 (.in(1'b1), .out(transistor_201_out), .gate(transistor_265_out));
  Transistor transistor_202 (.in(1'b1), .out(transistor_202_out), .gate(a1));
  Transistor transistor_203 (.in(1'b1), .out(transistor_202_out), .gate(transistor_162_out));
  Transistor #(.\type ("n")) transistor_204 (.in(transistor_205_out), .out(transistor_202_out), .gate(a1));
  Transistor #(.\type ("n")) transistor_205 (.in(1'b0), .out(transistor_205_out), .gate(transistor_162_out));
  Transistor transistor_206 (.in(1'b1), .out(transistor_206_out), .gate(transistor_162_out));
  Transistor transistor_207 (.in(1'b1), .out(transistor_206_out), .gate(transistor_129_out));
  Transistor #(.\type ("n")) transistor_208 (
    .in(transistor_209_out), .out(transistor_206_out), .gate(transistor_162_out));
  Transistor #(.\type ("n")) transistor_209 (.in(1'b0), .out(transistor_209_out), .gate(transistor_129_out));
  Transistor transistor_210 (.in(1'b1), .out(transistor_210_out), .gate(transistor_274_out));
  Transistor transistor_211 (.in(1'b1), .out(transistor_211_out), .gate(transistor_163_out));
  Transistor transistor_212 (.in(1'b1), .out(transistor_211_out), .gate(a2));
  Transistor #(.\type ("n")) transistor_213 (.in(transistor_214_out), .out(transistor_211_out), .gate(a2));
  Transistor #(.\type ("n")) transistor_214 (.in(1'b0), .out(transistor_214_out), .gate(transistor_163_out));
  Transistor transistor_215 (.in(1'b1), .out(transistor_215_out), .gate(transistor_133_out));
  Transistor transistor_216 (.in(1'b1), .out(transistor_215_out), .gate(transistor_163_out));
  Transistor #(.\type ("n")) transistor_217 (
    .in(transistor_218_out), .out(transistor_215_out), .gate(transistor_163_out));
  Transistor #(.\type ("n")) transistor_218 (.in(1'b0), .out(transistor_218_out), .gate(transistor_133_out));
  Transistor transistor_219 (.in(1'b1), .out(transistor_219_out), .gate(transistor_283_out));
  Transistor transistor_220 (.in(1'b1), .out(transistor_220_out), .gate(transistor_164_out));
  Transistor transistor_221 (.in(1'b1), .out(transistor_220_out), .gate(a3));
  Transistor #(.\type ("n")) transistor_222 (.in(transistor_223_out), .out(transistor_220_out), .gate(a3));
  Transistor #(.\type ("n")) transistor_223 (.in(1'b0), .out(transistor_223_out), .gate(transistor_164_out));
  Transistor transistor_224 (.in(1'b1), .out(transistor_224_out), .gate(transistor_137_out));
  Transistor transistor_225 (.in(1'b1), .out(transistor_224_out), .gate(transistor_164_out));
  Transistor #(.\type ("n")) transistor_226 (
    .in(transistor_227_out), .out(transistor_224_out), .gate(transistor_164_out));
  Transistor #(.\type ("n")) transistor_227 (.in(1'b0), .out(transistor_227_out), .gate(transistor_137_out));
  Transistor transistor_228 (.in(1'b1), .out(transistor_228_out), .gate(transistor_292_out));
  Transistor transistor_229 (.in(1'b1), .out(transistor_229_out), .gate(a4));
  Transistor transistor_230 (.in(1'b1), .out(transistor_229_out), .gate(transistor_165_out));
  Transistor #(.\type ("n")) transistor_231 (.in(transistor_232_out), .out(transistor_229_out), .gate(a4));
  Transistor #(.\type ("n")) transistor_232 (.in(1'b0), .out(transistor_232_out), .gate(transistor_165_out));
  Transistor transistor_233 (.in(1'b1), .out(transistor_233_out), .gate(transistor_165_out));
  Transistor transistor_234 (.in(1'b1), .out(transistor_233_out), .gate(transistor_141_out));
  Transistor #(.\type ("n")) transistor_235 (
    .in(transistor_236_out), .out(transistor_233_out), .gate(transistor_165_out));
  Transistor #(.\type ("n")) transistor_236 (.in(1'b0), .out(transistor_236_out), .gate(transistor_141_out));
  Transistor transistor_237 (.in(1'b1), .out(transistor_237_out), .gate(transistor_301_out));
  Transistor transistor_238 (.in(1'b1), .out(transistor_238_out), .gate(a5));
  Transistor transistor_239 (.in(1'b1), .out(transistor_238_out), .gate(transistor_166_out));
  Transistor #(.\type ("n")) transistor_240 (.in(transistor_241_out), .out(transistor_238_out), .gate(a5));
  Transistor #(.\type ("n")) transistor_241 (.in(1'b0), .out(transistor_241_out), .gate(transistor_166_out));
  Transistor transistor_242 (.in(1'b1), .out(transistor_242_out), .gate(transistor_166_out));
  Transistor transistor_243 (.in(1'b1), .out(transistor_242_out), .gate(transistor_145_out));
  Transistor #(.\type ("n")) transistor_244 (
    .in(transistor_245_out), .out(transistor_242_out), .gate(transistor_166_out));
  Transistor #(.\type ("n")) transistor_245 (.in(1'b0), .out(transistor_245_out), .gate(transistor_145_out));
  Transistor transistor_246 (.in(1'b1), .out(transistor_246_out), .gate(transistor_310_out));
  Transistor transistor_247 (.in(1'b1), .out(transistor_247_out), .gate(a6));
  Transistor transistor_248 (.in(1'b1), .out(transistor_247_out), .gate(transistor_167_out));
  Transistor #(.\type ("n")) transistor_249 (.in(transistor_250_out), .out(transistor_247_out), .gate(a6));
  Transistor #(.\type ("n")) transistor_250 (.in(1'b0), .out(transistor_250_out), .gate(transistor_167_out));
  Transistor transistor_251 (.in(1'b1), .out(transistor_251_out), .gate(transistor_167_out));
  Transistor transistor_252 (.in(1'b1), .out(transistor_251_out), .gate(transistor_149_out));
  Transistor #(.\type ("n")) transistor_253 (
    .in(transistor_254_out), .out(transistor_251_out), .gate(transistor_167_out));
  Transistor #(.\type ("n")) transistor_254 (.in(1'b0), .out(transistor_254_out), .gate(transistor_149_out));
  Transistor transistor_255 (.in(1'b1), .out(transistor_255_out), .gate(transistor_319_out));
  Transistor transistor_256 (.in(1'b1), .out(transistor_256_out), .gate(transistor_168_out));
  Transistor transistor_257 (.in(1'b1), .out(transistor_256_out), .gate(a7));
  Transistor #(.\type ("n")) transistor_258 (.in(transistor_259_out), .out(transistor_256_out), .gate(a7));
  Transistor #(.\type ("n")) transistor_259 (.in(1'b0), .out(transistor_259_out), .gate(transistor_168_out));
  Transistor transistor_260 (.in(1'b1), .out(transistor_260_out), .gate(transistor_168_out));
  Transistor transistor_261 (.in(1'b1), .out(transistor_260_out), .gate(transistor_153_out));
  Transistor #(.\type ("n")) transistor_262 (
    .in(transistor_263_out), .out(transistor_260_out), .gate(transistor_168_out));
  Transistor #(.\type ("n")) transistor_263 (.in(1'b0), .out(transistor_263_out), .gate(transistor_153_out));
  Transistor transistor_264 (.in(1'b1), .out(transistor_264_out), .gate(transistor_328_out));
  Transistor transistor_265 (.in(1'b1), .out(transistor_265_out), .gate(transistor_193_out));
  Transistor transistor_266 (.in(1'b1), .out(transistor_265_out), .gate(transistor_197_out));
  Transistor #(.\type ("n")) transistor_267 (
    .in(transistor_268_out), .out(transistor_265_out), .gate(transistor_193_out));
  Transistor #(.\type ("n")) transistor_268 (.in(1'b0), .out(transistor_268_out), .gate(transistor_197_out));
  Transistor transistor_269 (.in(1'b1), .out(transistor_201_out), .gate(transistor_121_out));
  Transistor transistor_270 (.in(1'b1), .out(transistor_270_out), .gate(transistor_201_out));
  Transistor #(.\type ("n")) transistor_271 (
    .in(transistor_273_out), .out(transistor_201_out), .gate(transistor_265_out));
  Transistor #(.\type ("n")) transistor_272 (.in(1'b0), .out(transistor_270_out), .gate(transistor_201_out));
  Transistor #(.\type ("n")) transistor_273 (.in(1'b0), .out(transistor_273_out), .gate(transistor_121_out));
  Transistor transistor_274 (.in(1'b1), .out(transistor_274_out), .gate(transistor_202_out));
  Transistor transistor_275 (.in(1'b1), .out(transistor_274_out), .gate(transistor_206_out));
  Transistor #(.\type ("n")) transistor_276 (
    .in(transistor_277_out), .out(transistor_274_out), .gate(transistor_202_out));
  Transistor #(.\type ("n")) transistor_277 (.in(1'b0), .out(transistor_277_out), .gate(transistor_206_out));
  Transistor transistor_278 (.in(1'b1), .out(transistor_278_out), .gate(transistor_210_out));
  Transistor transistor_279 (.in(1'b1), .out(transistor_210_out), .gate(transistor_510_out));
  Transistor #(.\type ("n")) transistor_280 (.in(1'b0), .out(transistor_278_out), .gate(transistor_210_out));
  Transistor #(.\type ("n")) transistor_281 (
    .in(transistor_282_out), .out(transistor_210_out), .gate(transistor_274_out));
  Transistor #(.\type ("n")) transistor_282 (.in(1'b0), .out(transistor_282_out), .gate(transistor_510_out));
  Transistor transistor_283 (.in(1'b1), .out(transistor_283_out), .gate(transistor_215_out));
  Transistor transistor_284 (.in(1'b1), .out(transistor_283_out), .gate(transistor_211_out));
  Transistor #(.\type ("n")) transistor_285 (
    .in(transistor_286_out), .out(transistor_283_out), .gate(transistor_211_out));
  Transistor #(.\type ("n")) transistor_286 (.in(1'b0), .out(transistor_286_out), .gate(transistor_215_out));
  Transistor transistor_287 (.in(1'b1), .out(transistor_287_out), .gate(transistor_219_out));
  Transistor transistor_288 (.in(1'b1), .out(transistor_219_out), .gate(transistor_519_out));
  Transistor #(.\type ("n")) transistor_289 (
    .in(transistor_291_out), .out(transistor_219_out), .gate(transistor_283_out));
  Transistor #(.\type ("n")) transistor_290 (.in(1'b0), .out(transistor_287_out), .gate(transistor_219_out));
  Transistor #(.\type ("n")) transistor_291 (.in(1'b0), .out(transistor_291_out), .gate(transistor_519_out));
  Transistor transistor_292 (.in(1'b1), .out(transistor_292_out), .gate(transistor_224_out));
  Transistor transistor_293 (.in(1'b1), .out(transistor_292_out), .gate(transistor_220_out));
  Transistor #(.\type ("n")) transistor_294 (
    .in(transistor_295_out), .out(transistor_292_out), .gate(transistor_220_out));
  Transistor #(.\type ("n")) transistor_295 (.in(1'b0), .out(transistor_295_out), .gate(transistor_224_out));
  Transistor transistor_296 (.in(1'b1), .out(transistor_296_out), .gate(transistor_228_out));
  Transistor transistor_297 (.in(1'b1), .out(transistor_228_out), .gate(transistor_529_out));
  Transistor #(.\type ("n")) transistor_298 (
    .in(transistor_300_out), .out(transistor_228_out), .gate(transistor_292_out));
  Transistor #(.\type ("n")) transistor_299 (.in(1'b0), .out(transistor_296_out), .gate(transistor_228_out));
  Transistor #(.\type ("n")) transistor_300 (.in(1'b0), .out(transistor_300_out), .gate(transistor_529_out));
  Transistor transistor_301 (.in(1'b1), .out(transistor_301_out), .gate(transistor_229_out));
  Transistor transistor_302 (.in(1'b1), .out(transistor_301_out), .gate(transistor_233_out));
  Transistor #(.\type ("n")) transistor_303 (
    .in(transistor_304_out), .out(transistor_301_out), .gate(transistor_229_out));
  Transistor #(.\type ("n")) transistor_304 (.in(1'b0), .out(transistor_304_out), .gate(transistor_233_out));
  Transistor transistor_305 (.in(1'b1), .out(transistor_237_out), .gate(transistor_538_out));
  Transistor transistor_306 (.in(1'b1), .out(transistor_306_out), .gate(transistor_237_out));
  Transistor #(.\type ("n")) transistor_307 (
    .in(transistor_309_out), .out(transistor_237_out), .gate(transistor_301_out));
  Transistor #(.\type ("n")) transistor_308 (.in(1'b0), .out(transistor_306_out), .gate(transistor_237_out));
  Transistor #(.\type ("n")) transistor_309 (.in(1'b0), .out(transistor_309_out), .gate(transistor_538_out));
  Transistor transistor_310 (.in(1'b1), .out(transistor_310_out), .gate(transistor_242_out));
  Transistor transistor_311 (.in(1'b1), .out(transistor_310_out), .gate(transistor_238_out));
  Transistor #(.\type ("n")) transistor_312 (
    .in(transistor_313_out), .out(transistor_310_out), .gate(transistor_238_out));
  Transistor #(.\type ("n")) transistor_313 (.in(1'b0), .out(transistor_313_out), .gate(transistor_242_out));
  Transistor transistor_314 (.in(1'b1), .out(transistor_314_out), .gate(transistor_246_out));
  Transistor transistor_315 (.in(1'b1), .out(transistor_246_out), .gate(transistor_547_out));
  Transistor #(.\type ("n")) transistor_316 (
    .in(transistor_318_out), .out(transistor_246_out), .gate(transistor_310_out));
  Transistor #(.\type ("n")) transistor_317 (.in(1'b0), .out(transistor_314_out), .gate(transistor_246_out));
  Transistor #(.\type ("n")) transistor_318 (.in(1'b0), .out(transistor_318_out), .gate(transistor_547_out));
  Transistor transistor_319 (.in(1'b1), .out(transistor_319_out), .gate(transistor_251_out));
  Transistor transistor_320 (.in(1'b1), .out(transistor_319_out), .gate(transistor_247_out));
  Transistor #(.\type ("n")) transistor_321 (
    .in(transistor_322_out), .out(transistor_319_out), .gate(transistor_247_out));
  Transistor #(.\type ("n")) transistor_322 (.in(1'b0), .out(transistor_322_out), .gate(transistor_251_out));
  Transistor transistor_323 (.in(1'b1), .out(transistor_323_out), .gate(transistor_255_out));
  Transistor transistor_324 (.in(1'b1), .out(transistor_255_out), .gate(transistor_555_out));
  Transistor #(.\type ("n")) transistor_325 (.in(1'b0), .out(transistor_323_out), .gate(transistor_255_out));
  Transistor #(.\type ("n")) transistor_326 (
    .in(transistor_327_out), .out(transistor_255_out), .gate(transistor_319_out));
  Transistor #(.\type ("n")) transistor_327 (.in(1'b0), .out(transistor_327_out), .gate(transistor_555_out));
  Transistor transistor_328 (.in(1'b1), .out(transistor_328_out), .gate(transistor_256_out));
  Transistor transistor_329 (.in(1'b1), .out(transistor_328_out), .gate(transistor_260_out));
  Transistor #(.\type ("n")) transistor_330 (
    .in(transistor_331_out), .out(transistor_328_out), .gate(transistor_256_out));
  Transistor #(.\type ("n")) transistor_331 (.in(1'b0), .out(transistor_331_out), .gate(transistor_260_out));
  Transistor transistor_332 (.in(1'b1), .out(transistor_264_out), .gate(transistor_565_out));
  Transistor transistor_333 (.in(1'b1), .out(transistor_333_out), .gate(transistor_264_out));
  Transistor #(.\type ("n")) transistor_334 (.in(1'b0), .out(transistor_333_out), .gate(transistor_264_out));
  Transistor #(.\type ("n")) transistor_335 (
    .in(transistor_336_out), .out(transistor_264_out), .gate(transistor_328_out));
  Transistor #(.\type ("n")) transistor_336 (.in(1'b0), .out(transistor_336_out), .gate(transistor_565_out));
  Transistor transistor_337 (.in(1'b1), .out(transistor_337_out), .gate(transistor_565_out));
  Transistor transistor_338 (.in(1'b1), .out(transistor_337_out), .gate(transistor_574_out));
  Transistor #(.\type ("n")) transistor_339 (
    .in(transistor_340_out), .out(transistor_337_out), .gate(transistor_574_out));
  Transistor #(.\type ("n")) transistor_340 (.in(1'b0), .out(transistor_340_out), .gate(transistor_565_out));
  Transistor transistor_341 (.in(1'b1), .out(transistor_341_out), .gate(transistor_265_out));
  Transistor transistor_342 (.in(1'b1), .out(transistor_342_out), .gate(a0));
  Transistor transistor_343 (.in(1'b1), .out(transistor_343_out), .gate(transistor_274_out));
  Transistor transistor_344 (.in(1'b1), .out(transistor_344_out), .gate(a1));
  Transistor transistor_345 (.in(1'b1), .out(transistor_345_out), .gate(transistor_283_out));
  Transistor transistor_346 (.in(1'b1), .out(transistor_346_out), .gate(a2));
  Transistor transistor_347 (.in(1'b1), .out(transistor_347_out), .gate(transistor_292_out));
  Transistor transistor_348 (.in(1'b1), .out(transistor_348_out), .gate(a3));
  Transistor transistor_349 (.in(1'b1), .out(transistor_349_out), .gate(transistor_301_out));
  Transistor transistor_350 (.in(1'b1), .out(transistor_350_out), .gate(a4));
  Transistor transistor_351 (.in(1'b1), .out(transistor_351_out), .gate(transistor_310_out));
  Transistor transistor_352 (.in(1'b1), .out(transistor_352_out), .gate(a5));
  Transistor transistor_353 (.in(1'b1), .out(transistor_353_out), .gate(transistor_319_out));
  Transistor transistor_354 (.in(1'b1), .out(transistor_354_out), .gate(a6));
  Transistor transistor_355 (.in(1'b1), .out(transistor_355_out), .gate(transistor_328_out));
  Transistor transistor_356 (.in(1'b1), .out(transistor_356_out), .gate(a7));
  Transistor transistor_357 (.in(1'b1), .out(transistor_357_out), .gate(transistor_574_out));
  Transistor transistor_358 (.in(1'b1), .out(transistor_358_out), .gate(transistor_337_out));
  Transistor transistor_359 (.in(1'b1), .out(transistor_359_out), .gate(transistor_265_out));
  Transistor transistor_360 (.in(1'b1), .out(transistor_341_out), .gate(transistor_121_out));
  Transistor transistor_361 (.in(1'b1), .out(transistor_361_out), .gate(transistor_341_out));
  Transistor #(.\type ("n")) transistor_362 (
    .in(transistor_363_out), .out(transistor_341_out), .gate(transistor_265_out));
  Transistor #(.\type ("n")) transistor_363 (.in(1'b0), .out(transistor_363_out), .gate(transistor_121_out));
  Transistor transistor_364 (.in(1'b1), .out(transistor_364_out), .gate(transistor_342_out));
  Transistor transistor_365 (.in(1'b1), .out(transistor_342_out), .gate(transistor_125_out));
  Transistor #(.\type ("n")) transistor_366 (.in(1'b0), .out(transistor_364_out), .gate(transistor_342_out));
  Transistor #(.\type ("n")) transistor_367 (.in(transistor_368_out), .out(transistor_342_out), .gate(a0));
  Transistor #(.\type ("n")) transistor_368 (.in(1'b0), .out(transistor_368_out), .gate(transistor_125_out));
  Transistor transistor_369 (.in(1'b1), .out(transistor_369_out), .gate(transistor_274_out));
  Transistor transistor_370 (.in(1'b1), .out(transistor_370_out), .gate(transistor_343_out));
  Transistor transistor_371 (.in(1'b1), .out(transistor_343_out), .gate(transistor_510_out));
  Transistor #(.\type ("n")) transistor_372 (
    .in(transistor_373_out), .out(transistor_343_out), .gate(transistor_274_out));
  Transistor #(.\type ("n")) transistor_373 (.in(1'b0), .out(transistor_373_out), .gate(transistor_510_out));
  Transistor transistor_374 (.in(1'b1), .out(transistor_344_out), .gate(transistor_129_out));
  Transistor transistor_375 (.in(1'b1), .out(transistor_375_out), .gate(transistor_344_out));
  Transistor #(.\type ("n")) transistor_376 (.in(1'b0), .out(transistor_375_out), .gate(transistor_344_out));
  Transistor #(.\type ("n")) transistor_377 (.in(transistor_378_out), .out(transistor_344_out), .gate(a1));
  Transistor #(.\type ("n")) transistor_378 (.in(1'b0), .out(transistor_378_out), .gate(transistor_129_out));
  Transistor transistor_379 (.in(1'b1), .out(transistor_379_out), .gate(transistor_283_out));
  Transistor transistor_380 (.in(1'b1), .out(transistor_345_out), .gate(transistor_519_out));
  Transistor transistor_381 (.in(1'b1), .out(transistor_381_out), .gate(transistor_345_out));
  Transistor #(.\type ("n")) transistor_382 (
    .in(transistor_383_out), .out(transistor_345_out), .gate(transistor_283_out));
  Transistor #(.\type ("n")) transistor_383 (.in(1'b0), .out(transistor_383_out), .gate(transistor_519_out));
  Transistor transistor_384 (.in(1'b1), .out(transistor_346_out), .gate(transistor_133_out));
  Transistor transistor_385 (.in(1'b1), .out(transistor_385_out), .gate(transistor_346_out));
  Transistor #(.\type ("n")) transistor_386 (.in(1'b0), .out(transistor_385_out), .gate(transistor_346_out));
  Transistor #(.\type ("n")) transistor_387 (.in(transistor_388_out), .out(transistor_346_out), .gate(a2));
  Transistor #(.\type ("n")) transistor_388 (.in(1'b0), .out(transistor_388_out), .gate(transistor_133_out));
  Transistor transistor_389 (.in(1'b1), .out(transistor_389_out), .gate(transistor_292_out));
  Transistor transistor_390 (.in(1'b1), .out(transistor_347_out), .gate(transistor_529_out));
  Transistor transistor_391 (.in(1'b1), .out(transistor_391_out), .gate(transistor_347_out));
  Transistor #(.\type ("n")) transistor_392 (
    .in(transistor_393_out), .out(transistor_347_out), .gate(transistor_292_out));
  Transistor #(.\type ("n")) transistor_393 (.in(1'b0), .out(transistor_393_out), .gate(transistor_529_out));
  Transistor transistor_394 (.in(1'b1), .out(transistor_394_out), .gate(transistor_348_out));
  Transistor transistor_395 (.in(1'b1), .out(transistor_348_out), .gate(transistor_137_out));
  Transistor #(.\type ("n")) transistor_396 (.in(transistor_398_out), .out(transistor_348_out), .gate(a3));
  Transistor #(.\type ("n")) transistor_397 (.in(1'b0), .out(transistor_394_out), .gate(transistor_348_out));
  Transistor #(.\type ("n")) transistor_398 (.in(1'b0), .out(transistor_398_out), .gate(transistor_137_out));
  Transistor transistor_399 (.in(1'b1), .out(transistor_399_out), .gate(transistor_301_out));
  Transistor transistor_400 (.in(1'b1), .out(transistor_400_out), .gate(transistor_349_out));
  Transistor transistor_401 (.in(1'b1), .out(transistor_349_out), .gate(transistor_538_out));
  Transistor #(.\type ("n")) transistor_402 (
    .in(transistor_403_out), .out(transistor_349_out), .gate(transistor_301_out));
  Transistor #(.\type ("n")) transistor_403 (.in(1'b0), .out(transistor_403_out), .gate(transistor_538_out));
  Transistor transistor_404 (.in(1'b1), .out(transistor_404_out), .gate(transistor_350_out));
  Transistor transistor_405 (.in(1'b1), .out(transistor_350_out), .gate(transistor_141_out));
  Transistor #(.\type ("n")) transistor_406 (.in(1'b0), .out(transistor_404_out), .gate(transistor_350_out));
  Transistor #(.\type ("n")) transistor_407 (.in(transistor_408_out), .out(transistor_350_out), .gate(a4));
  Transistor #(.\type ("n")) transistor_408 (.in(1'b0), .out(transistor_408_out), .gate(transistor_141_out));
  Transistor transistor_409 (.in(1'b1), .out(transistor_409_out), .gate(transistor_310_out));
  Transistor transistor_410 (.in(1'b1), .out(transistor_351_out), .gate(transistor_547_out));
  Transistor transistor_411 (.in(1'b1), .out(transistor_411_out), .gate(transistor_351_out));
  Transistor #(.\type ("n")) transistor_412 (
    .in(transistor_413_out), .out(transistor_351_out), .gate(transistor_310_out));
  Transistor #(.\type ("n")) transistor_413 (.in(1'b0), .out(transistor_413_out), .gate(transistor_547_out));
  Transistor transistor_414 (.in(1'b1), .out(transistor_352_out), .gate(transistor_145_out));
  Transistor transistor_415 (.in(1'b1), .out(transistor_415_out), .gate(transistor_352_out));
  Transistor #(.\type ("n")) transistor_416 (.in(1'b0), .out(transistor_415_out), .gate(transistor_352_out));
  Transistor #(.\type ("n")) transistor_417 (.in(transistor_418_out), .out(transistor_352_out), .gate(a5));
  Transistor #(.\type ("n")) transistor_418 (.in(1'b0), .out(transistor_418_out), .gate(transistor_145_out));
  Transistor transistor_419 (.in(1'b1), .out(transistor_419_out), .gate(transistor_319_out));
  Transistor transistor_420 (.in(1'b1), .out(transistor_353_out), .gate(transistor_555_out));
  Transistor transistor_421 (.in(1'b1), .out(transistor_421_out), .gate(transistor_353_out));
  Transistor #(.\type ("n")) transistor_422 (
    .in(transistor_423_out), .out(transistor_353_out), .gate(transistor_319_out));
  Transistor #(.\type ("n")) transistor_423 (.in(1'b0), .out(transistor_423_out), .gate(transistor_555_out));
  Transistor transistor_424 (.in(1'b1), .out(transistor_424_out), .gate(transistor_354_out));
  Transistor transistor_425 (.in(1'b1), .out(transistor_354_out), .gate(transistor_149_out));
  Transistor #(.\type ("n")) transistor_426 (.in(transistor_428_out), .out(transistor_354_out), .gate(a6));
  Transistor #(.\type ("n")) transistor_427 (.in(1'b0), .out(transistor_424_out), .gate(transistor_354_out));
  Transistor #(.\type ("n")) transistor_428 (.in(1'b0), .out(transistor_428_out), .gate(transistor_149_out));
  Transistor transistor_429 (.in(1'b1), .out(transistor_429_out), .gate(transistor_328_out));
  Transistor transistor_430 (.in(1'b1), .out(transistor_355_out), .gate(transistor_565_out));
  Transistor transistor_431 (.in(1'b1), .out(transistor_431_out), .gate(transistor_355_out));
  Transistor #(.\type ("n")) transistor_432 (
    .in(transistor_433_out), .out(transistor_355_out), .gate(transistor_328_out));
  Transistor #(.\type ("n")) transistor_433 (.in(1'b0), .out(transistor_433_out), .gate(transistor_565_out));
  Transistor transistor_434 (.in(1'b1), .out(transistor_356_out), .gate(transistor_153_out));
  Transistor transistor_435 (.in(1'b1), .out(transistor_435_out), .gate(transistor_356_out));
  Transistor #(.\type ("n")) transistor_436 (.in(1'b0), .out(transistor_435_out), .gate(transistor_356_out));
  Transistor #(.\type ("n")) transistor_437 (.in(transistor_438_out), .out(transistor_356_out), .gate(a7));
  Transistor #(.\type ("n")) transistor_438 (.in(1'b0), .out(transistor_438_out), .gate(transistor_153_out));
  Transistor transistor_439 (.in(1'b1), .out(transistor_357_out), .gate(transistor_337_out));
  Transistor #(.\type ("n")) transistor_440 (
    .in(transistor_441_out), .out(transistor_357_out), .gate(transistor_574_out));
  Transistor #(.\type ("n")) transistor_441 (.in(1'b0), .out(transistor_441_out), .gate(transistor_337_out));
  Transistor transistor_442 (.in(1'b1), .out(overflow), .gate(transistor_357_out));
  Transistor transistor_443 (.in(1'b1), .out(transistor_358_out), .gate(transistor_565_out));
  Transistor #(.\type ("n")) transistor_444 (
    .in(transistor_445_out), .out(transistor_358_out), .gate(transistor_337_out));
  Transistor #(.\type ("n")) transistor_445 (.in(1'b0), .out(transistor_445_out), .gate(transistor_565_out));
  Transistor transistor_446 (.in(1'b1), .out(transistor_359_out), .gate(transistor_341_out));
  Transistor #(.\type ("n")) transistor_447 (
    .in(transistor_448_out), .out(transistor_359_out), .gate(transistor_265_out));
  Transistor #(.\type ("n")) transistor_448 (.in(1'b0), .out(transistor_448_out), .gate(transistor_341_out));
  Transistor transistor_449 (.in(1'b1), .out(transistor_361_out), .gate(transistor_121_out));
  Transistor #(.\type ("n")) transistor_450 (
    .in(transistor_451_out), .out(transistor_361_out), .gate(transistor_341_out));
  Transistor #(.\type ("n")) transistor_451 (.in(1'b0), .out(transistor_451_out), .gate(transistor_121_out));
  Transistor #(.\type ("n")) transistor_452 (.in(1'b0), .out(transistor_452_out), .gate(transistor_270_out));
  Transistor transistor_453 (.in(1'b1), .out(transistor_369_out), .gate(transistor_343_out));
  Transistor #(.\type ("n")) transistor_454 (
    .in(transistor_455_out), .out(transistor_369_out), .gate(transistor_274_out));
  Transistor #(.\type ("n")) transistor_455 (.in(1'b0), .out(transistor_455_out), .gate(transistor_343_out));
  Transistor transistor_456 (.in(1'b1), .out(transistor_370_out), .gate(transistor_510_out));
  Transistor #(.\type ("n")) transistor_457 (
    .in(transistor_458_out), .out(transistor_370_out), .gate(transistor_343_out));
  Transistor #(.\type ("n")) transistor_458 (.in(1'b0), .out(transistor_458_out), .gate(transistor_510_out));
  Transistor #(.\type ("n")) transistor_459 (.in(1'b0), .out(transistor_459_out), .gate(transistor_278_out));
  Transistor transistor_460 (.in(1'b1), .out(transistor_379_out), .gate(transistor_345_out));
  Transistor #(.\type ("n")) transistor_461 (
    .in(transistor_462_out), .out(transistor_379_out), .gate(transistor_283_out));
  Transistor #(.\type ("n")) transistor_462 (.in(1'b0), .out(transistor_462_out), .gate(transistor_345_out));
  Transistor transistor_463 (.in(1'b1), .out(transistor_381_out), .gate(transistor_519_out));
  Transistor #(.\type ("n")) transistor_464 (
    .in(transistor_465_out), .out(transistor_381_out), .gate(transistor_345_out));
  Transistor #(.\type ("n")) transistor_465 (.in(1'b0), .out(transistor_465_out), .gate(transistor_519_out));
  Transistor #(.\type ("n")) transistor_466 (.in(1'b0), .out(transistor_466_out), .gate(transistor_287_out));
  Transistor transistor_467 (.in(1'b1), .out(transistor_389_out), .gate(transistor_347_out));
  Transistor #(.\type ("n")) transistor_468 (
    .in(transistor_469_out), .out(transistor_389_out), .gate(transistor_292_out));
  Transistor #(.\type ("n")) transistor_469 (.in(1'b0), .out(transistor_469_out), .gate(transistor_347_out));
  Transistor transistor_470 (.in(1'b1), .out(transistor_391_out), .gate(transistor_529_out));
  Transistor #(.\type ("n")) transistor_471 (
    .in(transistor_472_out), .out(transistor_391_out), .gate(transistor_347_out));
  Transistor #(.\type ("n")) transistor_472 (.in(1'b0), .out(transistor_472_out), .gate(transistor_529_out));
  Transistor #(.\type ("n")) transistor_473 (.in(1'b0), .out(transistor_473_out), .gate(transistor_296_out));
  Transistor transistor_474 (.in(1'b1), .out(transistor_399_out), .gate(transistor_349_out));
  Transistor #(.\type ("n")) transistor_475 (
    .in(transistor_476_out), .out(transistor_399_out), .gate(transistor_301_out));
  Transistor #(.\type ("n")) transistor_476 (.in(1'b0), .out(transistor_476_out), .gate(transistor_349_out));
  Transistor transistor_477 (.in(1'b1), .out(transistor_400_out), .gate(transistor_538_out));
  Transistor #(.\type ("n")) transistor_478 (
    .in(transistor_479_out), .out(transistor_400_out), .gate(transistor_349_out));
  Transistor #(.\type ("n")) transistor_479 (.in(1'b0), .out(transistor_479_out), .gate(transistor_538_out));
  Transistor #(.\type ("n")) transistor_480 (.in(1'b0), .out(transistor_480_out), .gate(transistor_306_out));
  Transistor transistor_481 (.in(1'b1), .out(transistor_409_out), .gate(transistor_351_out));
  Transistor #(.\type ("n")) transistor_482 (
    .in(transistor_483_out), .out(transistor_409_out), .gate(transistor_310_out));
  Transistor #(.\type ("n")) transistor_483 (.in(1'b0), .out(transistor_483_out), .gate(transistor_351_out));
  Transistor transistor_484 (.in(1'b1), .out(transistor_411_out), .gate(transistor_547_out));
  Transistor #(.\type ("n")) transistor_485 (
    .in(transistor_486_out), .out(transistor_411_out), .gate(transistor_351_out));
  Transistor #(.\type ("n")) transistor_486 (.in(1'b0), .out(transistor_486_out), .gate(transistor_547_out));
  Transistor #(.\type ("n")) transistor_487 (.in(1'b0), .out(transistor_487_out), .gate(transistor_314_out));
  Transistor transistor_488 (.in(1'b1), .out(transistor_419_out), .gate(transistor_353_out));
  Transistor #(.\type ("n")) transistor_489 (
    .in(transistor_490_out), .out(transistor_419_out), .gate(transistor_319_out));
  Transistor #(.\type ("n")) transistor_490 (.in(1'b0), .out(transistor_490_out), .gate(transistor_353_out));
  Transistor transistor_491 (.in(1'b1), .out(transistor_421_out), .gate(transistor_555_out));
  Transistor #(.\type ("n")) transistor_492 (
    .in(transistor_493_out), .out(transistor_421_out), .gate(transistor_353_out));
  Transistor #(.\type ("n")) transistor_493 (.in(1'b0), .out(transistor_493_out), .gate(transistor_555_out));
  Transistor #(.\type ("n")) transistor_494 (.in(1'b0), .out(transistor_494_out), .gate(transistor_323_out));
  Transistor transistor_495 (.in(1'b1), .out(transistor_429_out), .gate(transistor_355_out));
  Transistor #(.\type ("n")) transistor_496 (
    .in(transistor_497_out), .out(transistor_429_out), .gate(transistor_328_out));
  Transistor #(.\type ("n")) transistor_497 (.in(1'b0), .out(transistor_497_out), .gate(transistor_355_out));
  Transistor transistor_498 (.in(1'b1), .out(transistor_431_out), .gate(transistor_565_out));
  Transistor #(.\type ("n")) transistor_499 (
    .in(transistor_500_out), .out(transistor_431_out), .gate(transistor_355_out));
  Transistor #(.\type ("n")) transistor_500 (.in(1'b0), .out(transistor_500_out), .gate(transistor_565_out));
  Transistor #(.\type ("n")) transistor_501 (.in(1'b0), .out(transistor_501_out), .gate(transistor_333_out));
  Transistor transistor_502 (.in(1'b1), .out(overflow), .gate(transistor_358_out));
  Transistor #(.\type ("n")) transistor_503 (.in(transistor_504_out), .out(overflow), .gate(transistor_357_out));
  Transistor #(.\type ("n")) transistor_504 (.in(1'b0), .out(transistor_504_out), .gate(transistor_358_out));
  Transistor transistor_505 (.in(1'b1), .out(sum0), .gate(transistor_361_out));
  Transistor transistor_506 (.in(1'b1), .out(sum0), .gate(transistor_359_out));
  Transistor #(.\type ("n")) transistor_507 (.in(transistor_508_out), .out(sum0), .gate(transistor_359_out));
  Transistor #(.\type ("n")) transistor_508 (.in(1'b0), .out(transistor_508_out), .gate(transistor_361_out));
  Transistor transistor_509 (.in(1'b1), .out(transistor_509_out), .gate(transistor_270_out));
  Transistor transistor_510 (.in(1'b1), .out(transistor_510_out), .gate(transistor_452_out));
  Transistor transistor_511 (.in(transistor_509_out), .out(transistor_452_out), .gate(transistor_364_out));
  Transistor #(.\type ("n")) transistor_512 (.in(1'b0), .out(transistor_452_out), .gate(transistor_364_out));
  Transistor #(.\type ("n")) transistor_513 (.in(1'b0), .out(transistor_510_out), .gate(transistor_452_out));
  Transistor transistor_514 (.in(1'b1), .out(sum1), .gate(transistor_370_out));
  Transistor transistor_515 (.in(1'b1), .out(sum1), .gate(transistor_369_out));
  Transistor #(.\type ("n")) transistor_516 (.in(transistor_517_out), .out(sum1), .gate(transistor_369_out));
  Transistor #(.\type ("n")) transistor_517 (.in(1'b0), .out(transistor_517_out), .gate(transistor_370_out));
  Transistor transistor_518 (.in(1'b1), .out(transistor_518_out), .gate(transistor_278_out));
  Transistor transistor_519 (.in(1'b1), .out(transistor_519_out), .gate(transistor_459_out));
  Transistor transistor_520 (.in(transistor_518_out), .out(transistor_459_out), .gate(transistor_375_out));
  Transistor #(.\type ("n")) transistor_521 (.in(1'b0), .out(transistor_519_out), .gate(transistor_459_out));
  Transistor #(.\type ("n")) transistor_522 (.in(1'b0), .out(transistor_459_out), .gate(transistor_375_out));
  Transistor transistor_523 (.in(1'b1), .out(sum2), .gate(transistor_379_out));
  Transistor transistor_524 (.in(1'b1), .out(sum2), .gate(transistor_381_out));
  Transistor #(.\type ("n")) transistor_525 (.in(transistor_526_out), .out(sum2), .gate(transistor_379_out));
  Transistor #(.\type ("n")) transistor_526 (.in(1'b0), .out(transistor_526_out), .gate(transistor_381_out));
  Transistor transistor_527 (.in(1'b1), .out(transistor_527_out), .gate(transistor_287_out));
  Transistor transistor_528 (.in(transistor_527_out), .out(transistor_466_out), .gate(transistor_385_out));
  Transistor transistor_529 (.in(1'b1), .out(transistor_529_out), .gate(transistor_466_out));
  Transistor #(.\type ("n")) transistor_530 (.in(1'b0), .out(transistor_529_out), .gate(transistor_466_out));
  Transistor #(.\type ("n")) transistor_531 (.in(1'b0), .out(transistor_466_out), .gate(transistor_385_out));
  Transistor transistor_532 (.in(1'b1), .out(sum3), .gate(transistor_389_out));
  Transistor transistor_533 (.in(1'b1), .out(sum3), .gate(transistor_391_out));
  Transistor #(.\type ("n")) transistor_534 (.in(transistor_535_out), .out(sum3), .gate(transistor_389_out));
  Transistor #(.\type ("n")) transistor_535 (.in(1'b0), .out(transistor_535_out), .gate(transistor_391_out));
  Transistor transistor_536 (.in(1'b1), .out(transistor_536_out), .gate(transistor_296_out));
  Transistor transistor_537 (.in(transistor_536_out), .out(transistor_473_out), .gate(transistor_394_out));
  Transistor transistor_538 (.in(1'b1), .out(transistor_538_out), .gate(transistor_473_out));
  Transistor #(.\type ("n")) transistor_539 (.in(1'b0), .out(transistor_473_out), .gate(transistor_394_out));
  Transistor #(.\type ("n")) transistor_540 (.in(1'b0), .out(transistor_538_out), .gate(transistor_473_out));
  Transistor transistor_541 (.in(1'b1), .out(sum4), .gate(transistor_399_out));
  Transistor transistor_542 (.in(1'b1), .out(sum4), .gate(transistor_400_out));
  Transistor #(.\type ("n")) transistor_543 (.in(transistor_544_out), .out(sum4), .gate(transistor_399_out));
  Transistor #(.\type ("n")) transistor_544 (.in(1'b0), .out(transistor_544_out), .gate(transistor_400_out));
  Transistor transistor_545 (.in(1'b1), .out(transistor_545_out), .gate(transistor_306_out));
  Transistor transistor_546 (.in(transistor_545_out), .out(transistor_480_out), .gate(transistor_404_out));
  Transistor transistor_547 (.in(1'b1), .out(transistor_547_out), .gate(transistor_480_out));
  Transistor #(.\type ("n")) transistor_548 (.in(1'b0), .out(transistor_480_out), .gate(transistor_404_out));
  Transistor #(.\type ("n")) transistor_549 (.in(1'b0), .out(transistor_547_out), .gate(transistor_480_out));
  Transistor transistor_550 (.in(1'b1), .out(sum5), .gate(transistor_411_out));
  Transistor transistor_551 (.in(1'b1), .out(sum5), .gate(transistor_409_out));
  Transistor #(.\type ("n")) transistor_552 (.in(transistor_553_out), .out(sum5), .gate(transistor_409_out));
  Transistor #(.\type ("n")) transistor_553 (.in(1'b0), .out(transistor_553_out), .gate(transistor_411_out));
  Transistor transistor_554 (.in(1'b1), .out(transistor_554_out), .gate(transistor_314_out));
  Transistor transistor_555 (.in(1'b1), .out(transistor_555_out), .gate(transistor_487_out));
  Transistor transistor_556 (.in(transistor_554_out), .out(transistor_487_out), .gate(transistor_415_out));
  Transistor #(.\type ("n")) transistor_557 (.in(1'b0), .out(transistor_555_out), .gate(transistor_487_out));
  Transistor #(.\type ("n")) transistor_558 (.in(1'b0), .out(transistor_487_out), .gate(transistor_415_out));
  Transistor transistor_559 (.in(1'b1), .out(sum6), .gate(transistor_421_out));
  Transistor transistor_560 (.in(1'b1), .out(sum6), .gate(transistor_419_out));
  Transistor #(.\type ("n")) transistor_561 (.in(transistor_562_out), .out(sum6), .gate(transistor_419_out));
  Transistor #(.\type ("n")) transistor_562 (.in(1'b0), .out(transistor_562_out), .gate(transistor_421_out));
  Transistor transistor_563 (.in(1'b1), .out(transistor_563_out), .gate(transistor_323_out));
  Transistor transistor_564 (.in(transistor_563_out), .out(transistor_494_out), .gate(transistor_424_out));
  Transistor transistor_565 (.in(1'b1), .out(transistor_565_out), .gate(transistor_494_out));
  Transistor #(.\type ("n")) transistor_566 (.in(1'b0), .out(transistor_565_out), .gate(transistor_494_out));
  Transistor #(.\type ("n")) transistor_567 (.in(1'b0), .out(transistor_494_out), .gate(transistor_424_out));
  Transistor transistor_568 (.in(1'b1), .out(sum7), .gate(transistor_431_out));
  Transistor transistor_569 (.in(1'b1), .out(sum7), .gate(transistor_429_out));
  Transistor #(.\type ("n")) transistor_570 (.in(transistor_571_out), .out(sum7), .gate(transistor_429_out));
  Transistor #(.\type ("n")) transistor_571 (.in(1'b0), .out(transistor_571_out), .gate(transistor_431_out));
  Transistor transistor_572 (.in(1'b1), .out(transistor_572_out), .gate(transistor_333_out));
  Transistor transistor_573 (.in(transistor_572_out), .out(transistor_501_out), .gate(transistor_435_out));
  Transistor transistor_574 (.in(1'b1), .out(transistor_574_out), .gate(transistor_501_out));
  Transistor #(.\type ("n")) transistor_575 (.in(1'b0), .out(transistor_574_out), .gate(transistor_501_out));
  Transistor #(.\type ("n")) transistor_576 (.in(1'b0), .out(transistor_501_out), .gate(transistor_435_out));
endmodule
module TEMP (
  input  a0,
  input  a1,
  input  a2,
  input  a3,
  input  a4,
  input  a5,
  input  a6,
  input  a7,
  input  a0_2,
  input  a1_2,
  input  a2_2,
  input  a3_2,
  input  a4_2,
  input  a5_2,
  input  a6_2,
  input  a7_2,
  input  cin,
  input  sub,
  input  a0_3,
  input  b0,
  input  a1_3,
  input  b1,
  input  a2_3,
  input  b2,
  input  a3_3,
  input  b3,
  input  a4_3,
  input  b4,
  input  a5_3,
  input  b5,
  input  a6_3,
  input  b6,
  input  a7_3,
  input  b7,
  output out_35,
  output out_36,
  output out_37,
  output out_38,
  output out_39,
  output out_40,
  output out_41,
  output out_42,
  output out_43,
  output out_44,
  output out_45,
  output out_46,
  output out_47,
  output out_48,
  output out_49,
  output out_50,
  output sum0,
  output sum1,
  output sum2,
  output sum3,
  output sum4,
  output sum5,
  output sum6,
  output sum7,
  output cout,
  output overflow,
  output out_61,
  output out_62,
  output out_63,
  output out_64,
  output out_65,
  output out_66,
  output out_67,
  output out_68,
  output out_69,
  output out_70,
  output out_71,
  output out_72,
  output out_73,
  output out_74,
  output out_75,
  output out_76
);

  wire transistor_1_out, transistor_3_out, transistor_5_out, transistor_7_out, transistor_9_out,
       transistor_11_out, transistor_13_out, transistor_16_out, transistor_17_out, transistor_20_out,
       transistor_21_out, transistor_24_out, transistor_25_out, transistor_28_out, transistor_29_out,
       transistor_32_out, transistor_33_out, transistor_36_out, transistor_37_out, transistor_40_out,
       transistor_41_out, transistor_44_out, transistor_45_out, transistor_48_out, transistor_49_out,
       transistor_52_out, transistor_53_out, transistor_54_out, transistor_56_out, transistor_59_out,
       transistor_60_out, transistor_63_out, transistor_64_out, transistor_67_out, transistor_68_out,
       transistor_71_out, transistor_72_out, transistor_75_out, transistor_76_out, transistor_79_out,
       transistor_80_out, transistor_83_out, transistor_84_out, transistor_87_out, transistor_88_out,
       transistor_91_out, transistor_92_out, transistor_95_out, transistor_96_out, transistor_99_out,
       transistor_100_out, transistor_103_out, transistor_104_out, transistor_107_out, transistor_108_out,
       transistor_111_out, transistor_112_out, transistor_115_out, transistor_116_out, transistor_119_out,
       transistor_120_out, transistor_123_out, transistor_124_out, transistor_127_out, transistor_128_out,
       transistor_129_out, transistor_131_out, transistor_132_out, transistor_134_out, transistor_135_out,
       transistor_136_out, transistor_137_out, transistor_138_out, transistor_139_out, transistor_140_out,
       transistor_141_out, transistor_142_out, transistor_145_out, transistor_149_out, transistor_151_out,
       transistor_155_out, transistor_158_out, transistor_161_out, transistor_164_out, transistor_167_out,
       transistor_170_out, transistor_173_out, transistor_176_out, transistor_179_out, transistor_182_out,
       transistor_183_out, transistor_185_out, transistor_188_out, transistor_189_out, transistor_192_out,
       transistor_193_out, transistor_196_out, transistor_197_out, transistor_200_out, transistor_201_out,
       transistor_204_out, transistor_205_out, transistor_208_out, transistor_209_out, transistor_212_out,
       transistor_213_out, transistor_216_out, transistor_217_out, transistor_219_out, transistor_221_out,
       transistor_222_out, transistor_223_out, transistor_224_out, transistor_225_out, transistor_226_out,
       transistor_227_out, transistor_228_out, transistor_229_out, transistor_230_out, transistor_231_out,
       transistor_232_out, transistor_233_out, transistor_234_out, transistor_235_out, transistor_236_out,
       transistor_237_out, transistor_238_out, transistor_239_out, transistor_240_out, transistor_241_out,
       transistor_242_out, transistor_243_out, transistor_244_out, transistor_245_out, transistor_247_out,
       transistor_251_out, transistor_252_out, transistor_255_out, transistor_258_out, transistor_261_out,
       transistor_262_out, transistor_265_out, transistor_268_out, transistor_271_out, transistor_272_out,
       transistor_275_out, transistor_278_out, transistor_281_out, transistor_282_out, transistor_285_out,
       transistor_288_out, transistor_291_out, transistor_292_out, transistor_295_out, transistor_298_out,
       transistor_301_out, transistor_302_out, transistor_305_out, transistor_308_out, transistor_311_out,
       transistor_312_out, transistor_315_out, transistor_318_out, transistor_321_out, transistor_322_out,
       transistor_325_out, transistor_328_out, transistor_331_out, transistor_332_out, transistor_336_out,
       transistor_337_out, transistor_341_out, transistor_342_out, transistor_346_out, transistor_347_out,
       transistor_351_out, transistor_352_out, transistor_356_out, transistor_357_out, transistor_361_out,
       transistor_362_out, transistor_366_out, transistor_367_out, transistor_369_out, transistor_370_out,
       transistor_373_out, transistor_374_out, transistor_377_out, transistor_378_out, transistor_381_out,
       transistor_382_out, transistor_385_out, transistor_386_out, transistor_389_out, transistor_390_out,
       transistor_393_out, transistor_394_out, transistor_397_out, transistor_398_out, transistor_401_out,
       transistor_402_out, transistor_405_out, transistor_406_out, transistor_409_out, transistor_410_out,
       transistor_413_out, transistor_414_out, transistor_417_out, transistor_418_out, transistor_421_out,
       transistor_422_out, transistor_425_out, transistor_426_out, transistor_429_out, transistor_430_out,
       transistor_433_out, transistor_434_out, transistor_436_out, transistor_438_out, transistor_439_out,
       transistor_442_out, transistor_443_out, transistor_446_out, transistor_447_out, transistor_449_out,
       transistor_450_out, transistor_453_out, transistor_454_out, transistor_457_out, transistor_458_out,
       transistor_460_out, transistor_461_out, transistor_464_out, transistor_465_out, transistor_468_out,
       transistor_469_out, transistor_471_out, transistor_472_out, transistor_475_out, transistor_476_out,
       transistor_479_out, transistor_480_out, transistor_482_out, transistor_483_out, transistor_486_out,
       transistor_487_out, transistor_490_out, transistor_491_out, transistor_493_out, transistor_494_out,
       transistor_497_out, transistor_498_out, transistor_501_out, transistor_502_out, transistor_504_out,
       transistor_505_out, transistor_508_out, transistor_509_out, transistor_512_out, transistor_513_out,
       transistor_515_out, transistor_516_out, transistor_519_out, transistor_520_out, transistor_523_out,
       transistor_524_out, transistor_526_out, transistor_529_out, transistor_533_out, transistor_535_out,
       transistor_539_out, transistor_543_out, transistor_547_out, transistor_551_out, transistor_555_out,
       transistor_559_out, transistor_563_out, transistor_568_out, transistor_571_out, transistor_572_out,
       transistor_576_out, transistor_577_out, transistor_581_out, transistor_582_out, transistor_586_out,
       transistor_587_out, transistor_591_out, transistor_592_out, transistor_596_out, transistor_597_out,
       transistor_601_out, transistor_602_out, transistor_606_out, transistor_607_out, undriven, undriven_2,
       undriven_3, undriven_4, undriven_5, undriven_6, undriven_7, undriven_8, undriven_9;

  Transistor #(.gate("br")) transistor_1 (.in(undriven), .out(transistor_1_out), .gate(transistor_3_out));
  Transistor #(.\type ("n")) transistor_2 (.in(undriven), .out(transistor_1_out), .gate(undriven_8));
  Transistor transistor_3 (.in(1'b1), .out(transistor_3_out), .gate(undriven_8));
  Transistor #(.\type ("n")) transistor_4 (.in(1'b0), .out(transistor_3_out), .gate(undriven_8));
  Transistor #(.\type ("n")) transistor_5 (.in(undriven_2), .out(transistor_5_out), .gate(undriven_8));
  Transistor #(.gate("br")) transistor_6 (.in(undriven_2), .out(transistor_5_out), .gate(transistor_7_out));
  Transistor transistor_7 (.in(1'b1), .out(transistor_7_out), .gate(undriven_8));
  Transistor #(.\type ("n")) transistor_8 (.in(1'b0), .out(transistor_7_out), .gate(undriven_8));
  Transistor #(.\type ("n")) transistor_9 (.in(undriven_3), .out(transistor_9_out), .gate(undriven_8));
  Transistor #(.gate("br")) transistor_10 (.in(undriven_3), .out(transistor_9_out), .gate(transistor_11_out));
  Transistor transistor_11 (.in(1'b1), .out(transistor_11_out), .gate(undriven_8));
  Transistor #(.\type ("n")) transistor_12 (.in(1'b0), .out(transistor_11_out), .gate(undriven_8));
  Transistor transistor_13 (.in(1'b1), .out(transistor_13_out), .gate(cin));
  Transistor transistor_14 (.in(1'b1), .out(transistor_13_out), .gate(sub));
  Transistor #(.\type ("n")) transistor_15 (.in(transistor_16_out), .out(transistor_13_out), .gate(sub));
  Transistor #(.\type ("n")) transistor_16 (.in(1'b0), .out(transistor_16_out), .gate(cin));
  Transistor transistor_17 (.in(1'b1), .out(transistor_17_out), .gate(b0));
  Transistor transistor_18 (.in(1'b1), .out(transistor_17_out), .gate(sub));
  Transistor #(.\type ("n")) transistor_19 (.in(transistor_20_out), .out(transistor_17_out), .gate(sub));
  Transistor #(.\type ("n")) transistor_20 (.in(1'b0), .out(transistor_20_out), .gate(b0));
  Transistor transistor_21 (.in(1'b1), .out(transistor_21_out), .gate(b1));
  Transistor transistor_22 (.in(1'b1), .out(transistor_21_out), .gate(sub));
  Transistor #(.\type ("n")) transistor_23 (.in(transistor_24_out), .out(transistor_21_out), .gate(sub));
  Transistor #(.\type ("n")) transistor_24 (.in(1'b0), .out(transistor_24_out), .gate(b1));
  Transistor transistor_25 (.in(1'b1), .out(transistor_25_out), .gate(b2));
  Transistor transistor_26 (.in(1'b1), .out(transistor_25_out), .gate(sub));
  Transistor #(.\type ("n")) transistor_27 (.in(transistor_28_out), .out(transistor_25_out), .gate(sub));
  Transistor #(.\type ("n")) transistor_28 (.in(1'b0), .out(transistor_28_out), .gate(b2));
  Transistor transistor_29 (.in(1'b1), .out(transistor_29_out), .gate(sub));
  Transistor transistor_30 (.in(1'b1), .out(transistor_29_out), .gate(b3));
  Transistor #(.\type ("n")) transistor_31 (.in(transistor_32_out), .out(transistor_29_out), .gate(sub));
  Transistor #(.\type ("n")) transistor_32 (.in(1'b0), .out(transistor_32_out), .gate(b3));
  Transistor transistor_33 (.in(1'b1), .out(transistor_33_out), .gate(b4));
  Transistor transistor_34 (.in(1'b1), .out(transistor_33_out), .gate(sub));
  Transistor #(.\type ("n")) transistor_35 (.in(transistor_36_out), .out(transistor_33_out), .gate(sub));
  Transistor #(.\type ("n")) transistor_36 (.in(1'b0), .out(transistor_36_out), .gate(b4));
  Transistor transistor_37 (.in(1'b1), .out(transistor_37_out), .gate(b5));
  Transistor transistor_38 (.in(1'b1), .out(transistor_37_out), .gate(sub));
  Transistor #(.\type ("n")) transistor_39 (.in(transistor_40_out), .out(transistor_37_out), .gate(sub));
  Transistor #(.\type ("n")) transistor_40 (.in(1'b0), .out(transistor_40_out), .gate(b5));
  Transistor transistor_41 (.in(1'b1), .out(transistor_41_out), .gate(sub));
  Transistor transistor_42 (.in(1'b1), .out(transistor_41_out), .gate(b6));
  Transistor #(.\type ("n")) transistor_43 (.in(transistor_44_out), .out(transistor_41_out), .gate(sub));
  Transistor #(.\type ("n")) transistor_44 (.in(1'b0), .out(transistor_44_out), .gate(b6));
  Transistor transistor_45 (.in(1'b1), .out(transistor_45_out), .gate(b7));
  Transistor transistor_46 (.in(1'b1), .out(transistor_45_out), .gate(sub));
  Transistor #(.\type ("n")) transistor_47 (.in(transistor_48_out), .out(transistor_45_out), .gate(sub));
  Transistor #(.\type ("n")) transistor_48 (.in(1'b0), .out(transistor_48_out), .gate(b7));
  Transistor transistor_49 (.in(1'b1), .out(transistor_49_out), .gate(transistor_602_out));
  Transistor transistor_50 (.in(1'b1), .out(transistor_49_out), .gate(transistor_607_out));
  Transistor #(.\type ("n")) transistor_51 (.in(transistor_52_out), .out(transistor_49_out), .gate(transistor_607_out));
  Transistor #(.\type ("n")) transistor_52 (.in(1'b0), .out(transistor_52_out), .gate(transistor_602_out));
  Transistor #(.\type ("n")) transistor_53 (.in(undriven_9), .out(transistor_53_out), .gate(undriven_8));
  Transistor transistor_54 (.in(1'b1), .out(transistor_54_out), .gate(undriven_8));
  Transistor #(.\type ("n")) transistor_55 (.in(1'b0), .out(transistor_54_out), .gate(undriven_8));
  Transistor transistor_56 (.in(1'b1), .out(transistor_56_out), .gate(transistor_13_out));
  Transistor transistor_57 (.in(1'b1), .out(transistor_56_out), .gate(sub));
  Transistor #(.\type ("n")) transistor_58 (.in(transistor_59_out), .out(transistor_56_out), .gate(sub));
  Transistor #(.\type ("n")) transistor_59 (.in(1'b0), .out(transistor_59_out), .gate(transistor_13_out));
  Transistor transistor_60 (.in(1'b1), .out(transistor_60_out), .gate(transistor_13_out));
  Transistor transistor_61 (.in(1'b1), .out(transistor_60_out), .gate(cin));
  Transistor #(.\type ("n")) transistor_62 (.in(transistor_63_out), .out(transistor_60_out), .gate(transistor_13_out));
  Transistor #(.\type ("n")) transistor_63 (.in(1'b0), .out(transistor_63_out), .gate(cin));
  Transistor transistor_64 (.in(1'b1), .out(transistor_64_out), .gate(transistor_17_out));
  Transistor transistor_65 (.in(1'b1), .out(transistor_64_out), .gate(sub));
  Transistor #(.\type ("n")) transistor_66 (.in(transistor_67_out), .out(transistor_64_out), .gate(sub));
  Transistor #(.\type ("n")) transistor_67 (.in(1'b0), .out(transistor_67_out), .gate(transistor_17_out));
  Transistor transistor_68 (.in(1'b1), .out(transistor_68_out), .gate(transistor_17_out));
  Transistor transistor_69 (.in(1'b1), .out(transistor_68_out), .gate(b0));
  Transistor #(.\type ("n")) transistor_70 (.in(transistor_71_out), .out(transistor_68_out), .gate(transistor_17_out));
  Transistor #(.\type ("n")) transistor_71 (.in(1'b0), .out(transistor_71_out), .gate(b0));
  Transistor transistor_72 (.in(1'b1), .out(transistor_72_out), .gate(transistor_21_out));
  Transistor transistor_73 (.in(1'b1), .out(transistor_72_out), .gate(sub));
  Transistor #(.\type ("n")) transistor_74 (.in(transistor_75_out), .out(transistor_72_out), .gate(sub));
  Transistor #(.\type ("n")) transistor_75 (.in(1'b0), .out(transistor_75_out), .gate(transistor_21_out));
  Transistor transistor_76 (.in(1'b1), .out(transistor_76_out), .gate(b1));
  Transistor transistor_77 (.in(1'b1), .out(transistor_76_out), .gate(transistor_21_out));
  Transistor #(.\type ("n")) transistor_78 (.in(transistor_79_out), .out(transistor_76_out), .gate(transistor_21_out));
  Transistor #(.\type ("n")) transistor_79 (.in(1'b0), .out(transistor_79_out), .gate(b1));
  Transistor transistor_80 (.in(1'b1), .out(transistor_80_out), .gate(transistor_25_out));
  Transistor transistor_81 (.in(1'b1), .out(transistor_80_out), .gate(sub));
  Transistor #(.\type ("n")) transistor_82 (.in(transistor_83_out), .out(transistor_80_out), .gate(sub));
  Transistor #(.\type ("n")) transistor_83 (.in(1'b0), .out(transistor_83_out), .gate(transistor_25_out));
  Transistor transistor_84 (.in(1'b1), .out(transistor_84_out), .gate(transistor_25_out));
  Transistor transistor_85 (.in(1'b1), .out(transistor_84_out), .gate(b2));
  Transistor #(.\type ("n")) transistor_86 (.in(transistor_87_out), .out(transistor_84_out), .gate(transistor_25_out));
  Transistor #(.\type ("n")) transistor_87 (.in(1'b0), .out(transistor_87_out), .gate(b2));
  Transistor transistor_88 (.in(1'b1), .out(transistor_88_out), .gate(sub));
  Transistor transistor_89 (.in(1'b1), .out(transistor_88_out), .gate(transistor_29_out));
  Transistor #(.\type ("n")) transistor_90 (.in(transistor_91_out), .out(transistor_88_out), .gate(sub));
  Transistor #(.\type ("n")) transistor_91 (.in(1'b0), .out(transistor_91_out), .gate(transistor_29_out));
  Transistor transistor_92 (.in(1'b1), .out(transistor_92_out), .gate(transistor_29_out));
  Transistor transistor_93 (.in(1'b1), .out(transistor_92_out), .gate(b3));
  Transistor #(.\type ("n")) transistor_94 (.in(transistor_95_out), .out(transistor_92_out), .gate(transistor_29_out));
  Transistor #(.\type ("n")) transistor_95 (.in(1'b0), .out(transistor_95_out), .gate(b3));
  Transistor transistor_96 (.in(1'b1), .out(transistor_96_out), .gate(sub));
  Transistor transistor_97 (.in(1'b1), .out(transistor_96_out), .gate(transistor_33_out));
  Transistor #(.\type ("n")) transistor_98 (.in(transistor_99_out), .out(transistor_96_out), .gate(sub));
  Transistor #(.\type ("n")) transistor_99 (.in(1'b0), .out(transistor_99_out), .gate(transistor_33_out));
  Transistor transistor_100 (.in(1'b1), .out(transistor_100_out), .gate(transistor_33_out));
  Transistor transistor_101 (.in(1'b1), .out(transistor_100_out), .gate(b4));
  Transistor #(.\type ("n")) transistor_102 (
    .in(transistor_103_out), .out(transistor_100_out), .gate(transistor_33_out));
  Transistor #(.\type ("n")) transistor_103 (.in(1'b0), .out(transistor_103_out), .gate(b4));
  Transistor transistor_104 (.in(1'b1), .out(transistor_104_out), .gate(transistor_37_out));
  Transistor transistor_105 (.in(1'b1), .out(transistor_104_out), .gate(sub));
  Transistor #(.\type ("n")) transistor_106 (.in(transistor_107_out), .out(transistor_104_out), .gate(sub));
  Transistor #(.\type ("n")) transistor_107 (.in(1'b0), .out(transistor_107_out), .gate(transistor_37_out));
  Transistor transistor_108 (.in(1'b1), .out(transistor_108_out), .gate(b5));
  Transistor transistor_109 (.in(1'b1), .out(transistor_108_out), .gate(transistor_37_out));
  Transistor #(.\type ("n")) transistor_110 (
    .in(transistor_111_out), .out(transistor_108_out), .gate(transistor_37_out));
  Transistor #(.\type ("n")) transistor_111 (.in(1'b0), .out(transistor_111_out), .gate(b5));
  Transistor transistor_112 (.in(1'b1), .out(transistor_112_out), .gate(sub));
  Transistor transistor_113 (.in(1'b1), .out(transistor_112_out), .gate(transistor_41_out));
  Transistor #(.\type ("n")) transistor_114 (.in(transistor_115_out), .out(transistor_112_out), .gate(sub));
  Transistor #(.\type ("n")) transistor_115 (.in(1'b0), .out(transistor_115_out), .gate(transistor_41_out));
  Transistor transistor_116 (.in(1'b1), .out(transistor_116_out), .gate(transistor_41_out));
  Transistor transistor_117 (.in(1'b1), .out(transistor_116_out), .gate(b6));
  Transistor #(.\type ("n")) transistor_118 (
    .in(transistor_119_out), .out(transistor_116_out), .gate(transistor_41_out));
  Transistor #(.\type ("n")) transistor_119 (.in(1'b0), .out(transistor_119_out), .gate(b6));
  Transistor transistor_120 (.in(1'b1), .out(transistor_120_out), .gate(transistor_45_out));
  Transistor transistor_121 (.in(1'b1), .out(transistor_120_out), .gate(sub));
  Transistor #(.\type ("n")) transistor_122 (.in(transistor_123_out), .out(transistor_120_out), .gate(sub));
  Transistor #(.\type ("n")) transistor_123 (.in(1'b0), .out(transistor_123_out), .gate(transistor_45_out));
  Transistor transistor_124 (.in(1'b1), .out(transistor_124_out), .gate(b7));
  Transistor transistor_125 (.in(1'b1), .out(transistor_124_out), .gate(transistor_45_out));
  Transistor #(.\type ("n")) transistor_126 (
    .in(transistor_127_out), .out(transistor_124_out), .gate(transistor_45_out));
  Transistor #(.\type ("n")) transistor_127 (.in(1'b0), .out(transistor_127_out), .gate(b7));
  Transistor transistor_128 (.in(1'b1), .out(transistor_128_out), .gate(transistor_607_out));
  Transistor transistor_129 (.in(1'b1), .out(transistor_129_out), .gate(transistor_49_out));
  Transistor #(.gate("br")) transistor_130 (.in(undriven_9), .out(transistor_53_out), .gate(transistor_54_out));
  Transistor #(.\type ("n")) transistor_131 (.in(undriven_4), .out(transistor_131_out), .gate(undriven_8));
  Transistor transistor_132 (.in(1'b1), .out(transistor_132_out), .gate(undriven_8));
  Transistor #(.\type ("n")) transistor_133 (.in(1'b0), .out(transistor_132_out), .gate(undriven_8));
  Transistor transistor_134 (.in(1'b1), .out(transistor_134_out), .gate(transistor_56_out));
  Transistor transistor_135 (.in(1'b1), .out(transistor_135_out), .gate(transistor_64_out));
  Transistor transistor_136 (.in(1'b1), .out(transistor_136_out), .gate(transistor_72_out));
  Transistor transistor_137 (.in(1'b1), .out(transistor_137_out), .gate(transistor_80_out));
  Transistor transistor_138 (.in(1'b1), .out(transistor_138_out), .gate(transistor_88_out));
  Transistor transistor_139 (.in(1'b1), .out(transistor_139_out), .gate(transistor_96_out));
  Transistor transistor_140 (.in(1'b1), .out(transistor_140_out), .gate(transistor_104_out));
  Transistor transistor_141 (.in(1'b1), .out(transistor_141_out), .gate(transistor_112_out));
  Transistor transistor_142 (.in(1'b1), .out(transistor_142_out), .gate(transistor_120_out));
  Transistor transistor_143 (.in(1'b1), .out(transistor_128_out), .gate(transistor_49_out));
  Transistor #(.\type ("n")) transistor_144 (
    .in(transistor_145_out), .out(transistor_128_out), .gate(transistor_607_out));
  Transistor #(.\type ("n")) transistor_145 (.in(1'b0), .out(transistor_145_out), .gate(transistor_49_out));
  Transistor transistor_146 (.in(1'b1), .out(overflow), .gate(transistor_128_out));
  Transistor transistor_147 (.in(1'b1), .out(transistor_129_out), .gate(transistor_602_out));
  Transistor #(.\type ("n")) transistor_148 (
    .in(transistor_149_out), .out(transistor_129_out), .gate(transistor_49_out));
  Transistor #(.\type ("n")) transistor_149 (.in(1'b0), .out(transistor_149_out), .gate(transistor_602_out));
  Transistor #(.gate("br")) transistor_150 (.in(undriven_4), .out(transistor_131_out), .gate(transistor_132_out));
  Transistor transistor_151 (.in(1'b1), .out(transistor_151_out), .gate(undriven_8));
  Transistor #(.\type ("n")) transistor_152 (.in(1'b0), .out(transistor_151_out), .gate(undriven_8));
  Transistor transistor_153 (.in(1'b1), .out(transistor_134_out), .gate(transistor_60_out));
  Transistor #(.\type ("n")) transistor_154 (
    .in(transistor_155_out), .out(transistor_134_out), .gate(transistor_56_out));
  Transistor #(.\type ("n")) transistor_155 (.in(1'b0), .out(transistor_155_out), .gate(transistor_60_out));
  Transistor transistor_156 (.in(1'b1), .out(transistor_135_out), .gate(transistor_68_out));
  Transistor #(.\type ("n")) transistor_157 (
    .in(transistor_158_out), .out(transistor_135_out), .gate(transistor_64_out));
  Transistor #(.\type ("n")) transistor_158 (.in(1'b0), .out(transistor_158_out), .gate(transistor_68_out));
  Transistor transistor_159 (.in(1'b1), .out(transistor_136_out), .gate(transistor_76_out));
  Transistor #(.\type ("n")) transistor_160 (
    .in(transistor_161_out), .out(transistor_136_out), .gate(transistor_72_out));
  Transistor #(.\type ("n")) transistor_161 (.in(1'b0), .out(transistor_161_out), .gate(transistor_76_out));
  Transistor transistor_162 (.in(1'b1), .out(transistor_137_out), .gate(transistor_84_out));
  Transistor #(.\type ("n")) transistor_163 (
    .in(transistor_164_out), .out(transistor_137_out), .gate(transistor_80_out));
  Transistor #(.\type ("n")) transistor_164 (.in(1'b0), .out(transistor_164_out), .gate(transistor_84_out));
  Transistor transistor_165 (.in(1'b1), .out(transistor_138_out), .gate(transistor_92_out));
  Transistor #(.\type ("n")) transistor_166 (
    .in(transistor_167_out), .out(transistor_138_out), .gate(transistor_88_out));
  Transistor #(.\type ("n")) transistor_167 (.in(1'b0), .out(transistor_167_out), .gate(transistor_92_out));
  Transistor transistor_168 (.in(1'b1), .out(transistor_139_out), .gate(transistor_100_out));
  Transistor #(.\type ("n")) transistor_169 (
    .in(transistor_170_out), .out(transistor_139_out), .gate(transistor_96_out));
  Transistor #(.\type ("n")) transistor_170 (.in(1'b0), .out(transistor_170_out), .gate(transistor_100_out));
  Transistor transistor_171 (.in(1'b1), .out(transistor_140_out), .gate(transistor_108_out));
  Transistor #(.\type ("n")) transistor_172 (
    .in(transistor_173_out), .out(transistor_140_out), .gate(transistor_104_out));
  Transistor #(.\type ("n")) transistor_173 (.in(1'b0), .out(transistor_173_out), .gate(transistor_108_out));
  Transistor transistor_174 (.in(1'b1), .out(transistor_141_out), .gate(transistor_116_out));
  Transistor #(.\type ("n")) transistor_175 (
    .in(transistor_176_out), .out(transistor_141_out), .gate(transistor_112_out));
  Transistor #(.\type ("n")) transistor_176 (.in(1'b0), .out(transistor_176_out), .gate(transistor_116_out));
  Transistor transistor_177 (.in(1'b1), .out(transistor_142_out), .gate(transistor_124_out));
  Transistor #(.\type ("n")) transistor_178 (
    .in(transistor_179_out), .out(transistor_142_out), .gate(transistor_120_out));
  Transistor #(.\type ("n")) transistor_179 (.in(1'b0), .out(transistor_179_out), .gate(transistor_124_out));
  Transistor transistor_180 (.in(1'b1), .out(overflow), .gate(transistor_129_out));
  Transistor #(.\type ("n")) transistor_181 (.in(transistor_182_out), .out(overflow), .gate(transistor_128_out));
  Transistor #(.\type ("n")) transistor_182 (.in(1'b0), .out(transistor_182_out), .gate(transistor_129_out));
  Transistor #(.\type ("n")) transistor_183 (.in(undriven_5), .out(transistor_183_out), .gate(undriven_8));
  Transistor #(.gate("br")) transistor_184 (.in(undriven_5), .out(transistor_183_out), .gate(transistor_151_out));
  Transistor transistor_185 (.in(1'b1), .out(transistor_185_out), .gate(transistor_135_out));
  Transistor transistor_186 (.in(1'b1), .out(transistor_185_out), .gate(a0_3));
  Transistor #(.\type ("n")) transistor_187 (.in(transistor_188_out), .out(transistor_185_out), .gate(a0_3));
  Transistor #(.\type ("n")) transistor_188 (.in(1'b0), .out(transistor_188_out), .gate(transistor_135_out));
  Transistor transistor_189 (.in(1'b1), .out(transistor_189_out), .gate(a1_3));
  Transistor transistor_190 (.in(1'b1), .out(transistor_189_out), .gate(transistor_136_out));
  Transistor #(.\type ("n")) transistor_191 (.in(transistor_192_out), .out(transistor_189_out), .gate(a1_3));
  Transistor #(.\type ("n")) transistor_192 (.in(1'b0), .out(transistor_192_out), .gate(transistor_136_out));
  Transistor transistor_193 (.in(1'b1), .out(transistor_193_out), .gate(transistor_137_out));
  Transistor transistor_194 (.in(1'b1), .out(transistor_193_out), .gate(a2_3));
  Transistor #(.\type ("n")) transistor_195 (.in(transistor_196_out), .out(transistor_193_out), .gate(a2_3));
  Transistor #(.\type ("n")) transistor_196 (.in(1'b0), .out(transistor_196_out), .gate(transistor_137_out));
  Transistor transistor_197 (.in(1'b1), .out(transistor_197_out), .gate(a3_3));
  Transistor transistor_198 (.in(1'b1), .out(transistor_197_out), .gate(transistor_138_out));
  Transistor #(.\type ("n")) transistor_199 (.in(transistor_200_out), .out(transistor_197_out), .gate(a3_3));
  Transistor #(.\type ("n")) transistor_200 (.in(1'b0), .out(transistor_200_out), .gate(transistor_138_out));
  Transistor transistor_201 (.in(1'b1), .out(transistor_201_out), .gate(a4_3));
  Transistor transistor_202 (.in(1'b1), .out(transistor_201_out), .gate(transistor_139_out));
  Transistor #(.\type ("n")) transistor_203 (.in(transistor_204_out), .out(transistor_201_out), .gate(a4_3));
  Transistor #(.\type ("n")) transistor_204 (.in(1'b0), .out(transistor_204_out), .gate(transistor_139_out));
  Transistor transistor_205 (.in(1'b1), .out(transistor_205_out), .gate(transistor_140_out));
  Transistor transistor_206 (.in(1'b1), .out(transistor_205_out), .gate(a5_3));
  Transistor #(.\type ("n")) transistor_207 (.in(transistor_208_out), .out(transistor_205_out), .gate(a5_3));
  Transistor #(.\type ("n")) transistor_208 (.in(1'b0), .out(transistor_208_out), .gate(transistor_140_out));
  Transistor transistor_209 (.in(1'b1), .out(transistor_209_out), .gate(transistor_141_out));
  Transistor transistor_210 (.in(1'b1), .out(transistor_209_out), .gate(a6_3));
  Transistor #(.\type ("n")) transistor_211 (.in(transistor_212_out), .out(transistor_209_out), .gate(a6_3));
  Transistor #(.\type ("n")) transistor_212 (.in(1'b0), .out(transistor_212_out), .gate(transistor_141_out));
  Transistor transistor_213 (.in(1'b1), .out(transistor_213_out), .gate(transistor_142_out));
  Transistor transistor_214 (.in(1'b1), .out(transistor_213_out), .gate(a7_3));
  Transistor #(.\type ("n")) transistor_215 (.in(transistor_216_out), .out(transistor_213_out), .gate(a7_3));
  Transistor #(.\type ("n")) transistor_216 (.in(1'b0), .out(transistor_216_out), .gate(transistor_142_out));
  Transistor #(.gate("br")) transistor_217 (.in(undriven_6), .out(transistor_217_out), .gate(transistor_219_out));
  Transistor #(.\type ("n")) transistor_218 (.in(undriven_6), .out(transistor_217_out), .gate(undriven_8));
  Transistor transistor_219 (.in(1'b1), .out(transistor_219_out), .gate(undriven_8));
  Transistor #(.\type ("n")) transistor_220 (.in(1'b0), .out(transistor_219_out), .gate(undriven_8));
  Transistor transistor_221 (.in(1'b1), .out(transistor_221_out), .gate(a0_3));
  Transistor transistor_222 (.in(1'b1), .out(transistor_222_out), .gate(transistor_185_out));
  Transistor transistor_223 (.in(1'b1), .out(transistor_223_out), .gate(transistor_252_out));
  Transistor transistor_224 (.in(1'b1), .out(transistor_224_out), .gate(a1_3));
  Transistor transistor_225 (.in(1'b1), .out(transistor_225_out), .gate(transistor_189_out));
  Transistor transistor_226 (.in(1'b1), .out(transistor_226_out), .gate(transistor_262_out));
  Transistor transistor_227 (.in(1'b1), .out(transistor_227_out), .gate(a2_3));
  Transistor transistor_228 (.in(1'b1), .out(transistor_228_out), .gate(transistor_193_out));
  Transistor transistor_229 (.in(1'b1), .out(transistor_229_out), .gate(transistor_272_out));
  Transistor transistor_230 (.in(1'b1), .out(transistor_230_out), .gate(a3_3));
  Transistor transistor_231 (.in(1'b1), .out(transistor_231_out), .gate(transistor_197_out));
  Transistor transistor_232 (.in(1'b1), .out(transistor_232_out), .gate(transistor_282_out));
  Transistor transistor_233 (.in(1'b1), .out(transistor_233_out), .gate(a4_3));
  Transistor transistor_234 (.in(1'b1), .out(transistor_234_out), .gate(transistor_201_out));
  Transistor transistor_235 (.in(1'b1), .out(transistor_235_out), .gate(transistor_292_out));
  Transistor transistor_236 (.in(1'b1), .out(transistor_236_out), .gate(a5_3));
  Transistor transistor_237 (.in(1'b1), .out(transistor_237_out), .gate(transistor_205_out));
  Transistor transistor_238 (.in(1'b1), .out(transistor_238_out), .gate(transistor_302_out));
  Transistor transistor_239 (.in(1'b1), .out(transistor_239_out), .gate(a6_3));
  Transistor transistor_240 (.in(1'b1), .out(transistor_240_out), .gate(transistor_209_out));
  Transistor transistor_241 (.in(1'b1), .out(transistor_241_out), .gate(transistor_312_out));
  Transistor transistor_242 (.in(1'b1), .out(transistor_242_out), .gate(a7_3));
  Transistor transistor_243 (.in(1'b1), .out(transistor_243_out), .gate(transistor_213_out));
  Transistor transistor_244 (.in(1'b1), .out(transistor_244_out), .gate(transistor_322_out));
  Transistor #(.gate("br")) transistor_245 (.in(undriven_7), .out(transistor_245_out), .gate(transistor_247_out));
  Transistor #(.\type ("n")) transistor_246 (.in(undriven_7), .out(transistor_245_out), .gate(undriven_8));
  Transistor transistor_247 (.in(1'b1), .out(transistor_247_out), .gate(undriven_8));
  Transistor #(.\type ("n")) transistor_248 (.in(1'b0), .out(transistor_247_out), .gate(undriven_8));
  Transistor transistor_249 (.in(1'b1), .out(transistor_221_out), .gate(transistor_185_out));
  Transistor #(.\type ("n")) transistor_250 (.in(transistor_251_out), .out(transistor_221_out), .gate(a0_3));
  Transistor #(.\type ("n")) transistor_251 (.in(1'b0), .out(transistor_251_out), .gate(transistor_185_out));
  Transistor transistor_252 (.in(1'b1), .out(transistor_252_out), .gate(transistor_221_out));
  Transistor transistor_253 (.in(1'b1), .out(transistor_222_out), .gate(transistor_135_out));
  Transistor #(.\type ("n")) transistor_254 (
    .in(transistor_255_out), .out(transistor_222_out), .gate(transistor_185_out));
  Transistor #(.\type ("n")) transistor_255 (.in(1'b0), .out(transistor_255_out), .gate(transistor_135_out));
  Transistor transistor_256 (.in(1'b1), .out(transistor_223_out), .gate(transistor_134_out));
  Transistor #(.\type ("n")) transistor_257 (
    .in(transistor_258_out), .out(transistor_223_out), .gate(transistor_252_out));
  Transistor #(.\type ("n")) transistor_258 (.in(1'b0), .out(transistor_258_out), .gate(transistor_134_out));
  Transistor transistor_259 (.in(1'b1), .out(transistor_224_out), .gate(transistor_189_out));
  Transistor #(.\type ("n")) transistor_260 (.in(transistor_261_out), .out(transistor_224_out), .gate(a1_3));
  Transistor #(.\type ("n")) transistor_261 (.in(1'b0), .out(transistor_261_out), .gate(transistor_189_out));
  Transistor transistor_262 (.in(1'b1), .out(transistor_262_out), .gate(transistor_224_out));
  Transistor transistor_263 (.in(1'b1), .out(transistor_225_out), .gate(transistor_136_out));
  Transistor #(.\type ("n")) transistor_264 (
    .in(transistor_265_out), .out(transistor_225_out), .gate(transistor_189_out));
  Transistor #(.\type ("n")) transistor_265 (.in(1'b0), .out(transistor_265_out), .gate(transistor_136_out));
  Transistor transistor_266 (.in(1'b1), .out(transistor_226_out), .gate(transistor_572_out));
  Transistor #(.\type ("n")) transistor_267 (
    .in(transistor_268_out), .out(transistor_226_out), .gate(transistor_262_out));
  Transistor #(.\type ("n")) transistor_268 (.in(1'b0), .out(transistor_268_out), .gate(transistor_572_out));
  Transistor transistor_269 (.in(1'b1), .out(transistor_227_out), .gate(transistor_193_out));
  Transistor #(.\type ("n")) transistor_270 (.in(transistor_271_out), .out(transistor_227_out), .gate(a2_3));
  Transistor #(.\type ("n")) transistor_271 (.in(1'b0), .out(transistor_271_out), .gate(transistor_193_out));
  Transistor transistor_272 (.in(1'b1), .out(transistor_272_out), .gate(transistor_227_out));
  Transistor transistor_273 (.in(1'b1), .out(transistor_228_out), .gate(transistor_137_out));
  Transistor #(.\type ("n")) transistor_274 (
    .in(transistor_275_out), .out(transistor_228_out), .gate(transistor_193_out));
  Transistor #(.\type ("n")) transistor_275 (.in(1'b0), .out(transistor_275_out), .gate(transistor_137_out));
  Transistor transistor_276 (.in(1'b1), .out(transistor_229_out), .gate(transistor_577_out));
  Transistor #(.\type ("n")) transistor_277 (
    .in(transistor_278_out), .out(transistor_229_out), .gate(transistor_272_out));
  Transistor #(.\type ("n")) transistor_278 (.in(1'b0), .out(transistor_278_out), .gate(transistor_577_out));
  Transistor transistor_279 (.in(1'b1), .out(transistor_230_out), .gate(transistor_197_out));
  Transistor #(.\type ("n")) transistor_280 (.in(transistor_281_out), .out(transistor_230_out), .gate(a3_3));
  Transistor #(.\type ("n")) transistor_281 (.in(1'b0), .out(transistor_281_out), .gate(transistor_197_out));
  Transistor transistor_282 (.in(1'b1), .out(transistor_282_out), .gate(transistor_230_out));
  Transistor transistor_283 (.in(1'b1), .out(transistor_231_out), .gate(transistor_138_out));
  Transistor #(.\type ("n")) transistor_284 (
    .in(transistor_285_out), .out(transistor_231_out), .gate(transistor_197_out));
  Transistor #(.\type ("n")) transistor_285 (.in(1'b0), .out(transistor_285_out), .gate(transistor_138_out));
  Transistor transistor_286 (.in(1'b1), .out(transistor_232_out), .gate(transistor_582_out));
  Transistor #(.\type ("n")) transistor_287 (
    .in(transistor_288_out), .out(transistor_232_out), .gate(transistor_282_out));
  Transistor #(.\type ("n")) transistor_288 (.in(1'b0), .out(transistor_288_out), .gate(transistor_582_out));
  Transistor transistor_289 (.in(1'b1), .out(transistor_233_out), .gate(transistor_201_out));
  Transistor #(.\type ("n")) transistor_290 (.in(transistor_291_out), .out(transistor_233_out), .gate(a4_3));
  Transistor #(.\type ("n")) transistor_291 (.in(1'b0), .out(transistor_291_out), .gate(transistor_201_out));
  Transistor transistor_292 (.in(1'b1), .out(transistor_292_out), .gate(transistor_233_out));
  Transistor transistor_293 (.in(1'b1), .out(transistor_234_out), .gate(transistor_139_out));
  Transistor #(.\type ("n")) transistor_294 (
    .in(transistor_295_out), .out(transistor_234_out), .gate(transistor_201_out));
  Transistor #(.\type ("n")) transistor_295 (.in(1'b0), .out(transistor_295_out), .gate(transistor_139_out));
  Transistor transistor_296 (.in(1'b1), .out(transistor_235_out), .gate(transistor_587_out));
  Transistor #(.\type ("n")) transistor_297 (
    .in(transistor_298_out), .out(transistor_235_out), .gate(transistor_292_out));
  Transistor #(.\type ("n")) transistor_298 (.in(1'b0), .out(transistor_298_out), .gate(transistor_587_out));
  Transistor transistor_299 (.in(1'b1), .out(transistor_236_out), .gate(transistor_205_out));
  Transistor #(.\type ("n")) transistor_300 (.in(transistor_301_out), .out(transistor_236_out), .gate(a5_3));
  Transistor #(.\type ("n")) transistor_301 (.in(1'b0), .out(transistor_301_out), .gate(transistor_205_out));
  Transistor transistor_302 (.in(1'b1), .out(transistor_302_out), .gate(transistor_236_out));
  Transistor transistor_303 (.in(1'b1), .out(transistor_237_out), .gate(transistor_140_out));
  Transistor #(.\type ("n")) transistor_304 (
    .in(transistor_305_out), .out(transistor_237_out), .gate(transistor_205_out));
  Transistor #(.\type ("n")) transistor_305 (.in(1'b0), .out(transistor_305_out), .gate(transistor_140_out));
  Transistor transistor_306 (.in(1'b1), .out(transistor_238_out), .gate(transistor_592_out));
  Transistor #(.\type ("n")) transistor_307 (
    .in(transistor_308_out), .out(transistor_238_out), .gate(transistor_302_out));
  Transistor #(.\type ("n")) transistor_308 (.in(1'b0), .out(transistor_308_out), .gate(transistor_592_out));
  Transistor transistor_309 (.in(1'b1), .out(transistor_239_out), .gate(transistor_209_out));
  Transistor #(.\type ("n")) transistor_310 (.in(transistor_311_out), .out(transistor_239_out), .gate(a6_3));
  Transistor #(.\type ("n")) transistor_311 (.in(1'b0), .out(transistor_311_out), .gate(transistor_209_out));
  Transistor transistor_312 (.in(1'b1), .out(transistor_312_out), .gate(transistor_239_out));
  Transistor transistor_313 (.in(1'b1), .out(transistor_240_out), .gate(transistor_141_out));
  Transistor #(.\type ("n")) transistor_314 (
    .in(transistor_315_out), .out(transistor_240_out), .gate(transistor_209_out));
  Transistor #(.\type ("n")) transistor_315 (.in(1'b0), .out(transistor_315_out), .gate(transistor_141_out));
  Transistor transistor_316 (.in(1'b1), .out(transistor_241_out), .gate(transistor_597_out));
  Transistor #(.\type ("n")) transistor_317 (
    .in(transistor_318_out), .out(transistor_241_out), .gate(transistor_312_out));
  Transistor #(.\type ("n")) transistor_318 (.in(1'b0), .out(transistor_318_out), .gate(transistor_597_out));
  Transistor transistor_319 (.in(1'b1), .out(transistor_242_out), .gate(transistor_213_out));
  Transistor #(.\type ("n")) transistor_320 (.in(transistor_321_out), .out(transistor_242_out), .gate(a7_3));
  Transistor #(.\type ("n")) transistor_321 (.in(1'b0), .out(transistor_321_out), .gate(transistor_213_out));
  Transistor transistor_322 (.in(1'b1), .out(transistor_322_out), .gate(transistor_242_out));
  Transistor transistor_323 (.in(1'b1), .out(transistor_243_out), .gate(transistor_142_out));
  Transistor #(.\type ("n")) transistor_324 (
    .in(transistor_325_out), .out(transistor_243_out), .gate(transistor_213_out));
  Transistor #(.\type ("n")) transistor_325 (.in(1'b0), .out(transistor_325_out), .gate(transistor_142_out));
  Transistor transistor_326 (.in(1'b1), .out(transistor_244_out), .gate(transistor_602_out));
  Transistor #(.\type ("n")) transistor_327 (
    .in(transistor_328_out), .out(transistor_244_out), .gate(transistor_322_out));
  Transistor #(.\type ("n")) transistor_328 (.in(1'b0), .out(transistor_328_out), .gate(transistor_602_out));
  Transistor transistor_329 (.in(1'b1), .out(transistor_252_out), .gate(transistor_222_out));
  Transistor #(.\type ("n")) transistor_330 (
    .in(transistor_331_out), .out(transistor_252_out), .gate(transistor_221_out));
  Transistor #(.\type ("n")) transistor_331 (.in(1'b0), .out(transistor_331_out), .gate(transistor_222_out));
  Transistor transistor_332 (.in(1'b1), .out(transistor_332_out), .gate(transistor_223_out));
  Transistor #(.\type ("n")) transistor_333 (.in(1'b0), .out(transistor_332_out), .gate(transistor_223_out));
  Transistor transistor_334 (.in(1'b1), .out(transistor_262_out), .gate(transistor_225_out));
  Transistor #(.\type ("n")) transistor_335 (
    .in(transistor_336_out), .out(transistor_262_out), .gate(transistor_224_out));
  Transistor #(.\type ("n")) transistor_336 (.in(1'b0), .out(transistor_336_out), .gate(transistor_225_out));
  Transistor transistor_337 (.in(1'b1), .out(transistor_337_out), .gate(transistor_226_out));
  Transistor #(.\type ("n")) transistor_338 (.in(1'b0), .out(transistor_337_out), .gate(transistor_226_out));
  Transistor transistor_339 (.in(1'b1), .out(transistor_272_out), .gate(transistor_228_out));
  Transistor #(.\type ("n")) transistor_340 (
    .in(transistor_341_out), .out(transistor_272_out), .gate(transistor_227_out));
  Transistor #(.\type ("n")) transistor_341 (.in(1'b0), .out(transistor_341_out), .gate(transistor_228_out));
  Transistor transistor_342 (.in(1'b1), .out(transistor_342_out), .gate(transistor_229_out));
  Transistor #(.\type ("n")) transistor_343 (.in(1'b0), .out(transistor_342_out), .gate(transistor_229_out));
  Transistor transistor_344 (.in(1'b1), .out(transistor_282_out), .gate(transistor_231_out));
  Transistor #(.\type ("n")) transistor_345 (
    .in(transistor_346_out), .out(transistor_282_out), .gate(transistor_230_out));
  Transistor #(.\type ("n")) transistor_346 (.in(1'b0), .out(transistor_346_out), .gate(transistor_231_out));
  Transistor transistor_347 (.in(1'b1), .out(transistor_347_out), .gate(transistor_232_out));
  Transistor #(.\type ("n")) transistor_348 (.in(1'b0), .out(transistor_347_out), .gate(transistor_232_out));
  Transistor transistor_349 (.in(1'b1), .out(transistor_292_out), .gate(transistor_234_out));
  Transistor #(.\type ("n")) transistor_350 (
    .in(transistor_351_out), .out(transistor_292_out), .gate(transistor_233_out));
  Transistor #(.\type ("n")) transistor_351 (.in(1'b0), .out(transistor_351_out), .gate(transistor_234_out));
  Transistor transistor_352 (.in(1'b1), .out(transistor_352_out), .gate(transistor_235_out));
  Transistor #(.\type ("n")) transistor_353 (.in(1'b0), .out(transistor_352_out), .gate(transistor_235_out));
  Transistor transistor_354 (.in(1'b1), .out(transistor_302_out), .gate(transistor_237_out));
  Transistor #(.\type ("n")) transistor_355 (
    .in(transistor_356_out), .out(transistor_302_out), .gate(transistor_236_out));
  Transistor #(.\type ("n")) transistor_356 (.in(1'b0), .out(transistor_356_out), .gate(transistor_237_out));
  Transistor transistor_357 (.in(1'b1), .out(transistor_357_out), .gate(transistor_238_out));
  Transistor #(.\type ("n")) transistor_358 (.in(1'b0), .out(transistor_357_out), .gate(transistor_238_out));
  Transistor transistor_359 (.in(1'b1), .out(transistor_312_out), .gate(transistor_240_out));
  Transistor #(.\type ("n")) transistor_360 (
    .in(transistor_361_out), .out(transistor_312_out), .gate(transistor_239_out));
  Transistor #(.\type ("n")) transistor_361 (.in(1'b0), .out(transistor_361_out), .gate(transistor_240_out));
  Transistor transistor_362 (.in(1'b1), .out(transistor_362_out), .gate(transistor_241_out));
  Transistor #(.\type ("n")) transistor_363 (.in(1'b0), .out(transistor_362_out), .gate(transistor_241_out));
  Transistor transistor_364 (.in(1'b1), .out(transistor_322_out), .gate(transistor_243_out));
  Transistor #(.\type ("n")) transistor_365 (
    .in(transistor_366_out), .out(transistor_322_out), .gate(transistor_242_out));
  Transistor #(.\type ("n")) transistor_366 (.in(1'b0), .out(transistor_366_out), .gate(transistor_243_out));
  Transistor transistor_367 (.in(1'b1), .out(transistor_367_out), .gate(transistor_244_out));
  Transistor #(.\type ("n")) transistor_368 (.in(1'b0), .out(transistor_367_out), .gate(transistor_244_out));
  Transistor transistor_369 (.in(1'b1), .out(transistor_369_out), .gate(transistor_607_out));
  Transistor transistor_370 (.in(1'b1), .out(transistor_370_out), .gate(transistor_134_out));
  Transistor transistor_371 (.in(1'b1), .out(transistor_370_out), .gate(transistor_252_out));
  Transistor #(.\type ("n")) transistor_372 (
    .in(transistor_373_out), .out(transistor_370_out), .gate(transistor_252_out));
  Transistor #(.\type ("n")) transistor_373 (.in(1'b0), .out(transistor_373_out), .gate(transistor_134_out));
  Transistor transistor_374 (.in(1'b1), .out(transistor_374_out), .gate(transistor_135_out));
  Transistor transistor_375 (.in(1'b1), .out(transistor_374_out), .gate(a0_3));
  Transistor #(.\type ("n")) transistor_376 (.in(transistor_377_out), .out(transistor_374_out), .gate(a0_3));
  Transistor #(.\type ("n")) transistor_377 (.in(1'b0), .out(transistor_377_out), .gate(transistor_135_out));
  Transistor transistor_378 (.in(1'b1), .out(transistor_378_out), .gate(transistor_262_out));
  Transistor transistor_379 (.in(1'b1), .out(transistor_378_out), .gate(transistor_572_out));
  Transistor #(.\type ("n")) transistor_380 (
    .in(transistor_381_out), .out(transistor_378_out), .gate(transistor_262_out));
  Transistor #(.\type ("n")) transistor_381 (.in(1'b0), .out(transistor_381_out), .gate(transistor_572_out));
  Transistor transistor_382 (.in(1'b1), .out(transistor_382_out), .gate(transistor_136_out));
  Transistor transistor_383 (.in(1'b1), .out(transistor_382_out), .gate(a1_3));
  Transistor #(.\type ("n")) transistor_384 (.in(transistor_385_out), .out(transistor_382_out), .gate(a1_3));
  Transistor #(.\type ("n")) transistor_385 (.in(1'b0), .out(transistor_385_out), .gate(transistor_136_out));
  Transistor transistor_386 (.in(1'b1), .out(transistor_386_out), .gate(transistor_577_out));
  Transistor transistor_387 (.in(1'b1), .out(transistor_386_out), .gate(transistor_272_out));
  Transistor #(.\type ("n")) transistor_388 (
    .in(transistor_389_out), .out(transistor_386_out), .gate(transistor_272_out));
  Transistor #(.\type ("n")) transistor_389 (.in(1'b0), .out(transistor_389_out), .gate(transistor_577_out));
  Transistor transistor_390 (.in(1'b1), .out(transistor_390_out), .gate(transistor_137_out));
  Transistor transistor_391 (.in(1'b1), .out(transistor_390_out), .gate(a2_3));
  Transistor #(.\type ("n")) transistor_392 (.in(transistor_393_out), .out(transistor_390_out), .gate(a2_3));
  Transistor #(.\type ("n")) transistor_393 (.in(1'b0), .out(transistor_393_out), .gate(transistor_137_out));
  Transistor transistor_394 (.in(1'b1), .out(transistor_394_out), .gate(transistor_282_out));
  Transistor transistor_395 (.in(1'b1), .out(transistor_394_out), .gate(transistor_582_out));
  Transistor #(.\type ("n")) transistor_396 (
    .in(transistor_397_out), .out(transistor_394_out), .gate(transistor_282_out));
  Transistor #(.\type ("n")) transistor_397 (.in(1'b0), .out(transistor_397_out), .gate(transistor_582_out));
  Transistor transistor_398 (.in(1'b1), .out(transistor_398_out), .gate(transistor_138_out));
  Transistor transistor_399 (.in(1'b1), .out(transistor_398_out), .gate(a3_3));
  Transistor #(.\type ("n")) transistor_400 (.in(transistor_401_out), .out(transistor_398_out), .gate(a3_3));
  Transistor #(.\type ("n")) transistor_401 (.in(1'b0), .out(transistor_401_out), .gate(transistor_138_out));
  Transistor transistor_402 (.in(1'b1), .out(transistor_402_out), .gate(transistor_292_out));
  Transistor transistor_403 (.in(1'b1), .out(transistor_402_out), .gate(transistor_587_out));
  Transistor #(.\type ("n")) transistor_404 (
    .in(transistor_405_out), .out(transistor_402_out), .gate(transistor_292_out));
  Transistor #(.\type ("n")) transistor_405 (.in(1'b0), .out(transistor_405_out), .gate(transistor_587_out));
  Transistor transistor_406 (.in(1'b1), .out(transistor_406_out), .gate(transistor_139_out));
  Transistor transistor_407 (.in(1'b1), .out(transistor_406_out), .gate(a4_3));
  Transistor #(.\type ("n")) transistor_408 (.in(transistor_409_out), .out(transistor_406_out), .gate(a4_3));
  Transistor #(.\type ("n")) transistor_409 (.in(1'b0), .out(transistor_409_out), .gate(transistor_139_out));
  Transistor transistor_410 (.in(1'b1), .out(transistor_410_out), .gate(transistor_592_out));
  Transistor transistor_411 (.in(1'b1), .out(transistor_410_out), .gate(transistor_302_out));
  Transistor #(.\type ("n")) transistor_412 (
    .in(transistor_413_out), .out(transistor_410_out), .gate(transistor_302_out));
  Transistor #(.\type ("n")) transistor_413 (.in(1'b0), .out(transistor_413_out), .gate(transistor_592_out));
  Transistor transistor_414 (.in(1'b1), .out(transistor_414_out), .gate(a5_3));
  Transistor transistor_415 (.in(1'b1), .out(transistor_414_out), .gate(transistor_140_out));
  Transistor #(.\type ("n")) transistor_416 (.in(transistor_417_out), .out(transistor_414_out), .gate(a5_3));
  Transistor #(.\type ("n")) transistor_417 (.in(1'b0), .out(transistor_417_out), .gate(transistor_140_out));
  Transistor transistor_418 (.in(1'b1), .out(transistor_418_out), .gate(transistor_312_out));
  Transistor transistor_419 (.in(1'b1), .out(transistor_418_out), .gate(transistor_597_out));
  Transistor #(.\type ("n")) transistor_420 (
    .in(transistor_421_out), .out(transistor_418_out), .gate(transistor_312_out));
  Transistor #(.\type ("n")) transistor_421 (.in(1'b0), .out(transistor_421_out), .gate(transistor_597_out));
  Transistor transistor_422 (.in(1'b1), .out(transistor_422_out), .gate(transistor_141_out));
  Transistor transistor_423 (.in(1'b1), .out(transistor_422_out), .gate(a6_3));
  Transistor #(.\type ("n")) transistor_424 (.in(transistor_425_out), .out(transistor_422_out), .gate(a6_3));
  Transistor #(.\type ("n")) transistor_425 (.in(1'b0), .out(transistor_425_out), .gate(transistor_141_out));
  Transistor transistor_426 (.in(1'b1), .out(transistor_426_out), .gate(transistor_602_out));
  Transistor transistor_427 (.in(1'b1), .out(transistor_426_out), .gate(transistor_322_out));
  Transistor #(.\type ("n")) transistor_428 (
    .in(transistor_429_out), .out(transistor_426_out), .gate(transistor_322_out));
  Transistor #(.\type ("n")) transistor_429 (.in(1'b0), .out(transistor_429_out), .gate(transistor_602_out));
  Transistor transistor_430 (.in(1'b1), .out(transistor_430_out), .gate(transistor_142_out));
  Transistor transistor_431 (.in(1'b1), .out(transistor_430_out), .gate(a7_3));
  Transistor #(.\type ("n")) transistor_432 (.in(transistor_433_out), .out(transistor_430_out), .gate(a7_3));
  Transistor #(.\type ("n")) transistor_433 (.in(1'b0), .out(transistor_433_out), .gate(transistor_142_out));
  Transistor transistor_434 (.in(1'b1), .out(transistor_434_out), .gate(transistor_607_out));
  Transistor transistor_435 (.in(1'b1), .out(transistor_369_out), .gate(sub));
  Transistor transistor_436 (.in(1'b1), .out(transistor_436_out), .gate(transistor_369_out));
  Transistor #(.\type ("n")) transistor_437 (
    .in(transistor_438_out), .out(transistor_369_out), .gate(transistor_607_out));
  Transistor #(.\type ("n")) transistor_438 (.in(1'b0), .out(transistor_438_out), .gate(sub));
  Transistor transistor_439 (.in(1'b1), .out(transistor_439_out), .gate(transistor_252_out));
  Transistor transistor_440 (.in(1'b1), .out(transistor_439_out), .gate(transistor_370_out));
  Transistor #(.\type ("n")) transistor_441 (
    .in(transistor_442_out), .out(transistor_439_out), .gate(transistor_252_out));
  Transistor #(.\type ("n")) transistor_442 (.in(1'b0), .out(transistor_442_out), .gate(transistor_370_out));
  Transistor transistor_443 (.in(1'b1), .out(transistor_443_out), .gate(transistor_370_out));
  Transistor transistor_444 (.in(1'b1), .out(transistor_443_out), .gate(transistor_134_out));
  Transistor #(.\type ("n")) transistor_445 (
    .in(transistor_446_out), .out(transistor_443_out), .gate(transistor_370_out));
  Transistor #(.\type ("n")) transistor_446 (.in(1'b0), .out(transistor_446_out), .gate(transistor_134_out));
  Transistor transistor_447 (.in(1'b1), .out(transistor_447_out), .gate(transistor_374_out));
  Transistor #(.\type ("n")) transistor_448 (.in(1'b0), .out(transistor_447_out), .gate(transistor_374_out));
  Transistor #(.\type ("n")) transistor_449 (.in(1'b0), .out(transistor_449_out), .gate(transistor_332_out));
  Transistor transistor_450 (.in(1'b1), .out(transistor_450_out), .gate(transistor_262_out));
  Transistor transistor_451 (.in(1'b1), .out(transistor_450_out), .gate(transistor_378_out));
  Transistor #(.\type ("n")) transistor_452 (
    .in(transistor_453_out), .out(transistor_450_out), .gate(transistor_262_out));
  Transistor #(.\type ("n")) transistor_453 (.in(1'b0), .out(transistor_453_out), .gate(transistor_378_out));
  Transistor transistor_454 (.in(1'b1), .out(transistor_454_out), .gate(transistor_572_out));
  Transistor transistor_455 (.in(1'b1), .out(transistor_454_out), .gate(transistor_378_out));
  Transistor #(.\type ("n")) transistor_456 (
    .in(transistor_457_out), .out(transistor_454_out), .gate(transistor_378_out));
  Transistor #(.\type ("n")) transistor_457 (.in(1'b0), .out(transistor_457_out), .gate(transistor_572_out));
  Transistor transistor_458 (.in(1'b1), .out(transistor_458_out), .gate(transistor_382_out));
  Transistor #(.\type ("n")) transistor_459 (.in(1'b0), .out(transistor_458_out), .gate(transistor_382_out));
  Transistor #(.\type ("n")) transistor_460 (.in(1'b0), .out(transistor_460_out), .gate(transistor_337_out));
  Transistor transistor_461 (.in(1'b1), .out(transistor_461_out), .gate(transistor_272_out));
  Transistor transistor_462 (.in(1'b1), .out(transistor_461_out), .gate(transistor_386_out));
  Transistor #(.\type ("n")) transistor_463 (
    .in(transistor_464_out), .out(transistor_461_out), .gate(transistor_272_out));
  Transistor #(.\type ("n")) transistor_464 (.in(1'b0), .out(transistor_464_out), .gate(transistor_386_out));
  Transistor transistor_465 (.in(1'b1), .out(transistor_465_out), .gate(transistor_577_out));
  Transistor transistor_466 (.in(1'b1), .out(transistor_465_out), .gate(transistor_386_out));
  Transistor #(.\type ("n")) transistor_467 (
    .in(transistor_468_out), .out(transistor_465_out), .gate(transistor_386_out));
  Transistor #(.\type ("n")) transistor_468 (.in(1'b0), .out(transistor_468_out), .gate(transistor_577_out));
  Transistor transistor_469 (.in(1'b1), .out(transistor_469_out), .gate(transistor_390_out));
  Transistor #(.\type ("n")) transistor_470 (.in(1'b0), .out(transistor_469_out), .gate(transistor_390_out));
  Transistor #(.\type ("n")) transistor_471 (.in(1'b0), .out(transistor_471_out), .gate(transistor_342_out));
  Transistor transistor_472 (.in(1'b1), .out(transistor_472_out), .gate(transistor_282_out));
  Transistor transistor_473 (.in(1'b1), .out(transistor_472_out), .gate(transistor_394_out));
  Transistor #(.\type ("n")) transistor_474 (
    .in(transistor_475_out), .out(transistor_472_out), .gate(transistor_282_out));
  Transistor #(.\type ("n")) transistor_475 (.in(1'b0), .out(transistor_475_out), .gate(transistor_394_out));
  Transistor transistor_476 (.in(1'b1), .out(transistor_476_out), .gate(transistor_582_out));
  Transistor transistor_477 (.in(1'b1), .out(transistor_476_out), .gate(transistor_394_out));
  Transistor #(.\type ("n")) transistor_478 (
    .in(transistor_479_out), .out(transistor_476_out), .gate(transistor_394_out));
  Transistor #(.\type ("n")) transistor_479 (.in(1'b0), .out(transistor_479_out), .gate(transistor_582_out));
  Transistor transistor_480 (.in(1'b1), .out(transistor_480_out), .gate(transistor_398_out));
  Transistor #(.\type ("n")) transistor_481 (.in(1'b0), .out(transistor_480_out), .gate(transistor_398_out));
  Transistor #(.\type ("n")) transistor_482 (.in(1'b0), .out(transistor_482_out), .gate(transistor_347_out));
  Transistor transistor_483 (.in(1'b1), .out(transistor_483_out), .gate(transistor_292_out));
  Transistor transistor_484 (.in(1'b1), .out(transistor_483_out), .gate(transistor_402_out));
  Transistor #(.\type ("n")) transistor_485 (
    .in(transistor_486_out), .out(transistor_483_out), .gate(transistor_292_out));
  Transistor #(.\type ("n")) transistor_486 (.in(1'b0), .out(transistor_486_out), .gate(transistor_402_out));
  Transistor transistor_487 (.in(1'b1), .out(transistor_487_out), .gate(transistor_402_out));
  Transistor transistor_488 (.in(1'b1), .out(transistor_487_out), .gate(transistor_587_out));
  Transistor #(.\type ("n")) transistor_489 (
    .in(transistor_490_out), .out(transistor_487_out), .gate(transistor_402_out));
  Transistor #(.\type ("n")) transistor_490 (.in(1'b0), .out(transistor_490_out), .gate(transistor_587_out));
  Transistor transistor_491 (.in(1'b1), .out(transistor_491_out), .gate(transistor_406_out));
  Transistor #(.\type ("n")) transistor_492 (.in(1'b0), .out(transistor_491_out), .gate(transistor_406_out));
  Transistor #(.\type ("n")) transistor_493 (.in(1'b0), .out(transistor_493_out), .gate(transistor_352_out));
  Transistor transistor_494 (.in(1'b1), .out(transistor_494_out), .gate(transistor_410_out));
  Transistor transistor_495 (.in(1'b1), .out(transistor_494_out), .gate(transistor_302_out));
  Transistor #(.\type ("n")) transistor_496 (
    .in(transistor_497_out), .out(transistor_494_out), .gate(transistor_302_out));
  Transistor #(.\type ("n")) transistor_497 (.in(1'b0), .out(transistor_497_out), .gate(transistor_410_out));
  Transistor transistor_498 (.in(1'b1), .out(transistor_498_out), .gate(transistor_410_out));
  Transistor transistor_499 (.in(1'b1), .out(transistor_498_out), .gate(transistor_592_out));
  Transistor #(.\type ("n")) transistor_500 (
    .in(transistor_501_out), .out(transistor_498_out), .gate(transistor_410_out));
  Transistor #(.\type ("n")) transistor_501 (.in(1'b0), .out(transistor_501_out), .gate(transistor_592_out));
  Transistor transistor_502 (.in(1'b1), .out(transistor_502_out), .gate(transistor_414_out));
  Transistor #(.\type ("n")) transistor_503 (.in(1'b0), .out(transistor_502_out), .gate(transistor_414_out));
  Transistor #(.\type ("n")) transistor_504 (.in(1'b0), .out(transistor_504_out), .gate(transistor_357_out));
  Transistor transistor_505 (.in(1'b1), .out(transistor_505_out), .gate(transistor_418_out));
  Transistor transistor_506 (.in(1'b1), .out(transistor_505_out), .gate(transistor_312_out));
  Transistor #(.\type ("n")) transistor_507 (
    .in(transistor_508_out), .out(transistor_505_out), .gate(transistor_312_out));
  Transistor #(.\type ("n")) transistor_508 (.in(1'b0), .out(transistor_508_out), .gate(transistor_418_out));
  Transistor transistor_509 (.in(1'b1), .out(transistor_509_out), .gate(transistor_418_out));
  Transistor transistor_510 (.in(1'b1), .out(transistor_509_out), .gate(transistor_597_out));
  Transistor #(.\type ("n")) transistor_511 (
    .in(transistor_512_out), .out(transistor_509_out), .gate(transistor_418_out));
  Transistor #(.\type ("n")) transistor_512 (.in(1'b0), .out(transistor_512_out), .gate(transistor_597_out));
  Transistor transistor_513 (.in(1'b1), .out(transistor_513_out), .gate(transistor_422_out));
  Transistor #(.\type ("n")) transistor_514 (.in(1'b0), .out(transistor_513_out), .gate(transistor_422_out));
  Transistor #(.\type ("n")) transistor_515 (.in(1'b0), .out(transistor_515_out), .gate(transistor_362_out));
  Transistor transistor_516 (.in(1'b1), .out(transistor_516_out), .gate(transistor_426_out));
  Transistor transistor_517 (.in(1'b1), .out(transistor_516_out), .gate(transistor_322_out));
  Transistor #(.\type ("n")) transistor_518 (
    .in(transistor_519_out), .out(transistor_516_out), .gate(transistor_322_out));
  Transistor #(.\type ("n")) transistor_519 (.in(1'b0), .out(transistor_519_out), .gate(transistor_426_out));
  Transistor transistor_520 (.in(1'b1), .out(transistor_520_out), .gate(transistor_426_out));
  Transistor transistor_521 (.in(1'b1), .out(transistor_520_out), .gate(transistor_602_out));
  Transistor #(.\type ("n")) transistor_522 (
    .in(transistor_523_out), .out(transistor_520_out), .gate(transistor_426_out));
  Transistor #(.\type ("n")) transistor_523 (.in(1'b0), .out(transistor_523_out), .gate(transistor_602_out));
  Transistor transistor_524 (.in(1'b1), .out(transistor_524_out), .gate(transistor_430_out));
  Transistor #(.\type ("n")) transistor_525 (.in(1'b0), .out(transistor_524_out), .gate(transistor_430_out));
  Transistor #(.\type ("n")) transistor_526 (.in(1'b0), .out(transistor_526_out), .gate(transistor_367_out));
  Transistor transistor_527 (.in(1'b1), .out(transistor_434_out), .gate(transistor_369_out));
  Transistor #(.\type ("n")) transistor_528 (
    .in(transistor_529_out), .out(transistor_434_out), .gate(transistor_607_out));
  Transistor #(.\type ("n")) transistor_529 (.in(1'b0), .out(transistor_529_out), .gate(transistor_369_out));
  Transistor transistor_530 (.in(1'b1), .out(cout), .gate(transistor_434_out));
  Transistor transistor_531 (.in(1'b1), .out(transistor_436_out), .gate(sub));
  Transistor #(.\type ("n")) transistor_532 (
    .in(transistor_533_out), .out(transistor_436_out), .gate(transistor_369_out));
  Transistor #(.\type ("n")) transistor_533 (.in(1'b0), .out(transistor_533_out), .gate(sub));
  Transistor transistor_534 (.in(1'b1), .out(sum0), .gate(transistor_439_out));
  Transistor transistor_535 (.in(1'b1), .out(transistor_535_out), .gate(transistor_332_out));
  Transistor transistor_536 (.in(transistor_535_out), .out(transistor_449_out), .gate(transistor_447_out));
  Transistor #(.\type ("n")) transistor_537 (.in(1'b0), .out(transistor_449_out), .gate(transistor_447_out));
  Transistor transistor_538 (.in(1'b1), .out(sum1), .gate(transistor_450_out));
  Transistor transistor_539 (.in(1'b1), .out(transistor_539_out), .gate(transistor_337_out));
  Transistor transistor_540 (.in(transistor_539_out), .out(transistor_460_out), .gate(transistor_458_out));
  Transistor #(.\type ("n")) transistor_541 (.in(1'b0), .out(transistor_460_out), .gate(transistor_458_out));
  Transistor transistor_542 (.in(1'b1), .out(sum2), .gate(transistor_461_out));
  Transistor transistor_543 (.in(1'b1), .out(transistor_543_out), .gate(transistor_342_out));
  Transistor transistor_544 (.in(transistor_543_out), .out(transistor_471_out), .gate(transistor_469_out));
  Transistor #(.\type ("n")) transistor_545 (.in(1'b0), .out(transistor_471_out), .gate(transistor_469_out));
  Transistor transistor_546 (.in(1'b1), .out(sum3), .gate(transistor_472_out));
  Transistor transistor_547 (.in(1'b1), .out(transistor_547_out), .gate(transistor_347_out));
  Transistor transistor_548 (.in(transistor_547_out), .out(transistor_482_out), .gate(transistor_480_out));
  Transistor #(.\type ("n")) transistor_549 (.in(1'b0), .out(transistor_482_out), .gate(transistor_480_out));
  Transistor transistor_550 (.in(1'b1), .out(sum4), .gate(transistor_483_out));
  Transistor transistor_551 (.in(1'b1), .out(transistor_551_out), .gate(transistor_352_out));
  Transistor transistor_552 (.in(transistor_551_out), .out(transistor_493_out), .gate(transistor_491_out));
  Transistor #(.\type ("n")) transistor_553 (.in(1'b0), .out(transistor_493_out), .gate(transistor_491_out));
  Transistor transistor_554 (.in(1'b1), .out(sum5), .gate(transistor_494_out));
  Transistor transistor_555 (.in(1'b1), .out(transistor_555_out), .gate(transistor_357_out));
  Transistor transistor_556 (.in(transistor_555_out), .out(transistor_504_out), .gate(transistor_502_out));
  Transistor #(.\type ("n")) transistor_557 (.in(1'b0), .out(transistor_504_out), .gate(transistor_502_out));
  Transistor transistor_558 (.in(1'b1), .out(sum6), .gate(transistor_505_out));
  Transistor transistor_559 (.in(1'b1), .out(transistor_559_out), .gate(transistor_362_out));
  Transistor transistor_560 (.in(transistor_559_out), .out(transistor_515_out), .gate(transistor_513_out));
  Transistor #(.\type ("n")) transistor_561 (.in(1'b0), .out(transistor_515_out), .gate(transistor_513_out));
  Transistor transistor_562 (.in(1'b1), .out(sum7), .gate(transistor_516_out));
  Transistor transistor_563 (.in(1'b1), .out(transistor_563_out), .gate(transistor_367_out));
  Transistor transistor_564 (.in(transistor_563_out), .out(transistor_526_out), .gate(transistor_524_out));
  Transistor #(.\type ("n")) transistor_565 (.in(1'b0), .out(transistor_526_out), .gate(transistor_524_out));
  Transistor transistor_566 (.in(1'b1), .out(cout), .gate(transistor_436_out));
  Transistor #(.\type ("n")) transistor_567 (.in(transistor_568_out), .out(cout), .gate(transistor_434_out));
  Transistor #(.\type ("n")) transistor_568 (.in(1'b0), .out(transistor_568_out), .gate(transistor_436_out));
  Transistor transistor_569 (.in(1'b1), .out(sum0), .gate(transistor_443_out));
  Transistor #(.\type ("n")) transistor_570 (.in(transistor_571_out), .out(sum0), .gate(transistor_439_out));
  Transistor #(.\type ("n")) transistor_571 (.in(1'b0), .out(transistor_571_out), .gate(transistor_443_out));
  Transistor transistor_572 (.in(1'b1), .out(transistor_572_out), .gate(transistor_449_out));
  Transistor #(.\type ("n")) transistor_573 (.in(1'b0), .out(transistor_572_out), .gate(transistor_449_out));
  Transistor transistor_574 (.in(1'b1), .out(sum1), .gate(transistor_454_out));
  Transistor #(.\type ("n")) transistor_575 (.in(transistor_576_out), .out(sum1), .gate(transistor_450_out));
  Transistor #(.\type ("n")) transistor_576 (.in(1'b0), .out(transistor_576_out), .gate(transistor_454_out));
  Transistor transistor_577 (.in(1'b1), .out(transistor_577_out), .gate(transistor_460_out));
  Transistor #(.\type ("n")) transistor_578 (.in(1'b0), .out(transistor_577_out), .gate(transistor_460_out));
  Transistor transistor_579 (.in(1'b1), .out(sum2), .gate(transistor_465_out));
  Transistor #(.\type ("n")) transistor_580 (.in(transistor_581_out), .out(sum2), .gate(transistor_461_out));
  Transistor #(.\type ("n")) transistor_581 (.in(1'b0), .out(transistor_581_out), .gate(transistor_465_out));
  Transistor transistor_582 (.in(1'b1), .out(transistor_582_out), .gate(transistor_471_out));
  Transistor #(.\type ("n")) transistor_583 (.in(1'b0), .out(transistor_582_out), .gate(transistor_471_out));
  Transistor transistor_584 (.in(1'b1), .out(sum3), .gate(transistor_476_out));
  Transistor #(.\type ("n")) transistor_585 (.in(transistor_586_out), .out(sum3), .gate(transistor_472_out));
  Transistor #(.\type ("n")) transistor_586 (.in(1'b0), .out(transistor_586_out), .gate(transistor_476_out));
  Transistor transistor_587 (.in(1'b1), .out(transistor_587_out), .gate(transistor_482_out));
  Transistor #(.\type ("n")) transistor_588 (.in(1'b0), .out(transistor_587_out), .gate(transistor_482_out));
  Transistor transistor_589 (.in(1'b1), .out(sum4), .gate(transistor_487_out));
  Transistor #(.\type ("n")) transistor_590 (.in(transistor_591_out), .out(sum4), .gate(transistor_483_out));
  Transistor #(.\type ("n")) transistor_591 (.in(1'b0), .out(transistor_591_out), .gate(transistor_487_out));
  Transistor transistor_592 (.in(1'b1), .out(transistor_592_out), .gate(transistor_493_out));
  Transistor #(.\type ("n")) transistor_593 (.in(1'b0), .out(transistor_592_out), .gate(transistor_493_out));
  Transistor transistor_594 (.in(1'b1), .out(sum5), .gate(transistor_498_out));
  Transistor #(.\type ("n")) transistor_595 (.in(transistor_596_out), .out(sum5), .gate(transistor_494_out));
  Transistor #(.\type ("n")) transistor_596 (.in(1'b0), .out(transistor_596_out), .gate(transistor_498_out));
  Transistor transistor_597 (.in(1'b1), .out(transistor_597_out), .gate(transistor_504_out));
  Transistor #(.\type ("n")) transistor_598 (.in(1'b0), .out(transistor_597_out), .gate(transistor_504_out));
  Transistor transistor_599 (.in(1'b1), .out(sum6), .gate(transistor_509_out));
  Transistor #(.\type ("n")) transistor_600 (.in(transistor_601_out), .out(sum6), .gate(transistor_505_out));
  Transistor #(.\type ("n")) transistor_601 (.in(1'b0), .out(transistor_601_out), .gate(transistor_509_out));
  Transistor transistor_602 (.in(1'b1), .out(transistor_602_out), .gate(transistor_515_out));
  Transistor #(.\type ("n")) transistor_603 (.in(1'b0), .out(transistor_602_out), .gate(transistor_515_out));
  Transistor transistor_604 (.in(1'b1), .out(sum7), .gate(transistor_520_out));
  Transistor #(.\type ("n")) transistor_605 (.in(transistor_606_out), .out(sum7), .gate(transistor_516_out));
  Transistor #(.\type ("n")) transistor_606 (.in(1'b0), .out(transistor_606_out), .gate(transistor_520_out));
  Transistor transistor_607 (.in(1'b1), .out(transistor_607_out), .gate(transistor_526_out));
  Transistor #(.\type ("n")) transistor_608 (.in(1'b0), .out(transistor_607_out), .gate(transistor_526_out));

  assign out_35 = a0;
  assign out_36 = a1;
  assign out_37 = a2;
  assign out_38 = a3;
  assign out_39 = a4;
  assign out_40 = a5;
  assign out_41 = a6;
  assign out_42 = a7;
  assign out_43 = a0_2;
  assign out_44 = a1_2;
  assign out_45 = a2_2;
  assign out_46 = a3_2;
  assign out_47 = a4_2;
  assign out_48 = a5_2;
  assign out_49 = a6_2;
  assign out_50 = a7_2;
  assign out_62 = out_61;
  assign out_64 = out_63;
  assign out_66 = out_65;
  assign out_68 = out_67;
  assign out_70 = out_69;
  assign out_72 = out_71;
  assign out_74 = out_73;
  assign out_76 = out_75;
endmodule

module PROCESSOR (
  input  sub,
  input  bus_0,
  input  rst,
  input  cin,
  input  r0_w,
  input  r0_r,
  input  r1_w,
  input  r1_r,
  input  r2_w,
  input  r2_r,
  input  r3_w,
  input  r3_r,
  input  pc_w,
  input  pc_r,
  input  bus0,
  input  ra_w,
  input  rb_w,
  input  op2,
  input  op1,
  input  op0,
  input  rd_r,
  input  cin_shr,
  output bus_0_2,
  output sub_2,
  output cout_add,
  output rb_w_2,
  output ra_w_2,
  output bus0_2,
  output cout_shl,
  output cout_shr
);

  wire transistor_1_out, transistor_3_out, transistor_7_out, transistor_9_out, transistor_13_out,
       transistor_15_out, transistor_17_out, transistor_19_out, transistor_23_out, transistor_25_out,
       transistor_29_out, transistor_33_out, transistor_35_out, transistor_39_out, transistor_41_out,
       transistor_45_out, transistor_49_out, transistor_51_out, transistor_55_out, transistor_57_out,
       transistor_61_out, transistor_65_out, transistor_67_out, transistor_71_out, transistor_73_out,
       transistor_77_out, transistor_81_out, transistor_83_out, transistor_87_out, transistor_89_out,
       transistor_93_out, transistor_99_out, transistor_101_out, transistor_105_out, transistor_107_out,
       transistor_111_out, transistor_114_out, transistor_115_out, transistor_117_out, transistor_118_out,
       transistor_120_out, transistor_123_out, transistor_126_out, transistor_127_out, transistor_130_out,
       transistor_131_out, transistor_133_out, transistor_135_out, transistor_138_out, transistor_139_out,
       transistor_141_out, transistor_143_out, transistor_146_out, transistor_147_out, transistor_149_out,
       transistor_151_out, transistor_154_out, transistor_155_out, transistor_158_out, transistor_159_out,
       transistor_161_out, transistor_163_out, transistor_165_out, transistor_168_out, transistor_169_out,
       transistor_172_out, transistor_173_out, transistor_176_out, transistor_177_out, transistor_178_out,
       transistor_183_out, transistor_186_out, transistor_187_out, transistor_189_out, transistor_192_out,
       transistor_193_out, transistor_196_out, transistor_197_out, transistor_200_out, transistor_201_out,
       transistor_204_out, transistor_205_out, transistor_207_out, transistor_211_out, transistor_213_out,
       transistor_217_out, transistor_219_out, transistor_223_out, transistor_225_out, transistor_229_out,
       transistor_231_out, transistor_235_out, transistor_237_out, transistor_241_out, transistor_243_out,
       transistor_245_out, transistor_249_out, transistor_253_out;

  Pull_Resistor pull_resistor_1 (.node(bus_0));
  Transistor transistor_1 (.in(1'b1), .out(transistor_1_out), .gate(r0_w));
  Transistor #(.\type ("n")) transistor_2 (.in(1'b0), .out(transistor_1_out), .gate(r0_w));
  Transistor #(.\type ("n")) transistor_3 (.in(bus_0), .out(transistor_3_out), .gate(r0_w));
  Transistor #(.gate("br")) transistor_4 (.in(bus_0), .out(transistor_3_out), .gate(transistor_1_out));
  Transistor #(.\type ("n")) transistor_5 (.in(transistor_7_out), .out(transistor_3_out), .gate(transistor_1_out));
  Transistor #(.gate("br")) transistor_6 (.in(transistor_7_out), .out(transistor_3_out), .gate(r0_w));
  Transistor #(.\type ("n")) transistor_7 (.in(1'b0), .out(transistor_7_out), .gate(rst));
  Transistor #(.gate("br")) transistor_8 (.in(1'b0), .out(transistor_7_out), .gate(transistor_9_out));
  Transistor transistor_9 (.in(1'b1), .out(transistor_9_out), .gate(rst));
  Transistor #(.\type ("n")) transistor_10 (.in(1'b0), .out(transistor_9_out), .gate(rst));
  Transistor #(.\type ("n")) transistor_11 (.in(transistor_3_out), .out(transistor_7_out), .gate(transistor_9_out));
  Transistor #(.gate("br")) transistor_12 (.in(transistor_3_out), .out(transistor_7_out), .gate(rst));
  Transistor transistor_13 (.in(1'b1), .out(transistor_13_out), .gate(r0_r));
  Transistor #(.\type ("n")) transistor_14 (.in(1'b0), .out(transistor_13_out), .gate(r0_r));
  Transistor #(.gate("br")) transistor_15 (.in(transistor_7_out), .out(transistor_15_out), .gate(transistor_13_out));
  Transistor #(.\type ("n")) transistor_16 (.in(transistor_7_out), .out(transistor_15_out), .gate(r0_r));
  Transistor #(.\type ("n")) transistor_17 (.in(bus_0), .out(transistor_17_out), .gate(r1_w));
  Transistor #(.gate("br")) transistor_18 (.in(bus_0), .out(transistor_17_out), .gate(transistor_19_out));
  Transistor transistor_19 (.in(1'b1), .out(transistor_19_out), .gate(r1_w));
  Transistor #(.\type ("n")) transistor_20 (.in(1'b0), .out(transistor_19_out), .gate(r1_w));
  Transistor #(.\type ("n")) transistor_21 (.in(transistor_25_out), .out(transistor_17_out), .gate(transistor_19_out));
  Transistor #(.gate("br")) transistor_22 (.in(transistor_25_out), .out(transistor_17_out), .gate(r1_w));
  Transistor transistor_23 (.in(1'b1), .out(transistor_23_out), .gate(rst));
  Transistor #(.\type ("n")) transistor_24 (.in(1'b0), .out(transistor_23_out), .gate(rst));
  Transistor #(.\type ("n")) transistor_25 (.in(1'b0), .out(transistor_25_out), .gate(rst));
  Transistor #(.gate("br")) transistor_26 (.in(1'b0), .out(transistor_25_out), .gate(transistor_23_out));
  Transistor #(.\type ("n")) transistor_27 (.in(transistor_17_out), .out(transistor_25_out), .gate(transistor_23_out));
  Transistor #(.gate("br")) transistor_28 (.in(transistor_17_out), .out(transistor_25_out), .gate(rst));
  Transistor transistor_29 (.in(1'b1), .out(transistor_29_out), .gate(r1_r));
  Transistor #(.\type ("n")) transistor_30 (.in(1'b0), .out(transistor_29_out), .gate(r1_r));
  Transistor #(.gate("br")) transistor_31 (.in(transistor_25_out), .out(transistor_15_out), .gate(transistor_29_out));
  Transistor #(.\type ("n")) transistor_32 (.in(transistor_25_out), .out(transistor_15_out), .gate(r1_r));
  Transistor transistor_33 (.in(1'b1), .out(transistor_33_out), .gate(r2_w));
  Transistor #(.\type ("n")) transistor_34 (.in(1'b0), .out(transistor_33_out), .gate(r2_w));
  Transistor #(.\type ("n")) transistor_35 (.in(bus_0), .out(transistor_35_out), .gate(r2_w));
  Transistor #(.gate("br")) transistor_36 (.in(bus_0), .out(transistor_35_out), .gate(transistor_33_out));
  Transistor #(.\type ("n")) transistor_37 (.in(transistor_39_out), .out(transistor_35_out), .gate(transistor_33_out));
  Transistor #(.gate("br")) transistor_38 (.in(transistor_39_out), .out(transistor_35_out), .gate(r2_w));
  Transistor #(.\type ("n")) transistor_39 (.in(1'b0), .out(transistor_39_out), .gate(rst));
  Transistor #(.gate("br")) transistor_40 (.in(1'b0), .out(transistor_39_out), .gate(transistor_41_out));
  Transistor transistor_41 (.in(1'b1), .out(transistor_41_out), .gate(rst));
  Transistor #(.\type ("n")) transistor_42 (.in(1'b0), .out(transistor_41_out), .gate(rst));
  Transistor #(.\type ("n")) transistor_43 (.in(transistor_35_out), .out(transistor_39_out), .gate(transistor_41_out));
  Transistor #(.gate("br")) transistor_44 (.in(transistor_35_out), .out(transistor_39_out), .gate(rst));
  Transistor transistor_45 (.in(1'b1), .out(transistor_45_out), .gate(r2_r));
  Transistor #(.\type ("n")) transistor_46 (.in(1'b0), .out(transistor_45_out), .gate(r2_r));
  Transistor #(.\type ("n")) transistor_47 (.in(transistor_39_out), .out(transistor_15_out), .gate(r2_r));
  Transistor #(.gate("br")) transistor_48 (.in(transistor_39_out), .out(transistor_15_out), .gate(transistor_45_out));
  Transistor #(.\type ("n")) transistor_49 (.in(bus_0), .out(transistor_49_out), .gate(r3_w));
  Transistor #(.gate("br")) transistor_50 (.in(bus_0), .out(transistor_49_out), .gate(transistor_51_out));
  Transistor transistor_51 (.in(1'b1), .out(transistor_51_out), .gate(r3_w));
  Transistor #(.\type ("n")) transistor_52 (.in(1'b0), .out(transistor_51_out), .gate(r3_w));
  Transistor #(.\type ("n")) transistor_53 (.in(transistor_57_out), .out(transistor_49_out), .gate(transistor_51_out));
  Transistor #(.gate("br")) transistor_54 (.in(transistor_57_out), .out(transistor_49_out), .gate(r3_w));
  Transistor transistor_55 (.in(1'b1), .out(transistor_55_out), .gate(rst));
  Transistor #(.\type ("n")) transistor_56 (.in(1'b0), .out(transistor_55_out), .gate(rst));
  Transistor #(.\type ("n")) transistor_57 (.in(1'b0), .out(transistor_57_out), .gate(rst));
  Transistor #(.gate("br")) transistor_58 (.in(1'b0), .out(transistor_57_out), .gate(transistor_55_out));
  Transistor #(.\type ("n")) transistor_59 (.in(transistor_49_out), .out(transistor_57_out), .gate(transistor_55_out));
  Transistor #(.gate("br")) transistor_60 (.in(transistor_49_out), .out(transistor_57_out), .gate(rst));
  Transistor transistor_61 (.in(1'b1), .out(transistor_61_out), .gate(r3_r));
  Transistor #(.\type ("n")) transistor_62 (.in(1'b0), .out(transistor_61_out), .gate(r3_r));
  Transistor #(.gate("br")) transistor_63 (.in(transistor_57_out), .out(transistor_15_out), .gate(transistor_61_out));
  Transistor #(.\type ("n")) transistor_64 (.in(transistor_57_out), .out(transistor_15_out), .gate(r3_r));
  Transistor transistor_65 (.in(1'b1), .out(transistor_65_out), .gate(pc_w));
  Transistor #(.\type ("n")) transistor_66 (.in(1'b0), .out(transistor_65_out), .gate(pc_w));
  Transistor #(.\type ("n")) transistor_67 (.in(bus_0), .out(transistor_67_out), .gate(pc_w));
  Transistor #(.gate("br")) transistor_68 (.in(bus_0), .out(transistor_67_out), .gate(transistor_65_out));
  Transistor #(.\type ("n")) transistor_69 (.in(transistor_71_out), .out(transistor_67_out), .gate(transistor_65_out));
  Transistor #(.gate("br")) transistor_70 (.in(transistor_71_out), .out(transistor_67_out), .gate(pc_w));
  Transistor #(.\type ("n")) transistor_71 (.in(1'b0), .out(transistor_71_out), .gate(rst));
  Transistor #(.gate("br")) transistor_72 (.in(1'b0), .out(transistor_71_out), .gate(transistor_73_out));
  Transistor transistor_73 (.in(1'b1), .out(transistor_73_out), .gate(rst));
  Transistor #(.\type ("n")) transistor_74 (.in(1'b0), .out(transistor_73_out), .gate(rst));
  Transistor #(.\type ("n")) transistor_75 (.in(transistor_67_out), .out(transistor_71_out), .gate(transistor_73_out));
  Transistor #(.gate("br")) transistor_76 (.in(transistor_67_out), .out(transistor_71_out), .gate(rst));
  Transistor transistor_77 (.in(1'b1), .out(transistor_77_out), .gate(pc_r));
  Transistor #(.\type ("n")) transistor_78 (.in(1'b0), .out(transistor_77_out), .gate(pc_r));
  Transistor #(.gate("br")) transistor_79 (.in(transistor_71_out), .out(transistor_15_out), .gate(transistor_77_out));
  Transistor #(.\type ("n")) transistor_80 (.in(transistor_71_out), .out(transistor_15_out), .gate(pc_r));
  Transistor transistor_81 (.in(1'b0), .out(transistor_81_out), .gate(bus0));
  Transistor #(.\type ("n"), .gate("br")) transistor_82 (.in(1'b0), .out(transistor_81_out), .gate(transistor_83_out));
  Transistor transistor_83 (.in(1'b1), .out(transistor_83_out), .gate(bus0));
  Transistor #(.\type ("n")) transistor_84 (.in(1'b0), .out(transistor_83_out), .gate(bus0));
  Transistor transistor_85 (.in(transistor_15_out), .out(transistor_81_out), .gate(transistor_83_out));
  Transistor #(.\type ("n"), .gate("br")) transistor_86 (.in(transistor_15_out), .out(transistor_81_out), .gate(bus0));
  Transistor transistor_87 (.in(1'b1), .out(transistor_87_out), .gate(ra_w));
  Transistor #(.\type ("n")) transistor_88 (.in(1'b0), .out(transistor_87_out), .gate(ra_w));
  Pull_Resistor pull_resistor_2 (.node(transistor_81_out));
  Transistor #(.\type ("n")) transistor_89 (.in(transistor_81_out), .out(transistor_89_out), .gate(ra_w));
  Transistor #(.gate("br")) transistor_90 (.in(transistor_81_out), .out(transistor_89_out), .gate(transistor_87_out));
  Transistor #(.\type ("n")) transistor_91 (.in(cout_shl), .out(transistor_89_out), .gate(transistor_87_out));
  Transistor #(.gate("br")) transistor_92 (.in(cout_shl), .out(transistor_89_out), .gate(ra_w));
  Transistor transistor_93 (.in(1'b1), .out(transistor_93_out), .gate(rst));
  Transistor #(.\type ("n")) transistor_94 (.in(1'b0), .out(transistor_93_out), .gate(rst));
  Transistor #(.\type ("n")) transistor_95 (.in(1'b0), .out(cout_shl), .gate(rst));
  Transistor #(.gate("br")) transistor_96 (.in(1'b0), .out(cout_shl), .gate(transistor_93_out));
  Transistor #(.\type ("n")) transistor_97 (.in(transistor_89_out), .out(cout_shl), .gate(transistor_93_out));
  Transistor #(.gate("br")) transistor_98 (.in(transistor_89_out), .out(cout_shl), .gate(rst));
  Transistor transistor_99 (.in(1'b1), .out(transistor_99_out), .gate(rb_w));
  Transistor #(.\type ("n")) transistor_100 (.in(1'b0), .out(transistor_99_out), .gate(rb_w));
  Transistor #(.\type ("n")) transistor_101 (.in(transistor_81_out), .out(transistor_101_out), .gate(rb_w));
  Transistor #(.gate("br")) transistor_102 (.in(transistor_81_out), .out(transistor_101_out), .gate(transistor_99_out));
  Transistor #(.\type ("n")) transistor_103 (
    .in(transistor_105_out), .out(transistor_101_out), .gate(transistor_99_out));
  Transistor #(.gate("br")) transistor_104 (.in(transistor_105_out), .out(transistor_101_out), .gate(rb_w));
  Transistor #(.\type ("n")) transistor_105 (.in(1'b0), .out(transistor_105_out), .gate(rst));
  Transistor #(.gate("br")) transistor_106 (.in(1'b0), .out(transistor_105_out), .gate(transistor_107_out));
  Transistor transistor_107 (.in(1'b1), .out(transistor_107_out), .gate(rst));
  Transistor #(.\type ("n")) transistor_108 (.in(1'b0), .out(transistor_107_out), .gate(rst));
  Transistor #(.\type ("n")) transistor_109 (
    .in(transistor_101_out), .out(transistor_105_out), .gate(transistor_107_out));
  Transistor #(.gate("br")) transistor_110 (.in(transistor_101_out), .out(transistor_105_out), .gate(rst));
  Transistor transistor_111 (.in(1'b1), .out(transistor_111_out), .gate(cout_shl));
  Transistor transistor_112 (.in(1'b1), .out(transistor_111_out), .gate(transistor_105_out));
  Transistor #(.\type ("n")) transistor_113 (
    .in(transistor_114_out), .out(transistor_111_out), .gate(transistor_105_out));
  Transistor #(.\type ("n")) transistor_114 (.in(1'b0), .out(transistor_114_out), .gate(cout_shl));
  Transistor transistor_115 (.in(1'b1), .out(transistor_115_out), .gate(transistor_111_out));
  Transistor #(.\type ("n")) transistor_116 (.in(1'b0), .out(transistor_115_out), .gate(transistor_111_out));
  Transistor #(.\type ("n")) transistor_117 (.in(1'b0), .out(transistor_117_out), .gate(cout_shl));
  Transistor transistor_118 (.in(1'b1), .out(transistor_118_out), .gate(cout_shl));
  Transistor transistor_119 (.in(transistor_118_out), .out(transistor_117_out), .gate(transistor_105_out));
  Transistor transistor_120 (.in(1'b1), .out(transistor_120_out), .gate(transistor_117_out));
  Transistor #(.\type ("n")) transistor_121 (.in(1'b0), .out(transistor_117_out), .gate(transistor_105_out));
  Transistor #(.\type ("n")) transistor_122 (.in(1'b0), .out(transistor_120_out), .gate(transistor_117_out));
  Transistor transistor_123 (.in(1'b1), .out(transistor_123_out), .gate(cout_shl));
  Transistor transistor_124 (.in(1'b1), .out(transistor_123_out), .gate(transistor_105_out));
  Transistor #(.\type ("n")) transistor_125 (.in(transistor_126_out), .out(transistor_123_out), .gate(cout_shl));
  Transistor #(.\type ("n")) transistor_126 (.in(1'b0), .out(transistor_126_out), .gate(transistor_105_out));
  Transistor transistor_127 (.in(1'b1), .out(transistor_127_out), .gate(transistor_105_out));
  Transistor transistor_128 (.in(1'b1), .out(transistor_127_out), .gate(transistor_123_out));
  Transistor #(.\type ("n")) transistor_129 (
    .in(transistor_130_out), .out(transistor_127_out), .gate(transistor_123_out));
  Transistor #(.\type ("n")) transistor_130 (.in(1'b0), .out(transistor_130_out), .gate(transistor_105_out));
  Transistor transistor_131 (.in(1'b1), .out(transistor_131_out), .gate(cout_shl));
  Transistor transistor_132 (.in(1'b1), .out(transistor_131_out), .gate(transistor_123_out));
  Transistor transistor_133 (.in(1'b1), .out(transistor_133_out), .gate(transistor_131_out));
  Transistor #(.\type ("n")) transistor_134 (
    .in(transistor_135_out), .out(transistor_131_out), .gate(transistor_123_out));
  Transistor #(.\type ("n")) transistor_135 (.in(1'b0), .out(transistor_135_out), .gate(cout_shl));
  Transistor transistor_136 (.in(1'b1), .out(transistor_133_out), .gate(transistor_127_out));
  Transistor #(.\type ("n")) transistor_137 (
    .in(transistor_138_out), .out(transistor_133_out), .gate(transistor_131_out));
  Transistor #(.\type ("n")) transistor_138 (.in(1'b0), .out(transistor_138_out), .gate(transistor_127_out));
  Transistor transistor_139 (.in(1'b1), .out(transistor_139_out), .gate(sub));
  Transistor transistor_140 (.in(1'b1), .out(transistor_139_out), .gate(transistor_105_out));
  Transistor transistor_141 (.in(1'b1), .out(transistor_141_out), .gate(transistor_139_out));
  Transistor #(.\type ("n")) transistor_142 (.in(transistor_143_out), .out(transistor_139_out), .gate(sub));
  Transistor #(.\type ("n")) transistor_143 (.in(1'b0), .out(transistor_143_out), .gate(transistor_105_out));
  Transistor transistor_144 (.in(1'b1), .out(transistor_141_out), .gate(transistor_105_out));
  Transistor #(.\type ("n")) transistor_145 (
    .in(transistor_146_out), .out(transistor_141_out), .gate(transistor_139_out));
  Transistor #(.\type ("n")) transistor_146 (.in(1'b0), .out(transistor_146_out), .gate(transistor_105_out));
  Transistor transistor_147 (.in(1'b1), .out(transistor_147_out), .gate(sub));
  Transistor transistor_148 (.in(1'b1), .out(transistor_147_out), .gate(transistor_139_out));
  Transistor transistor_149 (.in(1'b1), .out(transistor_149_out), .gate(transistor_147_out));
  Transistor #(.\type ("n")) transistor_150 (
    .in(transistor_151_out), .out(transistor_147_out), .gate(transistor_139_out));
  Transistor #(.\type ("n")) transistor_151 (.in(1'b0), .out(transistor_151_out), .gate(sub));
  Transistor transistor_152 (.in(1'b1), .out(transistor_149_out), .gate(transistor_141_out));
  Transistor #(.\type ("n")) transistor_153 (
    .in(transistor_154_out), .out(transistor_149_out), .gate(transistor_147_out));
  Transistor #(.\type ("n")) transistor_154 (.in(1'b0), .out(transistor_154_out), .gate(transistor_141_out));
  Transistor transistor_155 (.in(1'b1), .out(transistor_155_out), .gate(cout_shl));
  Transistor transistor_156 (.in(1'b1), .out(transistor_155_out), .gate(transistor_149_out));
  Transistor #(.\type ("n")) transistor_157 (.in(transistor_158_out), .out(transistor_155_out), .gate(cout_shl));
  Transistor #(.\type ("n")) transistor_158 (.in(1'b0), .out(transistor_158_out), .gate(transistor_149_out));
  Transistor transistor_159 (.in(1'b1), .out(transistor_159_out), .gate(transistor_155_out));
  Transistor #(.\type ("n")) transistor_160 (.in(1'b0), .out(transistor_159_out), .gate(transistor_155_out));
  Transistor transistor_161 (.in(1'b1), .out(transistor_161_out), .gate(cout_shl));
  Transistor transistor_162 (.in(1'b1), .out(transistor_161_out), .gate(transistor_149_out));
  Transistor transistor_163 (.in(1'b1), .out(transistor_163_out), .gate(transistor_161_out));
  Transistor #(.\type ("n")) transistor_164 (.in(transistor_165_out), .out(transistor_161_out), .gate(cout_shl));
  Transistor #(.\type ("n")) transistor_165 (.in(1'b0), .out(transistor_165_out), .gate(transistor_149_out));
  Transistor transistor_166 (.in(1'b1), .out(transistor_163_out), .gate(transistor_149_out));
  Transistor #(.\type ("n")) transistor_167 (
    .in(transistor_168_out), .out(transistor_163_out), .gate(transistor_161_out));
  Transistor #(.\type ("n")) transistor_168 (.in(1'b0), .out(transistor_168_out), .gate(transistor_149_out));
  Transistor transistor_169 (.in(1'b1), .out(transistor_169_out), .gate(transistor_161_out));
  Transistor transistor_170 (.in(1'b1), .out(transistor_169_out), .gate(cout_shl));
  Transistor #(.\type ("n")) transistor_171 (
    .in(transistor_172_out), .out(transistor_169_out), .gate(transistor_161_out));
  Transistor #(.\type ("n")) transistor_172 (.in(1'b0), .out(transistor_172_out), .gate(cout_shl));
  Transistor transistor_173 (.in(1'b1), .out(transistor_173_out), .gate(transistor_169_out));
  Transistor transistor_174 (.in(1'b1), .out(transistor_173_out), .gate(transistor_163_out));
  Transistor #(.\type ("n")) transistor_175 (
    .in(transistor_176_out), .out(transistor_173_out), .gate(transistor_169_out));
  Transistor #(.\type ("n")) transistor_176 (.in(1'b0), .out(transistor_176_out), .gate(transistor_163_out));
  Transistor transistor_177 (.in(1'b1), .out(transistor_177_out), .gate(transistor_159_out));
  Transistor transistor_178 (.in(transistor_177_out), .out(transistor_178_out), .gate(transistor_187_out));
  Transistor #(.\type ("n")) transistor_179 (.in(1'b0), .out(transistor_178_out), .gate(transistor_187_out));
  Transistor #(.\type ("n")) transistor_180 (.in(1'b0), .out(transistor_178_out), .gate(transistor_159_out));
  Transistor transistor_181 (.in(1'b1), .out(cout_add), .gate(transistor_178_out));
  Transistor #(.\type ("n")) transistor_182 (.in(1'b0), .out(cout_add), .gate(transistor_178_out));
  Transistor transistor_183 (.in(1'b1), .out(transistor_183_out), .gate(transistor_173_out));
  Transistor transistor_184 (.in(1'b1), .out(transistor_183_out), .gate(cin));
  Transistor #(.\type ("n")) transistor_185 (.in(transistor_186_out), .out(transistor_183_out), .gate(cin));
  Transistor #(.\type ("n")) transistor_186 (.in(1'b0), .out(transistor_186_out), .gate(transistor_173_out));
  Transistor transistor_187 (.in(1'b1), .out(transistor_187_out), .gate(transistor_183_out));
  Transistor #(.\type ("n")) transistor_188 (.in(1'b0), .out(transistor_187_out), .gate(transistor_183_out));
  Transistor transistor_189 (.in(1'b1), .out(transistor_189_out), .gate(transistor_173_out));
  Transistor transistor_190 (.in(1'b1), .out(transistor_189_out), .gate(cin));
  Transistor #(.\type ("n")) transistor_191 (
    .in(transistor_192_out), .out(transistor_189_out), .gate(transistor_173_out));
  Transistor #(.\type ("n")) transistor_192 (.in(1'b0), .out(transistor_192_out), .gate(cin));
  Transistor transistor_193 (.in(1'b1), .out(transistor_193_out), .gate(transistor_189_out));
  Transistor transistor_194 (.in(1'b1), .out(transistor_193_out), .gate(cin));
  Transistor #(.\type ("n")) transistor_195 (
    .in(transistor_196_out), .out(transistor_193_out), .gate(transistor_189_out));
  Transistor #(.\type ("n")) transistor_196 (.in(1'b0), .out(transistor_196_out), .gate(cin));
  Transistor transistor_197 (.in(1'b1), .out(transistor_197_out), .gate(transistor_189_out));
  Transistor transistor_198 (.in(1'b1), .out(transistor_197_out), .gate(transistor_173_out));
  Transistor #(.\type ("n")) transistor_199 (
    .in(transistor_200_out), .out(transistor_197_out), .gate(transistor_189_out));
  Transistor #(.\type ("n")) transistor_200 (.in(1'b0), .out(transistor_200_out), .gate(transistor_173_out));
  Transistor transistor_201 (.in(1'b1), .out(transistor_201_out), .gate(transistor_197_out));
  Transistor transistor_202 (.in(1'b1), .out(transistor_201_out), .gate(transistor_193_out));
  Transistor #(.\type ("n")) transistor_203 (
    .in(transistor_204_out), .out(transistor_201_out), .gate(transistor_197_out));
  Transistor #(.\type ("n")) transistor_204 (.in(1'b0), .out(transistor_204_out), .gate(transistor_193_out));
  Transistor transistor_205 (.in(1'b1), .out(transistor_205_out), .gate(op0));
  Transistor #(.\type ("n")) transistor_206 (.in(1'b0), .out(transistor_205_out), .gate(op0));
  Transistor #(.\type ("n")) transistor_207 (.in(cin_shr), .out(transistor_207_out), .gate(op0));
  Transistor #(.gate("br")) transistor_208 (.in(cin_shr), .out(transistor_207_out), .gate(transistor_205_out));
  Transistor #(.gate("br")) transistor_209 (.in(1'b0), .out(transistor_207_out), .gate(op0));
  Transistor #(.\type ("n")) transistor_210 (.in(1'b0), .out(transistor_207_out), .gate(transistor_205_out));
  Transistor #(.\type ("n")) transistor_211 (.in(transistor_133_out), .out(transistor_211_out), .gate(op0));
  Transistor #(.gate("br")) transistor_212 (
    .in(transistor_133_out), .out(transistor_211_out), .gate(transistor_213_out));
  Transistor #(.\type ("n")) transistor_213 (.in(1'b0), .out(transistor_213_out), .gate(op0));
  Transistor transistor_214 (.in(1'b1), .out(transistor_213_out), .gate(op0));
  Transistor #(.gate("br")) transistor_215 (.in(transistor_120_out), .out(transistor_211_out), .gate(op0));
  Transistor #(.\type ("n")) transistor_216 (
    .in(transistor_120_out), .out(transistor_211_out), .gate(transistor_213_out));
  Transistor transistor_217 (.in(1'b1), .out(transistor_217_out), .gate(op0));
  Transistor #(.\type ("n")) transistor_218 (.in(1'b0), .out(transistor_217_out), .gate(op0));
  Transistor #(.gate("br")) transistor_219 (
    .in(transistor_115_out), .out(transistor_219_out), .gate(transistor_217_out));
  Transistor #(.\type ("n")) transistor_220 (.in(transistor_115_out), .out(transistor_219_out), .gate(op0));
  Transistor #(.gate("br")) transistor_221 (.in(cout_shl), .out(transistor_219_out), .gate(op0));
  Transistor #(.\type ("n")) transistor_222 (.in(cout_shl), .out(transistor_219_out), .gate(transistor_217_out));
  Transistor #(.gate("br")) transistor_223 (
    .in(transistor_207_out), .out(transistor_223_out), .gate(transistor_225_out));
  Transistor #(.\type ("n")) transistor_224 (.in(transistor_207_out), .out(transistor_223_out), .gate(op1));
  Transistor #(.\type ("n")) transistor_225 (.in(1'b0), .out(transistor_225_out), .gate(op1));
  Transistor transistor_226 (.in(1'b1), .out(transistor_225_out), .gate(op1));
  Transistor #(.gate("br")) transistor_227 (.in(transistor_201_out), .out(transistor_223_out), .gate(op1));
  Transistor #(.\type ("n")) transistor_228 (
    .in(transistor_201_out), .out(transistor_223_out), .gate(transistor_225_out));
  Transistor #(.\type ("n")) transistor_229 (.in(1'b0), .out(transistor_229_out), .gate(op1));
  Transistor transistor_230 (.in(1'b1), .out(transistor_229_out), .gate(op1));
  Transistor #(.gate("br")) transistor_231 (
    .in(transistor_211_out), .out(transistor_231_out), .gate(transistor_229_out));
  Transistor #(.\type ("n")) transistor_232 (.in(transistor_211_out), .out(transistor_231_out), .gate(op1));
  Transistor #(.gate("br")) transistor_233 (.in(transistor_219_out), .out(transistor_231_out), .gate(op1));
  Transistor #(.\type ("n")) transistor_234 (
    .in(transistor_219_out), .out(transistor_231_out), .gate(transistor_229_out));
  Transistor #(.gate("br")) transistor_235 (
    .in(transistor_223_out), .out(transistor_235_out), .gate(transistor_237_out));
  Transistor #(.\type ("n")) transistor_236 (.in(transistor_223_out), .out(transistor_235_out), .gate(op2));
  Transistor transistor_237 (.in(1'b1), .out(transistor_237_out), .gate(op2));
  Transistor #(.\type ("n")) transistor_238 (.in(1'b0), .out(transistor_237_out), .gate(op2));
  Transistor #(.\type ("n")) transistor_239 (
    .in(transistor_231_out), .out(transistor_235_out), .gate(transistor_237_out));
  Transistor #(.gate("br")) transistor_240 (.in(transistor_231_out), .out(transistor_235_out), .gate(op2));
  Pull_Resistor pull_resistor_3 (.node(transistor_235_out));
  Transistor transistor_241 (.in(1'b1), .out(transistor_241_out), .gate(1'b1));
  Transistor #(.\type ("n")) transistor_242 (.in(1'b0), .out(transistor_241_out), .gate(1'b1));
  Transistor #(.\type ("n")) transistor_243 (.in(transistor_235_out), .out(transistor_243_out), .gate(1'b1));
  Transistor #(.gate("br")) transistor_244 (
    .in(transistor_235_out), .out(transistor_243_out), .gate(transistor_241_out));
  Transistor transistor_245 (.in(1'b1), .out(transistor_245_out), .gate(rst));
  Transistor #(.\type ("n")) transistor_246 (.in(1'b0), .out(transistor_245_out), .gate(rst));
  Transistor #(.\type ("n")) transistor_247 (
    .in(transistor_249_out), .out(transistor_243_out), .gate(transistor_241_out));
  Transistor #(.gate("br")) transistor_248 (.in(transistor_249_out), .out(transistor_243_out), .gate(1'b1));
  Transistor #(.\type ("n")) transistor_249 (.in(1'b0), .out(transistor_249_out), .gate(rst));
  Transistor #(.gate("br")) transistor_250 (.in(1'b0), .out(transistor_249_out), .gate(transistor_245_out));
  Transistor #(.\type ("n")) transistor_251 (
    .in(transistor_243_out), .out(transistor_249_out), .gate(transistor_245_out));
  Transistor #(.gate("br")) transistor_252 (.in(transistor_243_out), .out(transistor_249_out), .gate(rst));
  Transistor transistor_253 (.in(1'b1), .out(transistor_253_out), .gate(rd_r));
  Transistor #(.\type ("n")) transistor_254 (.in(1'b0), .out(transistor_253_out), .gate(rd_r));
  Transistor #(.gate("br")) transistor_255 (.in(transistor_249_out), .out(bus_0_2), .gate(transistor_253_out));
  Transistor #(.\type ("n")) transistor_256 (.in(transistor_249_out), .out(bus_0_2), .gate(rd_r));

  assign bus0_2 = bus0;
  assign cout_shr = cout_shl;
  assign ra_w_2 = ra_w;
  assign rb_w_2 = rb_w;
  assign sub_2 = sub;

  // Notes on the sheet:
  //   cin[0] = xor(sub, cin), don't foget
  //   add/sub
  //   shr
  //   shl
  //   xor
  //   orr
  //   and
  //   mov
endmodule

module DLatch (
  input  data,
  input  write,
  input  reset,
  output out
);

  wire nand_1_out, nand_2_out, nand_3_out, nand_4_out, nand_6_out;

  nand nand_1 (nand_1_out, data, data);
  nand nand_2 (nand_2_out, data, write);
  nand nand_3 (nand_3_out, write, nand_1_out);
  nand nand_4 (nand_4_out, reset, reset);
  nand nand_5 (out, nand_2_out, nand_6_out);
  nand nand_6 (nand_6_out, out, nand_3_out, nand_4_out);
endmodule
module Reg4 (
  input  in0,
  input  in1,
  input  in2,
  input  in3,
  input  read,
  input  write,
  input  reset,
  output out0,
  output out1,
  output out2,
  output out3
);

  wire dlatch_1_out, dlatch_2_out, dlatch_3_out, dlatch_4_out;

  DLatch dlatch_1 (.data(in0), .write(write), .out(dlatch_1_out), .reset(reset));
  DLatch dlatch_2 (.data(in1), .write(write), .out(dlatch_2_out), .reset(reset));
  DLatch dlatch_3 (.data(in2), .write(write), .out(dlatch_3_out), .reset(reset));
  DLatch dlatch_4 (.data(in3), .write(write), .out(dlatch_4_out), .reset(reset));
  assign out0 = read ? dlatch_1_out : 1'bz;  // Controlled_Buffer controlled_buffer_1
  assign out1 = read ? dlatch_2_out : 1'bz;  // Controlled_Buffer controlled_buffer_2
  assign out2 = read ? dlatch_3_out : 1'bz;  // Controlled_Buffer controlled_buffer_3
  assign out3 = read ? dlatch_4_out : 1'bz;  // Controlled_Buffer controlled_buffer_4
endmodule

module Reg8 (
  input  read,
  input  write,
  input  reset,
  input  in0,
  input  in1,
  input  in2,
  input  in3,
  input  in4,
  input  in5,
  input  in6,
  input  in7,
  output out0,
  output out1,
  output out2,
  output out3,
  output out4,
  output out5,
  output out6,
  output out7
);

  Reg4 reg4_1 (
    .in0(in0), .in1(in1), .in2(in2), .in3(in3), .read(read), .write(write), .out0(out0), .out1(out1),
    .out2(out2), .out3(out3), .reset(reset));
  Reg4 reg4_2 (
    .in0(in4), .in1(in5), .in2(in6), .in3(in7), .read(read), .write(write), .out0(out4), .out1(out5),
    .out2(out6), .out3(out7), .reset(reset));
endmodule

module Ram256 (
  input  addr0,
  input  addr1,
  input  addr2,
  input  addr3,
  input  addr4,
  input  addr5,
  input  addr6,
  input  addr7,
  input  marw,
  input  read,
  input  write,
  input  clk,
  input  reset,
  input  in0,
  input  in1,
  input  in2,
  input  in3,
  input  in4,
  input  in5,
  input  in6,
  input  in7,
  output out0,
  output out1,
  output out2,
  output out3,
  output out4,
  output out5,
  output out6,
  output out7
);

  wire delayer_1_out, or_1_out;
  wire [7:0] MAR_out0;

  Reg8 MAR (
    .in0(addr0), .in1(addr1), .in2(addr2), .in3(addr3), .in4(addr4), .in5(addr5), .in6(addr6), .in7(addr7),
    .read(1'b1), .write(marw), .reset(reset), .out0(MAR_out0[0]), .out1(MAR_out0[1]), .out2(MAR_out0[2]),
    .out3(MAR_out0[3]), .out4(MAR_out0[4]), .out5(MAR_out0[5]), .out6(MAR_out0[6]), .out7(MAR_out0[7]));
  Delayer delayer_1 (.in(clk), .out(delayer_1_out));
  or or_1 (or_1_out, read, write);
  RAM #(.bus("separate")) ram_1 (
    .addr(MAR_out0), .din({in7, in6, in5, in4, in3, in2, in1, in0}),
    .data({out7, out6, out5, out4, out3, out2, out1, out0}), .str(write), .sel(or_1_out),
    .clk(delayer_1_out), .ld(read), .clr(reset));
endmodule

module LeftShifter8 (
  input  cin,
  input  in0,
  input  in1,
  input  in2,
  input  in3,
  input  in4,
  input  in5,
  input  in6,
  input  in7,
  output out0,
  output out1,
  output out2,
  output out3,
  output out4,
  output out6,
  output out6_2,
  output out7,
  output cout
);


  assign cout = in7;
  assign out0 = cin;
  assign out1 = in0;
  assign out2 = in1;
  assign out3 = in2;
  assign out4 = in3;
  assign out6 = in4;
  assign out6_2 = in5;
  assign out7 = in6;
endmodule

module RightShifter8 (
  input  in0,
  input  in1,
  input  in2,
  input  in3,
  input  in4,
  input  in5,
  input  in6,
  input  in7,
  input  cin,
  output cout,
  output out0,
  output out1,
  output out2,
  output out3,
  output out4,
  output out6,
  output out6_2,
  output out7
);


  assign cout = in0;
  assign out0 = in1;
  assign out1 = in2;
  assign out2 = in3;
  assign out3 = in4;
  assign out4 = in5;
  assign out6 = in6;
  assign out6_2 = in7;
  assign out7 = cin;
endmodule

module Ander8 (
  input  a0,
  input  b0,
  input  a1,
  input  b1,
  input  a2,
  input  b2,
  input  a3,
  input  b3,
  input  a4,
  input  b4,
  input  a5,
  input  b5,
  input  a6,
  input  b6,
  input  a7,
  input  b7,
  output out0,
  output out1,
  output out2,
  output out3,
  output out4,
  output out5,
  output out6,
  output out7
);

  and and_1 (out0, a0, b0);
  and and_2 (out1, a1, b1);
  and and_3 (out2, a2, b2);
  and and_4 (out3, a3, b3);
  and and_5 (out4, a4, b4);
  and and_6 (out5, a5, b5);
  and and_7 (out6, a6, b6);
  and and_8 (out7, a7, b7);
endmodule

module Orer8 (
  input  a0,
  input  b0,
  input  a1,
  input  b1,
  input  a2,
  input  b2,
  input  a3,
  input  b3,
  input  a4,
  input  b4,
  input  a5,
  input  b5,
  input  a6,
  input  b6,
  input  a7,
  input  b7,
  output out0,
  output out1,
  output out2,
  output out3,
  output out4,
  output out5,
  output out6,
  output out7
);

  or or_1 (out0, a0, b0);
  or or_2 (out1, a1, b1);
  or or_3 (out2, a2, b2);
  or or_4 (out3, a3, b3);
  or or_5 (out4, a4, b4);
  or or_6 (out5, a5, b5);
  or or_7 (out6, a6, b6);
  or or_8 (out7, a7, b7);
endmodule

module Xorer8 (
  input  a0,
  input  b0,
  input  a1,
  input  b1,
  input  a2,
  input  b2,
  input  a3,
  input  b3,
  input  a4,
  input  b4,
  input  a5,
  input  b5,
  input  a6,
  input  b6,
  input  a7,
  input  b7,
  output out0,
  output out1,
  output out2,
  output out3,
  output out4,
  output out5,
  output out6,
  output out7
);

  xor xor_1 (out0, a0, b0);
  xor xor_2 (out1, a1, b1);
  xor xor_3 (out2, a2, b2);
  xor xor_4 (out3, a3, b3);
  xor xor_5 (out4, a4, b4);
  xor xor_6 (out5, a5, b5);
  xor xor_7 (out6, a6, b6);
  xor xor_8 (out7, a7, b7);
endmodule

module FullAdder (
  input  a,
  input  b,
  input  cin,
  output sum,
  output cout
);

  wire and_1_out, and_2_out, xor_1_out;

  xor xor_1 (xor_1_out, a, b);
  xor xor_2 (sum, xor_1_out, cin);
  and and_1 (and_1_out, xor_1_out, cin);
  and and_2 (and_2_out, a, b);
  or or_1 (cout, and_1_out, and_2_out);
endmodule

module Adder8 (
  input  cin,
  input  a0,
  input  b0,
  input  a1,
  input  b1,
  input  a2,
  input  b2,
  input  a3,
  input  b3,
  input  a4,
  input  b4,
  input  a5,
  input  b5,
  input  a6,
  input  b6,
  input  a7,
  input  b7,
  output out0,
  output out1,
  output out2,
  output out3,
  output out4,
  output out5,
  output out6,
  output out7,
  output ovcarry,
  output cout
);

  wire fulladder_1_cout, fulladder_2_cout, fulladder_3_cout, fulladder_4_cout, fulladder_5_cout,
       fulladder_6_cout;

  FullAdder fulladder_1 (.a(a0), .b(b0), .cin(cin), .sum(out0), .cout(fulladder_1_cout));
  FullAdder fulladder_2 (.a(a1), .b(b1), .cin(fulladder_1_cout), .sum(out1), .cout(fulladder_2_cout));
  FullAdder fulladder_3 (.a(a2), .b(b2), .cin(fulladder_2_cout), .sum(out2), .cout(fulladder_3_cout));
  FullAdder fulladder_4 (.a(a3), .b(b3), .cin(fulladder_3_cout), .sum(out3), .cout(fulladder_4_cout));
  FullAdder fulladder_5 (.a(a4), .b(b4), .cin(fulladder_4_cout), .sum(out4), .cout(fulladder_5_cout));
  FullAdder fulladder_6 (.a(a5), .b(b5), .cin(fulladder_5_cout), .sum(out5), .cout(fulladder_6_cout));
  FullAdder fulladder_7 (.a(a6), .b(b6), .cin(fulladder_6_cout), .sum(out6), .cout(ovcarry));
  FullAdder fulladder_8 (.a(a7), .b(b7), .cin(ovcarry), .sum(out7), .cout(cout));
endmodule

module AddSub8 (
  input  sub,
  input  a0,
  input  b0,
  input  a1,
  input  b1,
  input  a2,
  input  b2,
  input  a3,
  input  b3,
  input  a4,
  input  b4,
  input  a5,
  input  b5,
  input  a6,
  input  b6,
  input  a7,
  input  b7,
  input  cin,
  output carry,
  output overflow,
  output out7,
  output out6,
  output out5,
  output out4,
  output out3,
  output out2,
  output out1,
  output out0
);

  wire adder8_1_cout, adder8_1_ovcarry, xor_3_out, xor_4_out, xor_5_out, xor_6_out, xor_7_out, xor_8_out,
       xor_9_out, xor_10_out, xor_11_out;

  xor xor_1 (carry, sub, adder8_1_cout);
  xor xor_2 (overflow, adder8_1_ovcarry, adder8_1_cout);
  xor xor_3 (xor_3_out, sub, b0);
  xor xor_4 (xor_4_out, sub, b1);
  xor xor_5 (xor_5_out, sub, b2);
  xor xor_6 (xor_6_out, sub, b3);
  xor xor_7 (xor_7_out, sub, b4);
  xor xor_8 (xor_8_out, sub, b5);
  xor xor_9 (xor_9_out, sub, b6);
  xor xor_10 (xor_10_out, sub, b7);
  Adder8 adder8_1 (
    .cin(xor_11_out), .a0(a0), .b0(xor_3_out), .a1(a1), .b1(xor_4_out), .a2(a2), .b2(xor_5_out), .a3(a3),
    .b3(xor_6_out), .a4(a4), .b4(xor_7_out), .a5(a5), .b5(xor_8_out), .a6(a6), .b6(xor_9_out), .a7(a7),
    .b7(xor_10_out), .out0(out0), .out1(out1), .out2(out2), .out3(out3), .out4(out4), .out5(out5),
    .out6(out6), .out7(out7), .ovcarry(adder8_1_ovcarry), .cout(adder8_1_cout));
  xor xor_11 (xor_11_out, sub, cin);
endmodule

module Bus0Gate (
  input  in7,
  input  in6,
  input  in5,
  input  in4,
  input  in3,
  input  in2,
  input  in1,
  input  in0,
  input  _0_bus,
  output out7,
  output out6,
  output out5,
  output out4,
  output out3,
  output out2,
  output out1,
  output out0
);

  and and_1 (out6, in6, _0_bus);
  and and_2 (out7, in7, _0_bus);
  and and_3 (out4, in4, _0_bus);
  and and_4 (out5, in5, _0_bus);
  and and_5 (out1, in1, _0_bus);
  and and_6 (out2, in2, _0_bus);
  and and_7 (out3, in3, _0_bus);
  and and_8 (out0, in0, _0_bus);
endmodule

module ALU (
  input  a7,
  input  a6,
  input  a5,
  input  a4,
  input  a3,
  input  a2,
  input  a1,
  input  a0,
  input  b7,
  input  b6,
  input  b5,
  input  b4,
  input  b3,
  input  b2,
  input  b1,
  input  b0,
  input  op2,
  input  op1,
  input  op0,
  input  cin,
  output out0,
  output out1,
  output out2,
  output out3,
  output out4,
  output out5,
  output out6,
  output out7,
  output overflow,
  output carry,
  output sign,
  output zero
);

  wire addsub8_1_carry, addsub8_1_out0, addsub8_1_out1, addsub8_1_out2, addsub8_1_out3, addsub8_1_out4,
       addsub8_1_out5, addsub8_1_out6, addsub8_1_out7, addsub8_1_overflow, ander8_1_out0, ander8_1_out1,
       ander8_1_out2, ander8_1_out3, ander8_1_out4, ander8_1_out5, ander8_1_out6, ander8_1_out7,
       leftshifter8_1_cout, leftshifter8_1_out0, leftshifter8_1_out1, leftshifter8_1_out2,
       leftshifter8_1_out3, leftshifter8_1_out4, leftshifter8_1_out6, leftshifter8_1_out6_2,
       leftshifter8_1_out7, nor_2_out, or_1_out, orer8_1_out0, orer8_1_out1, orer8_1_out2, orer8_1_out3,
       orer8_1_out4, orer8_1_out5, orer8_1_out6, orer8_1_out7, rightshifter8_1_cout, rightshifter8_1_out0,
       rightshifter8_1_out1, rightshifter8_1_out2, rightshifter8_1_out3, rightshifter8_1_out4,
       rightshifter8_1_out6, rightshifter8_1_out6_2, rightshifter8_1_out7, xorer8_1_out0, xorer8_1_out1,
       xorer8_1_out2, xorer8_1_out3, xorer8_1_out4, xorer8_1_out5, xorer8_1_out6, xorer8_1_out7;
  wire [7:0] decoder_1_out0;

  Ander8 ander8_1 (
    .a0(a0), .b0(b0), .a1(a1), .b1(b1), .a2(a2), .b2(b2), .a3(a3), .b3(b3), .a4(a4), .b4(b4), .a5(a5),
    .b5(b5), .a6(a6), .b6(b6), .a7(a7), .b7(b7), .out0(ander8_1_out0), .out1(ander8_1_out1),
    .out2(ander8_1_out2), .out3(ander8_1_out3), .out4(ander8_1_out4), .out5(ander8_1_out5),
    .out6(ander8_1_out6), .out7(ander8_1_out7));
  Orer8 orer8_1 (
    .a0(a0), .b0(b0), .a1(a1), .b1(b1), .a2(a2), .b2(b2), .a3(a3), .b3(b3), .a4(a4), .b4(b4), .a5(a5),
    .b5(b5), .a6(a6), .b6(b6), .a7(a7), .b7(b7), .out0(orer8_1_out0), .out1(orer8_1_out1),
    .out2(orer8_1_out2), .out3(orer8_1_out3), .out4(orer8_1_out4), .out5(orer8_1_out5), .out6(orer8_1_out6),
    .out7(orer8_1_out7));
  Xorer8 xorer8_1 (
    .a0(a0), .b0(b0), .a1(a1), .b1(b1), .a2(a2), .b2(b2), .a3(a3), .b3(b3), .a4(a4), .b4(b4), .a5(a5),
    .b5(b5), .a6(a6), .b6(b6), .a7(a7), .b7(b7), .out0(xorer8_1_out0), .out1(xorer8_1_out1),
    .out2(xorer8_1_out2), .out3(xorer8_1_out3), .out4(xorer8_1_out4), .out5(xorer8_1_out5),
    .out6(xorer8_1_out6), .out7(xorer8_1_out7));
  AddSub8 addsub8_1 (
    .cin(cin), .a0(a0), .b0(b0), .a1(a1), .b1(b1), .a2(a2), .b2(b2), .a3(a3), .b3(b3), .a4(a4), .b4(b4),
    .a5(a5), .b5(b5), .a6(a6), .b6(b6), .a7(a7), .b7(b7), .out0(addsub8_1_out0), .out1(addsub8_1_out1),
    .out2(addsub8_1_out2), .out3(addsub8_1_out3), .out4(addsub8_1_out4), .out5(addsub8_1_out5),
    .out6(addsub8_1_out6), .out7(addsub8_1_out7), .carry(addsub8_1_carry), .sub(decoder_1_out0[5]),
    .overflow(addsub8_1_overflow));
  LeftShifter8 leftshifter8_1 (
    .cin(cin), .in0(a0), .in1(a1), .in2(a2), .in3(a3), .in4(a4), .in5(a5), .in6(a6), .in7(a7),
    .out0(leftshifter8_1_out0), .out1(leftshifter8_1_out1), .out2(leftshifter8_1_out2),
    .out3(leftshifter8_1_out3), .out4(leftshifter8_1_out4), .out6(leftshifter8_1_out6),
    .out6_2(leftshifter8_1_out6_2), .out7(leftshifter8_1_out7), .cout(leftshifter8_1_cout));
  RightShifter8 rightshifter8_1 (
    .in0(a0), .in1(a1), .in2(a2), .in3(a3), .in4(a4), .in5(a5), .in6(a6), .in7(a7), .cin(cin),
    .cout(rightshifter8_1_cout), .out0(rightshifter8_1_out0), .out1(rightshifter8_1_out1),
    .out2(rightshifter8_1_out2), .out3(rightshifter8_1_out3), .out4(rightshifter8_1_out4),
    .out6(rightshifter8_1_out6), .out6_2(rightshifter8_1_out6_2), .out7(rightshifter8_1_out7));
  Decoder #(.select(3), .enable("false")) decoder_1 (
    .out0(decoder_1_out0[0]), .out1(decoder_1_out0[1]), .out2(decoder_1_out0[2]), .out3(decoder_1_out0[3]),
    .out4(decoder_1_out0[4]), .out5(decoder_1_out0[5]), .out6(decoder_1_out0[6]), .out7(decoder_1_out0[7]),
    .sel({op2, op1, op0}));
  EN8x1x8 en8x1x8_1 (
    .in0(a0), .in1(a1), .in2(a2), .in3(a3), .in4(a4), .in5(a5), .in6(a6), .in7(a7), .en(decoder_1_out0[0]),
    .out0(out0), .out1(out1), .out2(out2), .out3(out3), .out4(out4), .out6(out5), .out6_2(out6), .out7(out7));
  EN8x1x8 en8x1x8_2 (
    .in0(ander8_1_out0), .in1(ander8_1_out1), .in2(ander8_1_out2), .in3(ander8_1_out3), .in4(ander8_1_out4),
    .in5(ander8_1_out5), .in6(ander8_1_out6), .in7(ander8_1_out7), .en(decoder_1_out0[1]), .out0(out0),
    .out1(out1), .out2(out2), .out3(out3), .out4(out4), .out6(out5), .out6_2(out6), .out7(out7));
  EN8x1x8 en8x1x8_3 (
    .in0(orer8_1_out0), .in1(orer8_1_out1), .in2(orer8_1_out2), .in3(orer8_1_out3), .in4(orer8_1_out4),
    .in5(orer8_1_out5), .in6(orer8_1_out6), .in7(orer8_1_out7), .en(decoder_1_out0[2]), .out0(out0),
    .out1(out1), .out2(out2), .out3(out3), .out4(out4), .out6(out5), .out6_2(out6), .out7(out7));
  EN8x1x8 en8x1x8_4 (
    .in0(xorer8_1_out0), .in1(xorer8_1_out1), .in2(xorer8_1_out2), .in3(xorer8_1_out3), .in4(xorer8_1_out4),
    .in5(xorer8_1_out5), .in6(xorer8_1_out6), .in7(xorer8_1_out7), .en(decoder_1_out0[3]), .out0(out0),
    .out1(out1), .out2(out2), .out3(out3), .out4(out4), .out6(out5), .out6_2(out6), .out7(out7));
  or or_1 (or_1_out, decoder_1_out0[4], decoder_1_out0[5]);
  EN8x1x8 en8x1x8_5 (
    .in0(addsub8_1_out0), .in1(addsub8_1_out1), .in2(addsub8_1_out2), .in3(addsub8_1_out3),
    .in4(addsub8_1_out4), .in5(addsub8_1_out5), .in6(addsub8_1_out6), .in7(addsub8_1_out7), .en(or_1_out),
    .out0(out0), .out1(out1), .out2(out2), .out3(out3), .out4(out4), .out6(out5), .out6_2(out6), .out7(out7));
  EN8x1x8 en8x1x8_6 (
    .in0(leftshifter8_1_out0), .in1(leftshifter8_1_out1), .in2(leftshifter8_1_out2),
    .in3(leftshifter8_1_out3), .in4(leftshifter8_1_out4), .in5(leftshifter8_1_out6),
    .in6(leftshifter8_1_out6_2), .in7(leftshifter8_1_out7), .en(decoder_1_out0[6]), .out0(out0), .out1(out1),
    .out2(out2), .out3(out3), .out4(out4), .out6(out5), .out6_2(out6), .out7(out7));
  EN8x1x8 en8x1x8_7 (
    .in0(rightshifter8_1_out0), .in1(rightshifter8_1_out1), .in2(rightshifter8_1_out2),
    .in3(rightshifter8_1_out3), .in4(rightshifter8_1_out4), .in5(rightshifter8_1_out6),
    .in6(rightshifter8_1_out6_2), .in7(rightshifter8_1_out7), .en(decoder_1_out0[7]), .out0(out0),
    .out1(out1), .out2(out2), .out3(out3), .out4(out4), .out6(out5), .out6_2(out6), .out7(out7));
  nor nor_1 (zero, out7, out6, out5, out4, out3, out2, out1, out0);
  Multiplexer #(.enable("false")) multiplexer_1 (.in0(1'b0), .in1(addsub8_1_overflow), .out(overflow), .sel(or_1_out));
  nor nor_2 (nor_2_out, or_1_out, decoder_1_out0[6], decoder_1_out0[7]);
  assign carry = nor_2_out ? 1'b0 : 1'bz;  // Controlled_Buffer controlled_buffer_1
  assign carry = or_1_out ? addsub8_1_carry : 1'bz;  // Controlled_Buffer controlled_buffer_2
  assign carry = decoder_1_out0[6] ? leftshifter8_1_cout : 1'bz;  // Controlled_Buffer controlled_buffer_3
  assign carry = decoder_1_out0[7] ? rightshifter8_1_cout : 1'bz;  // Controlled_Buffer controlled_buffer_4

  assign sign = out7;
endmodule

module Clock (
  input  clk,
  input  rst,
  output clk_r,
  output clk_w
);

  wire j_k_ff_1_q, j_k_ff_1_qn, nand_1_out, nand_2_out, not_1_out;

  not not_1 (not_1_out, clk);
  nand nand_1 (nand_1_out, clk, j_k_ff_1_q);
  J_K_Flip_Flop j_k_ff_1 (
    .J(1'b1), .clk(not_1_out), .K(1'b1), .Q(j_k_ff_1_q), .Qn(j_k_ff_1_qn), .preset(rst), .en(1'b1),
    .reset(1'b0));
  nand nand_2 (nand_2_out, j_k_ff_1_qn, clk);
  buf buffer_1 (clk_r, nand_1_out);
  not not_2 (clk_w, nand_2_out);
endmodule

module Delayer (
  input  in,
  output out
);

  wire not_1_out, not_2_out, not_3_out, not_4_out, not_5_out, not_6_out, not_7_out;

  not not_1 (not_1_out, not_2_out);
  not not_2 (not_2_out, in);
  not not_3 (not_3_out, not_5_out);
  not not_4 (not_4_out, not_3_out);
  not not_5 (not_5_out, not_1_out);
  not not_6 (not_6_out, not_7_out);
  not not_7 (not_7_out, not_4_out);
  not not_8 (out, not_6_out);
endmodule

module BranchChecker (
  input  zero,
  input  sign,
  input  carry,
  input  overflow,
  input  op2,
  input  op1,
  input  op0,
  output result
);

  wire and_1_out, and_2_out, and_3_out, and_4_out, and_5_out, and_6_out, and_7_out, decoder_1_out0,
       decoder_1_out1, decoder_1_out2, decoder_1_out3, decoder_1_out4, decoder_1_out5, decoder_1_out6,
       decoder_1_out7, or_1_out, or_2_out, xor_1_out;

  Decoder #(.select(3), .enable("false")) decoder_1 (
    .out0(decoder_1_out0), .out1(decoder_1_out1), .out2(decoder_1_out2), .out3(decoder_1_out3),
    .out4(decoder_1_out4), .out5(decoder_1_out5), .out6(decoder_1_out6), .out7(decoder_1_out7),
    .sel({op2, op1, op0}));
  or or_1 (or_1_out, zero, xor_1_out);
  xor xor_1 (xor_1_out, overflow, sign);
  or or_2 (or_2_out, carry, zero);
  and and_1 (and_1_out, decoder_1_out1, zero);
  and and_2 (and_2_out, decoder_1_out2, sign);
  and and_3 (and_3_out, decoder_1_out3, overflow);
  and and_4 (and_4_out, decoder_1_out4, carry);
  and and_5 (and_5_out, decoder_1_out5, or_2_out);
  and and_6 (and_6_out, decoder_1_out6, xor_1_out);
  and and_7 (and_7_out, decoder_1_out7, or_1_out);
  or or_3 (result, and_7_out, and_6_out, and_5_out, and_4_out, and_3_out, and_2_out, and_1_out, decoder_1_out0);
endmodule

module ControlUnit (
  input  rst,
  input  zero,
  input  sign,
  input  carry,
  input  overflow,
  input  clk,
  input  ir7,
  input  ir6,
  input  ir5,
  input  ir4,
  input  ir3,
  input  ir2,
  input  ir1,
  input  ir0,
  output rd_r,
  output ra_w,
  output rb_w,
  output bus_0,
  output io,
  output io_in_out,
  output io_data_addr,
  output rx_r,
  output rx_w,
  output fr_w,
  output rx1,
  output pc_w,
  output rx0,
  output pc_r,
  output ir_w,
  output cin,
  output mar_w,
  output op2,
  output ram_w,
  output op1,
  output op0,
  output ram_r,
  output halt,
  output new_cycle,
  output new_instr
);

  wire and_10_out, and_13_out, and_14_out, and_15_out, branchchecker_1_result, clock_1_clk_r, clock_1_clk_w,
       delayer_1_out, instr_state_qn, or_1_out, or_2_out, or_3_out;
  wire [1:0] multiplexer_2_out, multiplexer_3_out;
  wire [6:0] adder_1_out, mPC_q, multiplexer_1_out, rom_1_data;
  wire [6:6] instr_state_q;
  wire [31:4] rom_1_data_2;

  and and_1 (fr_w, rom_1_data_2[12], clock_1_clk_w);
  and and_2 (pc_w, rom_1_data_2[13], clock_1_clk_w);
  and and_3 (pc_r, rom_1_data_2[14], clock_1_clk_r);
  and and_4 (ir_w, rom_1_data_2[15], clock_1_clk_w);
  and and_5 (mar_w, rom_1_data_2[16], clock_1_clk_w);
  and and_6 (ram_w, rom_1_data_2[17], clock_1_clk_w);
  and and_7 (ram_r, rom_1_data_2[18], clock_1_clk_r);
  Clock clock_1 (.clk_r(clock_1_clk_r), .clk(clk), .clk_w(clock_1_clk_w), .rst(or_1_out));
  nor nor_1 (new_cycle, clock_1_clk_r, clock_1_clk_w);
  or or_1 (or_1_out, rst, halt);
  and and_8 (ra_w, clock_1_clk_w, rom_1_data_2[10]);
  and and_9 (rd_r, clock_1_clk_r, rom_1_data_2[11]);
  Register #(.width(7)) mPC (.D(multiplexer_1_out), .en(1'b1), .Q(mPC_q), .clk(new_cycle), .clr(or_1_out));
  Multiplexer #(.select(2), .width(7), .enable("false")) multiplexer_1 (
    .in0(adder_1_out), .in1(adder_1_out), .in2(rom_1_data),
    .in3({instr_state_q[6], ir7, ir6, ir5, ir4, 2'b00}), .out(multiplexer_1_out), .sel(multiplexer_2_out));
  and and_10 (and_10_out, clock_1_clk_w, rom_1_data_2[31]);
  and and_11 (rb_w, clock_1_clk_w, rom_1_data_2[9]);
  Delayer delayer_1 (.in(new_cycle), .out(delayer_1_out));
  and and_12 (new_instr, delayer_1_out, and_13_out);
  and and_13 (and_13_out, ~mPC_q[6], ~mPC_q[5], ~mPC_q[4], ~mPC_q[3], ~mPC_q[2], ~mPC_q[1], mPC_q[0]);  // AND_Gate
  Adder #(.width(7)) adder_1 (.a(mPC_q), .b({7{1'b0}}), .out(adder_1_out), .cin(1'b1));  // open: cout
  D_Flip_Flop instr_state (
    .clk(and_10_out), .D(instr_state_qn), .Q(instr_state_q[6]), .Qn(instr_state_qn), .en(1'b1),
    .reset(or_1_out));  // open: preset
  ROM #(.addrWidth(7), .dataWidth(32)) rom_1 (
    .addr(mPC_q),
    .data({rom_1_data_2[31:27], rom_1_data, halt, rom_1_data_2[18:9], bus_0, io, rom_1_data_2[6:4], cin, op2, op1, op0}),
    .sel(1'b1));
  Multiplexer #(.select(2), .width(2), .enable("false")) multiplexer_2 (
    .in0(2'b00), .in1(multiplexer_3_out), .in2(2'b10), .in3(2'b11), .out(multiplexer_2_out),
    .sel(rom_1_data_2[29:28]));
  and and_14 (and_14_out, ir3, io);
  and and_15 (and_15_out, io, ~ir3);  // AND_Gate
  BranchChecker branchchecker_1 (
    .zero(zero), .sign(sign), .carry(carry), .overflow(overflow), .op0(ir0), .op1(ir1), .op2(ir2),
    .result(branchchecker_1_result));
  Multiplexer #(.width(2), .enable("false")) multiplexer_3 (
    .in0(2'b00), .in1(2'b10), .out(multiplexer_3_out), .sel(branchchecker_1_result));
  or or_2 (or_2_out, rom_1_data_2[6], and_15_out);
  or or_3 (or_3_out, rom_1_data_2[5], and_14_out);
  Multiplexer #(.width(2), .enable("false")) multiplexer_4 (
    .in0({ir3, ir2}), .in1({ir1, ir0}), .out({rx1, rx0}), .sel(rom_1_data_2[4]));
  and and_16 (rx_r, clock_1_clk_r, or_2_out);
  and and_17 (rx_w, clock_1_clk_w, or_3_out);

  assign io_data_addr = ir2;
  assign io_in_out = ir3;

  // Notes on the sheet:
  //   Map instructions to 1xxxx00 with xxxx=OPCODE
  //   to avoid collision with IFETCH.
  //   Instructions must complete in 4 steps.
  //   0x00 has no instruction since after reset it won't be executed.
  //   00xy -> jump to addr mPC+1
  //   01xy -> branch to either addr mPC+1 or ROM[mPC]
  //   10xy -> jump to addr ROM[mPC]
  //   11xy -> jump to instr in IR
  //   contents of rom_1 (hex, n*v repeats v):
  //   0 14700 280c b0048000 60*0 450 a0100820 0 0 14700 280c a0140030 0 10050 a0140020 0 0 10050 a0120040
  //   0 0 4400 2050 a0100830 0 15614400 a0102b0c 40200 a0102804 a0080000 0 0 0 a0100000 0 0 0 440 250
  //   a0101824 0 440 250 a0101825 0 450 a0101826 0 0 450 a0101827 0 0 440 250 a0101821 0 440 250 a0101822
  //   0 440 250 a0101823 0 440 a0101255
endmodule

module CPU_2 (
  input  in_1,
  input  in_2,
  input  in_3,
  input  in_4,
  input  in_5,
  input  in_6,
  input  in_7,
  input  in_8,
  input  MANUAL,
  input  in_10,
  input  in_11,
  input  in_12,
  input  in_13,
  input  in_14,
  input  in_15,
  input  in_16,
  input  in_17,
  output out_18,
  output out_19,
  output out_20,
  output out_21,
  output out_22,
  output out_23,
  output out_24,
  output out_25
);

  wire ADDR_out, alu_1_carry, alu_1_out0, alu_1_out1, alu_1_out2, alu_1_out3, alu_1_out4, alu_1_out5,
       alu_1_out6, alu_1_out7, alu_1_overflow, alu_1_sign, alu_1_zero, and_1_out, and_2_out, and_3_out,
       and_4_out, and_5_out, and_6_out, and_7_out, and_8_out, and_9_out, and_10_out, and_11_out, and_12_out,
       bus0gate_1_out0, bus0gate_1_out1, bus0gate_1_out2, bus0gate_1_out3, bus0gate_1_out4, bus0gate_1_out5,
       bus0gate_1_out6, bus0gate_1_out7, CLOCK_out, controlled_buffer_1_out, controlled_buffer_2_out,
       controlunit_1_bus_0, controlunit_1_cin, controlunit_1_fr_w, controlunit_1_halt, controlunit_1_ir_w,
       controlunit_1_mar_w, controlunit_1_new_cycle, controlunit_1_new_instr, controlunit_1_op0,
       controlunit_1_op1, controlunit_1_op2, controlunit_1_pc_r, controlunit_1_pc_w, controlunit_1_ra_w,
       controlunit_1_ram_r, controlunit_1_ram_w, controlunit_1_rb_w, controlunit_1_rd_r, controlunit_1_rx_r,
       controlunit_1_rx_w, decoder_1_out0, decoder_1_out1, decoder_1_out2, decoder_1_out3, FR_out0, FR_out1,
       FR_out2, FR_out3, HALT_2_q, HALT_2_qn, LDR_out, not_1_out, not_2_out, not_3_out, not_4_out, or_1_out,
       or_2_out, or_3_out, or_4_out, or_5_out, or_6_out, or_7_out, RA_out0, RA_out1, RA_out2, RA_out3,
       RA_out4, RA_out5, RA_out6, RA_out7, RB_out0, RB_out1, RB_out2, RB_out3, RB_out4, RB_out5, RB_out6,
       RB_out7, RESET_3_out, RESET_out, RESUME_out, STEP_out, STR_out;
  wire [1:0] controlunit_1_rx0;
  wire [3:0] CYCLES_q, CYCLES_q_2;
  wire [7:0] INSTR_q, IR_out0;

  ALU alu_1 (
    .a7(RA_out7), .a6(RA_out6), .a5(RA_out5), .a4(RA_out4), .a3(RA_out3), .a2(RA_out2), .a1(RA_out1),
    .a0(RA_out0), .b7(RB_out7), .b6(RB_out6), .b5(RB_out5), .b4(RB_out4), .b3(RB_out3), .b2(RB_out2),
    .b1(RB_out1), .b0(RB_out0), .cin(controlunit_1_cin), .op2(controlunit_1_op2), .op1(controlunit_1_op1),
    .op0(controlunit_1_op0), .out0(alu_1_out0), .out1(alu_1_out1), .out2(alu_1_out2), .out3(alu_1_out3),
    .out4(alu_1_out4), .out5(alu_1_out5), .out6(alu_1_out6), .out7(alu_1_out7), .overflow(alu_1_overflow),
    .sign(alu_1_sign), .zero(alu_1_zero), .carry(alu_1_carry));
  Button RESET (.out(RESET_out));
  LED Reset_2 (.in(RESET_out));
  Button RESUME (.out(RESUME_out));
  not not_1 (not_1_out, MANUAL);
  assign controlled_buffer_1_out = MANUAL ? STEP_out : 1'bz;  // Controlled_Buffer controlled_buffer_1
  Button STEP (.out(STEP_out));
  Clock_part CLOCK (.out(CLOCK_out));
  Pull_Resistor pull_resistor_1 (.node(controlled_buffer_1_out));
  Reg8 RA (
    .in0(out_25), .in1(out_24), .in2(out_23), .in3(out_22), .in4(out_21), .in5(out_20), .in6(out_19),
    .in7(out_18), .read(1'b1), .write(controlunit_1_ra_w), .reset(RESET_out), .out0(RA_out0), .out1(RA_out1),
    .out2(RA_out2), .out3(RA_out3), .out4(RA_out4), .out5(RA_out5), .out6(RA_out6), .out7(RA_out7));
  LED u_Manual (.in(MANUAL));
  LED Auto (.in(not_2_out));
  not not_2 (not_2_out, MANUAL);
  or or_1 (or_1_out, controlled_buffer_1_out, controlled_buffer_2_out);
  assign controlled_buffer_2_out = not_1_out ? CLOCK_out : 1'bz;  // Controlled_Buffer controlled_buffer_2
  Pull_Resistor pull_resistor_2 (.node(controlled_buffer_2_out));
  Reg8 RB (
    .in0(bus0gate_1_out0), .in1(bus0gate_1_out1), .in2(bus0gate_1_out2), .in3(bus0gate_1_out3),
    .in4(bus0gate_1_out4), .in5(bus0gate_1_out5), .in6(bus0gate_1_out6), .in7(bus0gate_1_out7), .read(1'b1),
    .write(controlunit_1_rb_w), .reset(RESET_out), .out0(RB_out0), .out1(RB_out1), .out2(RB_out2),
    .out3(RB_out3), .out4(RB_out4), .out5(RB_out5), .out6(RB_out6), .out7(RB_out7));
  Reg8 RD (
    .in0(alu_1_out0), .in1(alu_1_out1), .in2(alu_1_out2), .in3(alu_1_out3), .in4(alu_1_out4),
    .in5(alu_1_out5), .in6(alu_1_out6), .in7(alu_1_out7), .read(controlunit_1_rd_r), .write(1'b1),
    .reset(RESET_out), .out0(out_25), .out1(out_24), .out2(out_23), .out3(out_22), .out4(out_21),
    .out5(out_20), .out6(out_19), .out7(out_18));
  LED Clock_2 (.in(or_1_out));
  LED Halt (.in(HALT_2_q));
  not not_3 (not_3_out, not_2_out);
  not not_4 (not_4_out, controlunit_1_bus_0);
  Bus0Gate bus0gate_1 (
    .in7(out_18), .in6(out_19), .in5(out_20), .in4(out_21), .in3(out_22), .in2(out_23), .in1(out_24),
    .in0(out_25), ._0_bus(not_4_out), .out7(bus0gate_1_out7), .out6(bus0gate_1_out6), .out5(bus0gate_1_out5),
    .out4(bus0gate_1_out4), .out3(bus0gate_1_out3), .out2(bus0gate_1_out2), .out1(bus0gate_1_out1),
    .out0(bus0gate_1_out0));
  and and_1 (and_1_out, ~HALT_2_q, or_1_out);  // AND_Gate
  Reg4 FR (
    .in0(alu_1_zero), .in1(alu_1_sign), .in2(alu_1_carry), .in3(alu_1_overflow), .read(1'b1),
    .write(controlunit_1_fr_w), .out0(FR_out0), .out1(FR_out1), .out2(FR_out2), .out3(FR_out3),
    .reset(RESET_out));
  ControlUnit controlunit_1 (
    .op0(controlunit_1_op0), .op1(controlunit_1_op1), .op2(controlunit_1_op2), .fr_w(controlunit_1_fr_w),
    .mar_w(controlunit_1_mar_w), .ram_r(controlunit_1_ram_r), .ram_w(controlunit_1_ram_w), .carry(FR_out2),
    .sign(FR_out1), .zero(FR_out0), .ra_w(controlunit_1_ra_w), .rb_w(controlunit_1_rb_w),
    .bus_0(controlunit_1_bus_0), .rx_r(controlunit_1_rx_r), .rx_w(controlunit_1_rx_w), .clk(and_1_out),
    .rst(RESET_out), .rd_r(controlunit_1_rd_r), .ir0(IR_out0[0]), .ir1(IR_out0[1]), .ir2(IR_out0[2]),
    .ir3(IR_out0[3]), .ir4(IR_out0[4]), .ir5(IR_out0[5]), .ir6(IR_out0[6]), .ir7(IR_out0[7]),
    .ir_w(controlunit_1_ir_w), .pc_w(controlunit_1_pc_w), .pc_r(controlunit_1_pc_r), .overflow(FR_out3),
    .halt(controlunit_1_halt), .cin(controlunit_1_cin), .new_instr(controlunit_1_new_instr),
    .new_cycle(controlunit_1_new_cycle), .rx0(controlunit_1_rx0[0]), .rx1(controlunit_1_rx0[1]));  // open: io_in_out, io_data_addr, io
  D_Flip_Flop HALT_2 (
    .clk(controlunit_1_halt), .D(HALT_2_qn), .Q(HALT_2_q), .Qn(HALT_2_qn), .en(1'b1), .reset(or_2_out));  // open: preset
  or or_2 (or_2_out, RESUME_out, RESET_out);
  Reg8 R0 (
    .in0(out_25), .in1(out_24), .in2(out_23), .in3(out_22), .in4(out_21), .in5(out_20), .in6(out_19),
    .in7(out_18), .read(and_2_out), .write(and_3_out), .reset(RESET_out), .out0(out_25), .out1(out_24),
    .out2(out_23), .out3(out_22), .out4(out_21), .out5(out_20), .out6(out_19), .out7(out_18));
  and and_2 (and_2_out, controlunit_1_rx_r, decoder_1_out0);
  Decoder #(.select(2), .enable("false")) decoder_1 (
    .out0(decoder_1_out0), .out1(decoder_1_out1), .out2(decoder_1_out2), .out3(decoder_1_out3),
    .sel(controlunit_1_rx0));
  Counter #(.trigger("falling")) INSTR (
    .load(1'b0), .count(1'b1), .Q(INSTR_q), .clk(controlunit_1_new_instr), .clr(RESET_out));  // open: D, carry
  Hex_Digit_Display hex_digit_display_1 (.value(INSTR_q[7:4]));  // open: dp
  Hex_Digit_Display hex_digit_display_2 (.value(INSTR_q[3:0]));  // open: dp
  and and_3 (and_3_out, decoder_1_out0, controlunit_1_rx_w);
  Counter CYCLES (
    .load(1'b0), .count(1'b1), .Q({CYCLES_q_2, CYCLES_q}), .clk(controlunit_1_new_cycle), .clr(or_3_out));  // open: D, carry
  or or_3 (or_3_out, controlunit_1_new_instr, RESET_out);
  Hex_Digit_Display hex_digit_display_3 (.value(CYCLES_q_2));  // open: dp
  Reg8 IR (
    .in0(out_25), .in1(out_24), .in2(out_23), .in3(out_22), .in4(out_21), .in5(out_20), .in6(out_19),
    .in7(out_18), .read(1'b1), .write(controlunit_1_ir_w), .reset(RESET_out), .out0(IR_out0[0]),
    .out1(IR_out0[1]), .out2(IR_out0[2]), .out3(IR_out0[3]), .out4(IR_out0[4]), .out5(IR_out0[5]),
    .out6(IR_out0[6]), .out7(IR_out0[7]));
  Hex_Digit_Display hex_digit_display_4 (.value(CYCLES_q));  // open: dp
  Reg8 R1 (
    .in0(out_25), .in1(out_24), .in2(out_23), .in3(out_22), .in4(out_21), .in5(out_20), .in6(out_19),
    .in7(out_18), .read(and_4_out), .write(and_5_out), .reset(RESET_out), .out0(out_25), .out1(out_24),
    .out2(out_23), .out3(out_22), .out4(out_21), .out5(out_20), .out6(out_19), .out7(out_18));
  and and_4 (and_4_out, controlunit_1_rx_r, decoder_1_out1);
  and and_5 (and_5_out, decoder_1_out1, controlunit_1_rx_w);
  and and_6 (and_6_out, not_3_out, LDR_out);
  and and_7 (and_7_out, ADDR_out, not_3_out);
  Button LDR (.out(LDR_out));
  Button ADDR (.out(ADDR_out));
  Reg8 R2 (
    .in0(out_25), .in1(out_24), .in2(out_23), .in3(out_22), .in4(out_21), .in5(out_20), .in6(out_19),
    .in7(out_18), .read(and_8_out), .write(and_10_out), .reset(RESET_out), .out0(out_25), .out1(out_24),
    .out2(out_23), .out3(out_22), .out4(out_21), .out5(out_20), .out6(out_19), .out7(out_18));
  and and_8 (and_8_out, controlunit_1_rx_r, decoder_1_out2);
  Reg8 PC (
    .in0(out_25), .in1(out_24), .in2(out_23), .in3(out_22), .in4(out_21), .in5(out_20), .in6(out_19),
    .in7(out_18), .read(controlunit_1_pc_r), .write(controlunit_1_pc_w), .reset(RESET_out), .out0(out_25),
    .out1(out_24), .out2(out_23), .out3(out_22), .out4(out_21), .out5(out_20), .out6(out_19), .out7(out_18));
  and and_9 (and_9_out, not_3_out, STR_out);
  Button STR (.out(STR_out));
  and and_10 (and_10_out, decoder_1_out2, controlunit_1_rx_w);
  assign out_19 = and_7_out ? in_2 : 1'bz;  // Controlled_Buffer controlled_buffer_3
  assign out_18 = and_7_out ? in_1 : 1'bz;  // Controlled_Buffer controlled_buffer_4
  assign out_21 = and_7_out ? in_4 : 1'bz;  // Controlled_Buffer controlled_buffer_5
  assign out_20 = and_7_out ? in_3 : 1'bz;  // Controlled_Buffer controlled_buffer_6
  assign out_20 = and_9_out ? in_12 : 1'bz;  // Controlled_Buffer controlled_buffer_7
  assign out_21 = and_9_out ? in_13 : 1'bz;  // Controlled_Buffer controlled_buffer_8
  assign out_19 = and_9_out ? in_11 : 1'bz;  // Controlled_Buffer controlled_buffer_9
  assign out_18 = and_9_out ? in_10 : 1'bz;  // Controlled_Buffer controlled_buffer_10
  assign out_25 = and_7_out ? in_8 : 1'bz;  // Controlled_Buffer controlled_buffer_11
  assign out_22 = and_7_out ? in_5 : 1'bz;  // Controlled_Buffer controlled_buffer_12
  assign out_24 = and_7_out ? in_7 : 1'bz;  // Controlled_Buffer controlled_buffer_13
  assign out_23 = and_7_out ? in_6 : 1'bz;  // Controlled_Buffer controlled_buffer_14
  assign out_23 = and_9_out ? in_15 : 1'bz;  // Controlled_Buffer controlled_buffer_15
  assign out_24 = and_9_out ? in_16 : 1'bz;  // Controlled_Buffer controlled_buffer_16
  assign out_22 = and_9_out ? in_14 : 1'bz;  // Controlled_Buffer controlled_buffer_17
  assign out_25 = and_9_out ? in_17 : 1'bz;  // Controlled_Buffer controlled_buffer_18
  Reg8 R3 (
    .in0(out_25), .in1(out_24), .in2(out_23), .in3(out_22), .in4(out_21), .in5(out_20), .in6(out_19),
    .in7(out_18), .read(and_11_out), .write(and_12_out), .reset(RESET_out), .out0(out_25), .out1(out_24),
    .out2(out_23), .out3(out_22), .out4(out_21), .out5(out_20), .out6(out_19), .out7(out_18));
  and and_11 (and_11_out, controlunit_1_rx_r, decoder_1_out3);
  and and_12 (and_12_out, decoder_1_out3, controlunit_1_rx_w);
  or or_4 (or_4_out, controlunit_1_mar_w, and_7_out);
  or or_5 (or_5_out, controlunit_1_ram_r, and_6_out);
  or or_6 (or_6_out, controlunit_1_ram_w, and_9_out);
  or or_7 (or_7_out, and_1_out, and_7_out, and_6_out, and_9_out);
  Button RESET_3 (.out(RESET_3_out));
  Ram256 ram256_1 (
    .addr0(out_25), .addr1(out_24), .addr2(out_23), .addr3(out_22), .addr4(out_21), .addr5(out_20),
    .addr6(out_19), .addr7(out_18), .marw(or_4_out), .read(or_5_out), .write(or_6_out), .reset(RESET_3_out),
    .in0(out_25), .in1(out_24), .in2(out_23), .in3(out_22), .in4(out_21), .in5(out_20), .in6(out_19),
    .in7(out_18), .out0(out_25), .out1(out_24), .out2(out_23), .out3(out_22), .out4(out_21), .out5(out_20),
    .out6(out_19), .out7(out_18), .clk(or_7_out));

  // Notes on the sheet:
  //   bits | cond   | flag test  | description
  //   0000 | r      | -----      | branch always
  //   0001 | zs/eq  | z=1        | branch if equal
  //   0010 | ss/neg | s=1        | branch if negative
  //   0011 | ov     | v=1        | branch if overflow
  //   0100 | cs/ltu | c=1        | branch if uint <
  //   0101 | leu    | c=1 or z=1 | branch if uint <=
  //   0110 | lt     | v+s        | branch if int <
  //   0111 | le     | v+s or z=1 | branch if int <=
  //   0000 00 00  ->  mov  ra, rb    ->  ra = rb
  //   0001 00 rb  ->  data rb, imm8  ->  rb = ram[pc++]
  //   0010 ra rb  ->  ldr  ra, [rb]  ->  ra = ram[rb]
  //   0011 ra rb  ->  str  ra, [rb]  ->  ram[rb] = ra
  //   0100 00 rb  ->  jalr rb        ->  pc <-> rb
  //   0101  cond  ->  b<cond> imm8   ->  pc += cond ? ram[pc] : 1
  //   0110 00 00  ->  halt           ->  stop computer
  //   0111 00 rb  ->  in   data, rb  ->  rb = io[active].data
  //   0111 10 rb  ->  out  data, rb  ->  io[active].data = rb
  //   0111 01 rb  ->  in   addr, rb  ->  rb = io[active].addr
  //   0111 11 rb  ->  out  addr, rb  ->  io[rb].active = true
  //   1000 ra rb  ->  add ra, rb  ->  ra = ra + rb       [vcsz]
  //   1001 ra rb  ->  sub ra, rb  ->  ra = ra - rb       [vcsz]
  //   1010 ra rb  ->  shl ra, rb  ->  ra = [rb << 1, 0]  [0csz]
  //   1011 ra rb  ->  shr ra, rb  ->  ra = [0, rb >> 1]  [0csz]
  //   1100 ra rb  ->  and ra, rb  ->  ra = ra & rb       [00sz]
  //   1101 ra rb  ->  orr ra, rb  ->  ra = ra | rb       [00sz]
  //   1110 ra rb  ->  xor ra, rb  ->  ra = ra ^ rb       [00sz]
  //   1111 ra rb  ->  cmp ra, rb  ->  fr = ra - rb       [vcsz]
endmodule
