// Logisim project scott.circ as structural Verilog
module Main (
  input  in_1,
  input  in_2
);

  wire button_1_out, button_2_out, button_3_out, clock_1_out, cpu_1_addr_0, cpu_1_addr_1, cpu_1_addr_2,
       cpu_1_addr_3, cpu_1_addr_4, cpu_1_addr_5, cpu_1_addr_6, cpu_1_addr_7, cpu_1_addr_8, cpu_1_addr_9,
       cpu_1_bus_clk, cpu_1_bus_en_2, cpu_1_bus_ld_str_2, cpu_1_bus_rst, cpu_1_out_0, cpu_1_out_1,
       cpu_1_out_2, cpu_1_out_3, cpu_1_out_4, cpu_1_out_5, cpu_1_out_6, cpu_1_out_7, led8_1__0, led8_1__1,
       led8_1__2, led8_1__3, led8_1__4, led8_1__5, led8_1__6, led8_1__7, led8_2__0, led8_2__1, led8_2__2,
       led8_2__3, led8_2__4, led8_2__5, led8_2__6, led8_2__7, led8_3__0, led8_3__1, led8_3__2, led8_3__3,
       led8_3__4, led8_3__5, led8_3__6, led8_3__7, led8_4__0, led8_4__1, led8_4__2, led8_4__3, led8_4__4,
       led8_4__5, led8_4__6, led8_4__7, led8_5__0, led8_5__1, led8_5__2, led8_5__3, led8_5__4, led8_5__5,
       led8_5__6, led8_5__7, led8_6__0, led8_6__1, led8_6__2, led8_6__3, led8_6__4, led8_6__5, led8_6__6,
       led8_6__7, led8_7__0, led8_7__1, led8_7__2, led8_7__3, led8_7__4, led8_7__5, led8_7__6, led8_7__7,
       led8_8__0, led8_8__1, led8_8__2, led8_8__3, led8_8__4, led8_8__5, led8_8__6, led8_8__7, led8_9__0,
       led8_9__1, led8_9__2, led8_9__3, led8_9__4, led8_9__5, led8_9__6, led8_9__7, led8_10__0, led8_10__1,
       led8_10__2, led8_10__3, led8_10__4, led8_10__5, led8_10__6, led8_10__7, led8_11__0, led8_11__1,
       led8_11__2, led8_11__3, led8_11__4, led8_11__5, led8_11__6, led8_11__7, led8_12__0, led8_12__1,
       led8_12__2, led8_12__3, led8_12__4, led8_12__5, led8_12__6, led8_12__7, led8_13__0, led8_13__1,
       led8_13__2, led8_13__3, led8_13__4, led8_13__5, led8_13__6, led8_13__7, led8_14__0, led8_14__1,
       led8_14__2, led8_14__3, led8_14__4, led8_14__5, led8_14__6, led8_14__7, led10_1__0, led10_1__1,
       led10_1__2, led10_1__3, led10_1__4, led10_1__5, led10_1__6, led10_1__7, led10_1__8, led10_1__9,
       memoryunit_1_mem0_en, memoryunit_1_mem1_clk, memoryunit_1_mem1_en, memoryunit_1_mem1_ld,
       memoryunit_1_mem1_rst, memoryunit_1_mem1_str, memoryunit_1_mem2_clk, memoryunit_1_mem2_en,
       memoryunit_1_mem2_ld, memoryunit_1_mem2_rst, memoryunit_1_mem2_str, memoryunit_1_out_0,
       memoryunit_1_out_1, memoryunit_1_out_2, memoryunit_1_out_3, memoryunit_1_out_4, memoryunit_1_out_5,
       memoryunit_1_out_6, memoryunit_1_out_7, n7segdisplay_1_a, n7segdisplay_1_b, n7segdisplay_1_c,
       n7segdisplay_1_d, n7segdisplay_1_dp, n7segdisplay_1_e, n7segdisplay_1_f, n7segdisplay_1_g,
       n7segdisplay_2_a, n7segdisplay_2_b, n7segdisplay_2_c, n7segdisplay_2_d, n7segdisplay_2_dp,
       n7segdisplay_2_e, n7segdisplay_2_f, n7segdisplay_2_g, n7segdisplay_3_a, n7segdisplay_3_b,
       n7segdisplay_3_c, n7segdisplay_3_d, n7segdisplay_3_dp, n7segdisplay_3_e, n7segdisplay_3_f,
       n7segdisplay_3_g, n7segdisplay_4_a, n7segdisplay_4_b, n7segdisplay_4_c, n7segdisplay_4_d,
       n7segdisplay_4_dp, n7segdisplay_4_e, n7segdisplay_4_f, n7segdisplay_4_g;
  wire [3:0] cpu_1_cycles_0, cpu_1_cycles_1, cpu_1_cycles_2, cpu_1_cycles_3;
  wire [7:0] cpu_1_dbga, cpu_1_dbgb, cpu_1_dbgd, cpu_1_dbgfr, cpu_1_dbgin, cpu_1_dbgir, cpu_1_dbgnpc,
       cpu_1_dbgout, cpu_1_dbgpc, cpu_1_dbgr0, cpu_1_dbgr1, cpu_1_dbgr2, cpu_1_dbgr3, cpu_1_dbgsp,
       memoryunit_1_mem0_addr, memoryunit_1_mem1_addr, memoryunit_1_mem1_out, memoryunit_1_mem2_addr,
       memoryunit_1_mem2_out, ram_1_data, ram_2_data, rom_1_data;
  wire [9:0] cpu_1_dbgaddr;

  MemoryUnit memoryunit_1 (
    .addr_0(cpu_1_addr_0), .addr_1(cpu_1_addr_1), .addr_2(cpu_1_addr_2), .addr_3(cpu_1_addr_3),
    .addr_4(cpu_1_addr_4), .addr_5(cpu_1_addr_5), .addr_6(cpu_1_addr_6), .addr_7(cpu_1_addr_7),
    .addr_8(cpu_1_addr_8), .addr_9(cpu_1_addr_9), .in_0(cpu_1_out_0), .in_1(cpu_1_out_1), .in_2(cpu_1_out_2),
    .in_3(cpu_1_out_3), .in_4(cpu_1_out_4), .in_5(cpu_1_out_5), .in_6(cpu_1_out_6), .in_7(cpu_1_out_7),
    .en(cpu_1_bus_en_2), .ld_str(cpu_1_bus_ld_str_2), .clk(cpu_1_bus_clk), .rst(cpu_1_bus_rst),
    .out_0(memoryunit_1_out_0), .out_1(memoryunit_1_out_1), .out_2(memoryunit_1_out_2),
    .out_3(memoryunit_1_out_3), .out_4(memoryunit_1_out_4), .out_5(memoryunit_1_out_5),
    .out_6(memoryunit_1_out_6), .out_7(memoryunit_1_out_7), .mem1_addr(memoryunit_1_mem1_addr),
    .mem1_in(ram_1_data), .mem1_out(memoryunit_1_mem1_out), .mem1_en(memoryunit_1_mem1_en),
    .mem1_ld(memoryunit_1_mem1_ld), .mem1_str(memoryunit_1_mem1_str), .mem1_clk(memoryunit_1_mem1_clk),
    .mem1_rst(memoryunit_1_mem1_rst), .mem2_addr(memoryunit_1_mem2_addr), .mem2_in(ram_2_data),
    .mem2_out(memoryunit_1_mem2_out), .mem2_en(memoryunit_1_mem2_en), .mem2_ld(memoryunit_1_mem2_ld),
    .mem2_str(memoryunit_1_mem2_str), .mem2_clk(memoryunit_1_mem2_clk), .mem2_rst(memoryunit_1_mem2_rst),
    .mem0_addr(memoryunit_1_mem0_addr), .mem0_in(rom_1_data), .mem0_en(memoryunit_1_mem0_en));  // open: mem3_addr, mem3_in, mem3_out, mem3_en, mem3_ld, mem3_str, mem3_clk, mem3_rst, mem0_out, mem0_ld, mem0_str, mem0_clk, mem0_rst
  CPU cpu_1 (
    .clk(clock_1_out), .reset(button_1_out), .dbgR2(cpu_1_dbgr2), .dbgR3(cpu_1_dbgr3), .dbgFR(cpu_1_dbgfr),
    .dbgSP(cpu_1_dbgsp), .dbgNPC(cpu_1_dbgnpc), .dbgPC(cpu_1_dbgpc), .dbgIR(cpu_1_dbgir),
    .dbgR0(cpu_1_dbgr0), .dbgR1(cpu_1_dbgr1), .bus_en_2(cpu_1_bus_en_2), .bus_ld_str_2(cpu_1_bus_ld_str_2),
    .resume(button_2_out), .dbgADDR(cpu_1_dbgaddr), .dbgA(cpu_1_dbga), .dbgB(cpu_1_dbgb), .dbgD(cpu_1_dbgd),
    .dbgIN(cpu_1_dbgin), .dbgOUT(cpu_1_dbgout), .cycles_0(cpu_1_cycles_0), .cycles_1(cpu_1_cycles_1),
    .cycles_2(cpu_1_cycles_2), .cycles_3(cpu_1_cycles_3), .manual(in_2), .tick(button_3_out), .off_on(in_1),
    .addr_5(cpu_1_addr_5), .addr_0(cpu_1_addr_0), .addr_1(cpu_1_addr_1), .addr_2(cpu_1_addr_2),
    .addr_3(cpu_1_addr_3), .addr_4(cpu_1_addr_4), .addr_6(cpu_1_addr_6), .addr_7(cpu_1_addr_7),
    .addr_8(cpu_1_addr_8), .addr_9(cpu_1_addr_9), .out_7(cpu_1_out_7), .out_0(cpu_1_out_0),
    .out_6(cpu_1_out_6), .out_1(cpu_1_out_1), .out_5(cpu_1_out_5), .out_2(cpu_1_out_2), .out_4(cpu_1_out_4),
    .out_3(cpu_1_out_3), .in_7(memoryunit_1_out_7), .in_0(memoryunit_1_out_0), .in_6(memoryunit_1_out_6),
    .in_1(memoryunit_1_out_1), .in_5(memoryunit_1_out_5), .in_2(memoryunit_1_out_2),
    .in_4(memoryunit_1_out_4), .in_3(memoryunit_1_out_3), .bus_clk(cpu_1_bus_clk), .bus_rst(cpu_1_bus_rst));  // open: mux_ra, mux_rb, mux_rd_2, mux_rd, selRA, selRB, selRD, op, cin, fr_w, rd_w, sp_w, ix, sp_inc_dec, ix_w, npc_w, pc_w, mux_npc, bus_ld_str, bus_en, branch, mux_addr, br_op, halt
  LED led_1 (.in(led8_1__7));
  LED led_2 (.in(led8_2__7));
  LED led_3 (.in(led8_3__7));
  LED led_4 (.in(led8_4__7));
  LED led_5 (.in(led8_5__7));
  LED8 led8_1 (
    .in(cpu_1_dbgr0), ._7(led8_1__7), ._6(led8_1__6), ._5(led8_1__5), ._4(led8_1__4), ._3(led8_1__3),
    ._2(led8_1__2), ._1(led8_1__1), ._0(led8_1__0));
  LED led_6 (.in(led8_1__6));
  LED led_7 (.in(led8_1__3));
  LED led_8 (.in(led8_1__5));
  LED led_9 (.in(led8_1__4));
  LED8 led8_2 (
    .in(cpu_1_dbgr1), ._7(led8_2__7), ._6(led8_2__6), ._5(led8_2__5), ._4(led8_2__4), ._3(led8_2__3),
    ._2(led8_2__2), ._1(led8_2__1), ._0(led8_2__0));
  LED led_10 (.in(led8_2__4));
  LED led_11 (.in(led8_2__5));
  LED led_12 (.in(led8_2__6));
  LED led_13 (.in(led8_2__3));
  LED8 led8_3 (
    .in(cpu_1_dbgr2), ._7(led8_3__7), ._6(led8_3__6), ._5(led8_3__5), ._4(led8_3__4), ._3(led8_3__3),
    ._2(led8_3__2), ._1(led8_3__1), ._0(led8_3__0));
  LED led_14 (.in(led8_3__6));
  LED led_15 (.in(led8_3__4));
  LED led_16 (.in(led8_3__5));
  LED led_17 (.in(led8_3__3));
  LED8 led8_4 (
    .in(cpu_1_dbgr3), ._7(led8_4__7), ._6(led8_4__6), ._5(led8_4__5), ._4(led8_4__4), ._3(led8_4__3),
    ._2(led8_4__2), ._1(led8_4__1), ._0(led8_4__0));
  LED led_18 (.in(led8_4__4));
  LED led_19 (.in(led8_4__5));
  LED led_20 (.in(led8_4__3));
  LED led_21 (.in(led8_4__6));
  LED8 led8_5 (
    .in(cpu_1_dbgsp), ._7(led8_5__7), ._6(led8_5__6), ._5(led8_5__5), ._4(led8_5__4), ._3(led8_5__3),
    ._2(led8_5__2), ._1(led8_5__1), ._0(led8_5__0));
  LED led_22 (.in(led8_5__4));
  LED led_23 (.in(led8_5__6));
  LED led_24 (.in(led8_5__3));
  LED led_25 (.in(led8_5__5));
  LED led_26 (.in(in_1));
  LED led_27 (.in(led8_1__0));
  LED led_28 (.in(led8_1__1));
  LED led_29 (.in(led8_1__2));
  LED led_30 (.in(led8_2__0));
  LED led_31 (.in(led8_2__1));
  LED led_32 (.in(led8_2__2));
  LED led_33 (.in(led8_3__1));
  LED led_34 (.in(led8_3__0));
  LED led_35 (.in(led8_3__2));
  LED led_36 (.in(led8_4__2));
  LED led_37 (.in(led8_4__1));
  LED led_38 (.in(led8_4__0));
  LED led_39 (.in(led8_5__2));
  LED led_40 (.in(led8_5__0));
  LED led_41 (.in(led8_5__1));
  ROM rom_1 (.addr(memoryunit_1_mem0_addr), .data(rom_1_data), .sel(memoryunit_1_mem0_en));
  LED led_42 (.in(led8_6__6));
  LED led_43 (.in(led8_6__7));
  LED led_44 (.in(led8_7__7));
  LED led_45 (.in(led8_7__6));
  LED led_46 (.in(led8_8__7));
  LED led_47 (.in(led8_8__6));
  LED led_48 (.in(led8_9__6));
  LED led_49 (.in(led8_9__7));
  _7_Segment_Display u_7_segment_display_1 (
    .g(n7segdisplay_2_g), .f(n7segdisplay_2_f), .a(n7segdisplay_2_a), .b(n7segdisplay_2_b),
    .e(n7segdisplay_2_e), .d(n7segdisplay_2_d), .c(n7segdisplay_2_c), .dp(n7segdisplay_2_dp));
  _7SegDisplay u_7segdisplay_1 (
    .BCD(cpu_1_cycles_2), .a(n7segdisplay_1_a), .b(n7segdisplay_1_b), .c(n7segdisplay_1_c),
    .d(n7segdisplay_1_d), .e(n7segdisplay_1_e), .f(n7segdisplay_1_f), .dp(n7segdisplay_1_dp),
    .g(n7segdisplay_1_g));
  _7SegDisplay u_7segdisplay_2 (
    .BCD(cpu_1_cycles_3), .a(n7segdisplay_2_a), .b(n7segdisplay_2_b), .c(n7segdisplay_2_c),
    .d(n7segdisplay_2_d), .e(n7segdisplay_2_e), .f(n7segdisplay_2_f), .dp(n7segdisplay_2_dp),
    .g(n7segdisplay_2_g));
  LED led_50 (.in(button_1_out));
  Button button_1 (.out(button_1_out));
  LED8 led8_6 (
    .in(cpu_1_dbgnpc), ._7(led8_6__7), ._6(led8_6__6), ._5(led8_6__5), ._4(led8_6__4), ._3(led8_6__3),
    ._2(led8_6__2), ._1(led8_6__1), ._0(led8_6__0));
  LED led_51 (.in(led8_6__5));
  LED led_52 (.in(led8_6__3));
  LED led_53 (.in(led8_6__4));
  LED8 led8_7 (
    .in(cpu_1_dbgpc), ._7(led8_7__7), ._6(led8_7__6), ._5(led8_7__5), ._4(led8_7__4), ._3(led8_7__3),
    ._2(led8_7__2), ._1(led8_7__1), ._0(led8_7__0));
  LED led_54 (.in(led8_7__5));
  LED led_55 (.in(led8_7__3));
  LED led_56 (.in(led8_7__4));
  LED8 led8_8 (
    .in(cpu_1_dbgir), ._7(led8_8__7), ._6(led8_8__6), ._5(led8_8__5), ._4(led8_8__4), ._3(led8_8__3),
    ._2(led8_8__2), ._1(led8_8__1), ._0(led8_8__0));
  LED led_57 (.in(led8_8__4));
  LED led_58 (.in(led8_8__5));
  LED led_59 (.in(led8_8__3));
  LED8 led8_9 (
    .in(cpu_1_dbgfr), ._7(led8_9__7), ._6(led8_9__6), ._5(led8_9__5), ._4(led8_9__4), ._3(led8_9__3),
    ._2(led8_9__2), ._1(led8_9__1), ._0(led8_9__0));
  LED led_60 (.in(led8_9__3));
  LED led_61 (.in(led8_9__5));
  LED led_62 (.in(led8_9__4));
  _7_Segment_Display u_7_segment_display_2 (
    .g(n7segdisplay_3_g), .f(n7segdisplay_3_f), .a(n7segdisplay_3_a), .b(n7segdisplay_3_b),
    .e(n7segdisplay_3_e), .d(n7segdisplay_3_d), .c(n7segdisplay_3_c), .dp(n7segdisplay_3_dp));
  _7_Segment_Display u_7_segment_display_3 (
    .g(n7segdisplay_1_g), .f(n7segdisplay_1_f), .a(n7segdisplay_1_a), .b(n7segdisplay_1_b),
    .e(n7segdisplay_1_e), .d(n7segdisplay_1_d), .c(n7segdisplay_1_c), .dp(n7segdisplay_1_dp));
  _7SegDisplay u_7segdisplay_3 (
    .BCD(cpu_1_cycles_1), .a(n7segdisplay_3_a), .b(n7segdisplay_3_b), .c(n7segdisplay_3_c),
    .d(n7segdisplay_3_d), .e(n7segdisplay_3_e), .f(n7segdisplay_3_f), .dp(n7segdisplay_3_dp),
    .g(n7segdisplay_3_g));
  LED led_63 (.in(button_2_out));
  Button button_2 (.out(button_2_out));
  RAM #(.bus("separate")) ram_1 (
    .addr(memoryunit_1_mem1_addr), .din(memoryunit_1_mem1_out), .data(ram_1_data),
    .str(memoryunit_1_mem1_str), .sel(memoryunit_1_mem1_en), .clk(memoryunit_1_mem1_clk),
    .ld(memoryunit_1_mem1_ld), .clr(memoryunit_1_mem1_rst));
  LED led_64 (.in(led8_6__1));
  LED led_65 (.in(led8_6__2));
  LED led_66 (.in(led8_6__0));
  LED led_67 (.in(led8_7__2));
  LED led_68 (.in(led8_7__0));
  LED led_69 (.in(led8_7__1));
  LED led_70 (.in(led8_8__0));
  LED led_71 (.in(led8_8__2));
  LED led_72 (.in(led8_8__1));
  LED led_73 (.in(led8_9__0));
  LED led_74 (.in(led8_9__2));
  LED led_75 (.in(led8_9__1));
  _7_Segment_Display u_7_segment_display_4 (
    .g(n7segdisplay_4_g), .f(n7segdisplay_4_f), .a(n7segdisplay_4_a), .b(n7segdisplay_4_b),
    .e(n7segdisplay_4_e), .d(n7segdisplay_4_d), .c(n7segdisplay_4_c), .dp(n7segdisplay_4_dp));
  _7SegDisplay u_7segdisplay_4 (
    .BCD(cpu_1_cycles_0), .a(n7segdisplay_4_a), .b(n7segdisplay_4_b), .c(n7segdisplay_4_c),
    .d(n7segdisplay_4_d), .e(n7segdisplay_4_e), .f(n7segdisplay_4_f), .dp(n7segdisplay_4_dp),
    .g(n7segdisplay_4_g));
  LED led_76 (.in(in_2));
  LED led_77 (.in(led10_1__9));
  LED led_78 (.in(led10_1__8));
  LED led_79 (.in(button_3_out));
  Button button_3 (.out(button_3_out));
  LED led_80 (.in(led8_10__4));
  LED led_81 (.in(led8_10__5));
  LED led_82 (.in(led8_10__7));
  LED led_83 (.in(led8_10__6));
  LED led_84 (.in(led8_11__6));
  LED led_85 (.in(led8_11__7));
  LED led_86 (.in(led8_11__4));
  LED led_87 (.in(led8_11__5));
  LED led_88 (.in(led8_12__5));
  LED led_89 (.in(led8_12__4));
  LED led_90 (.in(led8_12__7));
  LED led_91 (.in(led8_12__6));
  LED10 led10_1 (
    .in(cpu_1_dbgaddr), ._9(led10_1__9), ._8(led10_1__8), ._7(led10_1__7), ._6(led10_1__6), ._5(led10_1__5),
    ._4(led10_1__4), ._3(led10_1__3), ._2(led10_1__2), ._1(led10_1__1), ._0(led10_1__0));
  LED led_92 (.in(led10_1__4));
  LED led_93 (.in(led10_1__6));
  LED led_94 (.in(led10_1__5));
  LED led_95 (.in(led10_1__7));
  LED led_96 (.in(led8_13__7));
  LED led_97 (.in(led8_13__4));
  LED led_98 (.in(led8_13__5));
  LED led_99 (.in(led8_13__6));
  LED led_100 (.in(led8_14__7));
  LED led_101 (.in(led8_14__6));
  LED led_102 (.in(led8_14__5));
  LED led_103 (.in(led8_14__4));
  RAM #(.bus("separate")) ram_2 (
    .addr(memoryunit_1_mem2_addr), .din(memoryunit_1_mem2_out), .data(ram_2_data),
    .str(memoryunit_1_mem2_str), .sel(memoryunit_1_mem2_en), .clk(memoryunit_1_mem2_clk),
    .ld(memoryunit_1_mem2_ld), .clr(memoryunit_1_mem2_rst));
  LED8 led8_10 (
    .in(cpu_1_dbga), ._7(led8_10__7), ._6(led8_10__6), ._5(led8_10__5), ._4(led8_10__4), ._3(led8_10__3),
    ._2(led8_10__2), ._1(led8_10__1), ._0(led8_10__0));
  LED led_104 (.in(led8_10__1));
  LED led_105 (.in(led8_10__2));
  LED led_106 (.in(led8_10__3));
  LED8 led8_11 (
    .in(cpu_1_dbgb), ._7(led8_11__7), ._6(led8_11__6), ._5(led8_11__5), ._4(led8_11__4), ._3(led8_11__3),
    ._2(led8_11__2), ._1(led8_11__1), ._0(led8_11__0));
  LED led_107 (.in(led8_11__1));
  LED led_108 (.in(led8_11__2));
  LED led_109 (.in(led8_11__3));
  LED8 led8_12 (
    .in(cpu_1_dbgd), ._7(led8_12__7), ._6(led8_12__6), ._5(led8_12__5), ._4(led8_12__4), ._3(led8_12__3),
    ._2(led8_12__2), ._1(led8_12__1), ._0(led8_12__0));
  LED led_110 (.in(led8_12__3));
  LED led_111 (.in(led8_12__2));
  LED led_112 (.in(led8_12__1));
  LED led_113 (.in(led10_1__1));
  LED led_114 (.in(led10_1__2));
  LED led_115 (.in(led10_1__3));
  LED8 led8_13 (
    .in(cpu_1_dbgin), ._7(led8_13__7), ._6(led8_13__6), ._5(led8_13__5), ._4(led8_13__4), ._3(led8_13__3),
    ._2(led8_13__2), ._1(led8_13__1), ._0(led8_13__0));
  LED led_116 (.in(led8_13__2));
  LED led_117 (.in(led8_13__3));
  LED led_118 (.in(led8_13__1));
  LED8 led8_14 (
    .in(cpu_1_dbgout), ._7(led8_14__7), ._6(led8_14__6), ._5(led8_14__5), ._4(led8_14__4), ._3(led8_14__3),
    ._2(led8_14__2), ._1(led8_14__1), ._0(led8_14__0));
  LED led_119 (.in(led8_14__2));
  LED led_120 (.in(led8_14__3));
  LED led_121 (.in(led8_14__1));
  LED led_122 (.in(clock_1_out));
  Clock clock_1 (.out(clock_1_out));
  LED led_123 (.in(led8_10__0));
  LED led_124 (.in(led8_11__0));
  LED led_125 (.in(led8_12__0));
  LED led_126 (.in(led10_1__0));
  LED led_127 (.in(led8_13__0));
  LED led_128 (.in(led8_14__0));

  // Notes on the sheet:
  //   contents of rom_1 (hex, n*v repeats v):
  //   1c 5 14 1 9 10 2 fc 54 a 1 82 9 4 10 1 9c 50 f3 10 1 34 60
  //   0000 ra rb  ->  mov  ra, rb    ->  ra = rb
  //   0001 ra xx  ->  data ra, imm8  ->  ra = ram[pc++]
  //   0010 ra rb  ->  ldr  ra, [rb]  ->  ra = ram[rb]
  //   0011 ra rb  ->  str  ra, [rb]  ->  ram[rb] = ra
  //   0100 ra ra  ->  jalr ra        ->  pc <-> ra
  //   0101  cond  ->  b<cond> imm8   ->  pc += cond ? ram[pc] : 1
  //   0110 00 00  ->  halt           ->  stop computer
  //   0111 ra 00  ->  in   ra, data  ->  ra = io[active].data
  //   0111 ra 10  ->  out  ra, data  ->  io[active].data = ra
  //   0111 ra 01  ->  in   ra, addr  ->  ra = io[active].addr
  //   0111 ra 11  ->  out  ra, addr  ->  io[ra].active = true
  //   1000 ra rb  ->  add  ra, rb    ->  ra = ra + rb       [vcsz]
  //   1001 ra rb  ->  sub  ra, rb    ->  ra = ra - rb       [vcsz]
  //   1010 ra rb  ->  shl  ra, rb    ->  ra = [rb << 1, 0]  [0csz]
  //   1011 ra rb  ->  shr  ra, rb    ->  ra = [0, rb >> 1]  [0csz]
  //   1100 ra rb  ->  and  ra, rb    ->  ra = ra & rb       [00sz]
  //   1101 ra rb  ->  orr  ra, rb    ->  ra = ra | rb       [00sz]
  //   1110 ra rb  ->  xor  ra, rb    ->  ra = ra ^ rb       [00sz]
  //   1111 ra rb  ->  cmp  ra, rb    ->  fr = ra - rb       [vcsz]
  //   bits | cond   | flag test  | description
  //   0000 | r      | -----      | branch always
  //   0001 | zs/eq  | z=1        | branch if equal
  //   0010 | ss/neg | s=1        | branch if negative
  //   0011 | ov     | v=1        | branch if overflow
  //   0100 | cs/ltu | c=1        | branch if uint <
  //   0101 | leu    | c=1 or z=1 | branch if uint <=
  //   0110 | lt     | v+s        | branch if int <
  //   0111 | le     | v+s or z=1 | branch if int <=
endmodule

module CPU (
  input  mux_npc,
  input  mux_ra,
  input  [2:0] op,
  input  mux_rd,
  input  [1:0] ix,
  input  fr_w,
  input  sp_w,
  input  halt,
  input  bus_ld_str,
  input  cin,
  input  sp_inc_dec,
  input  branch,
  input  mux_rb,
  input  npc_w,
  input  [2:0] br_op,
  input  [1:0] selRA,
  input  mux_rd_2,
  input  bus_en,
  input  [1:0] mux_addr,
  input  [1:0] selRB,
  input  ix_w,
  input  pc_w,
  input  [1:0] selRD,
  input  rd_w,
  input  manual,
  input  tick,
  input  clk,
  input  resume,
  input  reset,
  input  off_on,
  input  in_7,
  input  in_0,
  input  in_6,
  input  in_1,
  input  in_5,
  input  in_2,
  input  in_4,
  input  in_3,
  output [7:0] dbgR0,
  output [7:0] dbgR1,
  output [7:0] dbgR2,
  output [7:0] dbgR3,
  output [7:0] dbgSP,
  output [7:0] dbgNPC,
  output [7:0] dbgPC,
  output [7:0] dbgIR,
  output [7:0] dbgFR,
  output [7:0] dbgA,
  output [7:0] dbgB,
  output [7:0] dbgD,
  output [7:0] dbgIN,
  output [7:0] dbgOUT,
  output [9:0] dbgADDR,
  output [3:0] cycles_0,
  output [3:0] cycles_1,
  output [3:0] cycles_2,
  output [3:0] cycles_3,
  output bus_clk,
  output bus_rst,
  output bus_en_2,
  output bus_ld_str_2,
  output addr_9,
  output addr_0,
  output out_7,
  output out_0,
  output addr_8,
  output addr_1,
  output out_6,
  output out_1,
  output addr_7,
  output addr_2,
  output out_5,
  output out_2,
  output addr_6,
  output addr_3,
  output out_4,
  output out_3,
  output addr_5,
  output addr_4
);

  wire and_1_out, and_2_out, and_3_out, and_4_out, and_5_out, and_6_out, bcdinc_2_cout, bcdinc_3_cout,
       bcdinc_4_cout, branchchecker_1_result, ifetch_exec_q, ifetch_exec_qn, multiplexer_1_out, not_1_out,
       or_1_out, or_5_out, or_6_out, or_7_out, t_ff_1_qn, t_ff_2_q;
  wire [3:0] alu_1_zero, bcdinc_1_out, bcdinc_2_out, bcdinc_3_out, bcdinc_4_out, reg4_1_out_3__0;
  wire [7:0] alu_1_out, inc8_1_out, inc8_2_out, multiplexer_2_out, reg8_1_out, reg8_2_out, reg8_3_out,
       reg8_4_out, reg8_5_out, reg8_6_out, regfile_1_rb;

  Multiplexer #(.enable("false")) multiplexer_1 (.in0(clk), .in1(tick), .out(multiplexer_1_out), .sel(manual));
  nand nand_1 (bus_clk, multiplexer_1_out, t_ff_1_qn);
  T_Flip_Flop t_ff_1 (
    .clk(bus_clk), .T(t_ff_1_qn), .Q(dbgFR[6]), .Qn(t_ff_1_qn), .reset(or_1_out), .en(and_1_out));  // open: preset
  or or_1 (or_1_out, t_ff_2_q, bus_rst);
  T_Flip_Flop t_ff_2 (.clk(resume), .T(1'b1), .Q(t_ff_2_q), .reset(t_ff_2_q), .en(1'b1));  // open: Qn, preset
  T_Flip_Flop ifetch_exec (
    .clk(bus_clk), .T(1'b1), .Q(ifetch_exec_q), .Qn(ifetch_exec_qn), .reset(bus_rst), .en(1'b1));  // open: preset
  or or_2 (bus_rst, reset, ~off_on);  // OR_Gate
  and and_1 (and_1_out, 1'b0, ifetch_exec_q);
  Reg8 reg8_1 (
    .in({in_7, in_6, in_5, in_4, in_3, in_2, in_1, in_0}), .dbg(dbgIR), .r(1'b1), .w(ifetch_exec_qn),
    .en(1'b1), .clk(bus_clk), .rst(bus_rst), .out(reg8_1_out));
  ControlUnit controlunit_1 ();
  or or_3 (bus_en_2, ifetch_exec_qn, 1'b0);
  or or_4 (bus_ld_str_2, 1'b0, ~ifetch_exec_qn);  // OR_Gate
  and and_2 (and_2_out, 1'b0, branchchecker_1_result);
  Multiplexer #(.width(8), .enable("false")) multiplexer_2 (
    .in0(inc8_1_out), .in1(alu_1_out), .out(multiplexer_2_out), .sel(or_5_out));
  or or_5 (or_5_out, 1'b0, and_2_out);
  BranchChecker branchchecker_1 (
    .zero(reg4_1_out_3__0[0]), .sign(reg4_1_out_3__0[1]), .carry(reg4_1_out_3__0[2]),
    .overflow(reg4_1_out_3__0[3]), .op0(1'b0), .op1(1'b0), .op2(1'b0), .result(branchchecker_1_result));
  Reg8 reg8_2 (
    .in(multiplexer_2_out), .dbg(dbgNPC), .r(1'b1), .w(or_6_out), .en(1'b1), .clk(bus_clk), .rst(bus_rst),
    .out(reg8_2_out));
  or or_6 (or_6_out, 1'b0, ifetch_exec_qn);
  Multiplexer #(.select(2), .width(10), .enable("false")) multiplexer_3 (
    .in0({2'b00, reg8_3_out}), .in1({dbgFR[5:4], alu_1_out}), .in2({2'b01, reg8_4_out}),
    .in3({2'b01, inc8_2_out}),
    .out({addr_9, addr_8, addr_7, addr_6, addr_5, addr_4, addr_3, addr_2, addr_1, addr_0}), .sel(2'b00));
  or or_7 (or_7_out, 1'b0, ifetch_exec_qn);
  Inc8 inc8_1 (.in(reg8_3_out), .out(inc8_1_out), .cin(1'b1), .add_sub(1'b0));  // open: cout
  Reg8 reg8_3 (
    .in(reg8_2_out), .dbg(dbgPC), .r(1'b1), .w(or_7_out), .en(1'b1), .clk(not_1_out), .rst(bus_rst),
    .out(reg8_3_out));
  not not_1 (not_1_out, bus_clk);
  RegFile regfile_1 (
    .rd(dbgD), .reg_w(and_3_out), .selRD0(1'b0), .selRD1(1'b0), .clk(bus_clk), .rst(bus_rst), .selRA0(1'b0),
    .selRA1(1'b0), .selRB0(1'b0), .selRB1(1'b0), .ra(dbgOUT), .rb(regfile_1_rb), .dbgR3(dbgR3),
    .dbgR2(dbgR2), .dbgR0(dbgR0), .dbgR1(dbgR1));
  and and_3 (and_3_out, 1'b0, ifetch_exec_q);
  RegMux regmux_1 (
    .RAin0(dbgOUT), .RAin1(reg8_3_out), .RBin0(regfile_1_rb),
    .RBin1({in_7, in_6, in_5, in_4, in_3, in_2, in_1, in_0}), .RDout(dbgD), .RAout(dbgA), .RBout(dbgB),
    .RDin0(alu_1_out), .RDin1({in_7, in_6, in_5, in_4, in_3, in_2, in_1, in_0}), .RDin2(inc8_1_out),
    .muxRA(1'b0), .muxRB(1'b0), .muxRD1(1'b0), .muxRD0(1'b0));
  and and_4 (and_4_out, 1'b0, bus_clk);
  Reg4 reg4_1 (
    .r(1'b1), .w(and_5_out), .en(1'b1), .clk(bus_clk), .rst(bus_rst), .in_3__0(alu_1_zero),
    .out_3__0(reg4_1_out_3__0), .dbg_3__0(dbgFR[3:0]));
  and and_5 (and_5_out, ifetch_exec_q, 1'b0);
  D_Flip_Flop d_ff_1 (.clk(and_4_out), .D(1'b0), .Q(dbgFR[4]), .en(1'b1), .reset(bus_rst));  // open: Qn, preset
  D_Flip_Flop d_ff_2 (.clk(and_4_out), .D(1'b0), .Q(dbgFR[5]), .preset(bus_rst), .en(1'b1));  // open: Qn, reset
  ALU_2 alu_1 (
    .cin(1'b0), .op2(1'b0), .op1(1'b0), .op0(1'b0), .overflow(alu_1_zero[3]), .sign(alu_1_zero[1]),
    .zero(alu_1_zero[0]), .carry(alu_1_zero[2]), .out(alu_1_out), .b(dbgB), .a(dbgA));
  Inc8 inc8_2 (.in(reg8_4_out), .out(inc8_2_out), .cin(1'b1), .add_sub(1'b0));  // open: cout
  Reg8 reg8_4 (
    .in(inc8_2_out), .dbg(dbgSP), .r(1'b1), .w(and_6_out), .en(1'b1), .clk(bus_clk), .rst(bus_rst),
    .out(reg8_4_out));
  and and_6 (and_6_out, 1'b0, ifetch_exec_q);
  Reg8 reg8_5 (
    .in({bcdinc_1_out, bcdinc_2_out}), .dbg({cycles_3, cycles_2}), .r(1'b1), .w(1'b1), .en(1'b1),
    .clk(ifetch_exec_qn), .rst(bus_rst), .out(reg8_5_out));
  BCDinc bcdinc_1 (.cin(bcdinc_2_cout), .out(bcdinc_1_out), .in(reg8_5_out[7:4]));  // open: cout
  BCDinc bcdinc_2 (.cout(bcdinc_2_cout), .cin(bcdinc_3_cout), .out(bcdinc_2_out), .in(reg8_5_out[3:0]));
  Reg8 reg8_6 (
    .in({bcdinc_3_out, bcdinc_4_out}), .dbg({cycles_1, cycles_0}), .r(1'b1), .w(1'b1), .en(1'b1),
    .clk(ifetch_exec_qn), .rst(bus_rst), .out(reg8_6_out));
  BCDinc bcdinc_3 (.cout(bcdinc_3_cout), .cin(bcdinc_4_cout), .out(bcdinc_3_out), .in(reg8_6_out[7:4]));
  BCDinc bcdinc_4 (.cout(bcdinc_4_cout), .cin(1'b1), .out(bcdinc_4_out), .in(reg8_6_out[3:0]));

  assign dbgADDR = {addr_9, addr_8, addr_7, addr_6, addr_5, addr_4, addr_3, addr_2, addr_1, addr_0};
  assign dbgFR[7] = manual;
  assign dbgIN = {in_7, in_6, in_5, in_4, in_3, in_2, in_1, in_0};
  assign out_0 = dbgOUT[0];
  assign out_1 = dbgOUT[1];
  assign out_2 = dbgOUT[2];
  assign out_3 = dbgOUT[3];
  assign out_4 = dbgOUT[4];
  assign out_5 = dbgOUT[5];
  assign out_6 = dbgOUT[6];
  assign out_7 = dbgOUT[7];

  // Other names for the same wires on the sheet: A[7:0] = dbgA;
  //   ADDR[9:0] = {addr_9, addr_8, addr_7, addr_6, addr_5, addr_4, addr_3, addr_2, addr_1, addr_0}; B[7:0] = dbgB;
  //   D[7:0] = dbgD; FR[3:0] = dbgFR[3:0]; IX_t[1:0] = dbgFR[5:4]; HALT_t = dbgFR[6]; MAN = manual;
  //   IN[7:0] = {in_7, in_6, in_5, in_4, in_3, in_2, in_1, in_0}; IR[7:0] = dbgIR; NPC[7:0] = dbgNPC;
  //   OUT[7:0] = dbgOUT; PC[7:0] = dbgPC; R0[7:0] = dbgR0; R1[7:0] = dbgR1; R2[7:0] = dbgR2; R3[7:0] = dbgR3;
  //   SP[7:0] = dbgSP
endmodule

module LED8 (
  input  [7:0] in,
  output _7,
  output _6,
  output _5,
  output _4,
  output _3,
  output _2,
  output _1,
  output _0
);


  assign _0 = in[0];
  assign _1 = in[1];
  assign _2 = in[2];
  assign _3 = in[3];
  assign _4 = in[4];
  assign _5 = in[5];
  assign _6 = in[6];
  assign _7 = in[7];
endmodule

module LED10 (
  input  [9:0] in,
  output _9,
  output _8,
  output _7,
  output _6,
  output _5,
  output _4,
  output _3,
  output _2,
  output _1,
  output _0
);


  assign _0 = in[0];
  assign _1 = in[1];
  assign _2 = in[2];
  assign _3 = in[3];
  assign _4 = in[4];
  assign _5 = in[5];
  assign _6 = in[6];
  assign _7 = in[7];
  assign _8 = in[8];
  assign _9 = in[9];
endmodule

module _7SegDisplay (
  input  [3:0] BCD,
  output a,
  output b,
  output c,
  output d,
  output e,
  output f,
  output g,
  output dp
);

  wire decoder_1_out0, decoder_1_out1, decoder_1_out2, decoder_1_out3, decoder_1_out4, decoder_1_out5,
       decoder_1_out6, decoder_1_out7, decoder_1_out8, decoder_1_out9;

  Decoder #(.select(4), .enable("false")) decoder_1 (
    .out0(decoder_1_out0), .out1(decoder_1_out1), .out2(decoder_1_out2), .out3(decoder_1_out3),
    .out4(decoder_1_out4), .out5(decoder_1_out5), .out6(decoder_1_out6), .out7(decoder_1_out7),
    .out8(decoder_1_out8), .out9(decoder_1_out9), .sel(BCD));  // open: out10, out11, out12, out13, out14, out15
  or or_1 (a, decoder_1_out9, decoder_1_out8, decoder_1_out7, decoder_1_out6, decoder_1_out5, 1'b0, decoder_1_out3, decoder_1_out2, 1'b0, decoder_1_out0);
  or or_2 (b, decoder_1_out9, decoder_1_out8, decoder_1_out7, 1'b0, 1'b0, decoder_1_out4, decoder_1_out3, decoder_1_out2, decoder_1_out1, decoder_1_out0);
  or or_3 (c, decoder_1_out9, decoder_1_out8, decoder_1_out7, decoder_1_out6, decoder_1_out5, decoder_1_out4, decoder_1_out3, 1'b0, decoder_1_out1, decoder_1_out0);
  or or_4 (d, decoder_1_out9, decoder_1_out8, 1'b0, decoder_1_out6, decoder_1_out5, 1'b0, decoder_1_out3, decoder_1_out2, 1'b0, decoder_1_out0);
  or or_5 (e, 1'b0, decoder_1_out8, 1'b0, decoder_1_out6, 1'b0, 1'b0, 1'b0, decoder_1_out2, 1'b0, decoder_1_out0);
  or or_6 (f, decoder_1_out9, decoder_1_out8, 1'b0, decoder_1_out6, decoder_1_out5, decoder_1_out4, 1'b0, 1'b0, 1'b0, decoder_1_out0);
  or or_7 (g, decoder_1_out9, decoder_1_out8, 1'b0, decoder_1_out6, decoder_1_out5, decoder_1_out4, decoder_1_out3, decoder_1_out2, 1'b0, 1'b0);
  or or_8 (dp, 1'b0, 1'b0, 1'b0, 1'b0, 1'b0, 1'b0, 1'b0, 1'b0, 1'b0, 1'b0);
endmodule

module BCDinc (
  input  [3:0] in,
  input  cin,
  output cout,
  output [3:0] out
);

  wire and_1_out, and_2_out, fulladder_1_cout, fulladder_1_sum, fulladder_3_cout, fulladder_3_sum,
       fulladder_4_cout, fulladder_5_cout, fulladder_5_sum, fulladder_6_cout, fulladder_7_cout,
       fulladder_8_cout, fulladder_8_sum;

  or or_1 (cout, fulladder_1_cout, and_1_out, and_2_out);
  FullAdder fulladder_1 (.a(in[3]), .b(1'b0), .cin(fulladder_3_cout), .sum(fulladder_1_sum), .cout(fulladder_1_cout));
  and and_1 (and_1_out, fulladder_5_sum, fulladder_1_sum);
  and and_2 (and_2_out, fulladder_3_sum, fulladder_1_sum);
  FullAdder fulladder_2 (.a(fulladder_1_sum), .b(1'b0), .cin(fulladder_4_cout), .sum(out[3]));  // open: cout
  FullAdder fulladder_3 (.a(in[2]), .b(1'b0), .cin(fulladder_5_cout), .sum(fulladder_3_sum), .cout(fulladder_3_cout));
  FullAdder fulladder_4 (.a(fulladder_3_sum), .b(cout), .cin(fulladder_7_cout), .sum(out[2]), .cout(fulladder_4_cout));
  FullAdder fulladder_5 (.a(in[1]), .b(1'b0), .cin(fulladder_8_cout), .sum(fulladder_5_sum), .cout(fulladder_5_cout));
  FullAdder fulladder_6 (.a(fulladder_8_sum), .b(1'b0), .cin(1'b0), .sum(out[0]), .cout(fulladder_6_cout));
  FullAdder fulladder_7 (.a(fulladder_5_sum), .b(cout), .cin(fulladder_6_cout), .sum(out[1]), .cout(fulladder_7_cout));
  FullAdder fulladder_8 (.a(in[0]), .b(1'b0), .cin(cin), .sum(fulladder_8_sum), .cout(fulladder_8_cout));
endmodule

module MemoryUnit (
  input  addr_0,
  input  in_0,
  input  addr_1,
  input  in_1,
  input  addr_2,
  input  in_2,
  input  addr_3,
  input  in_3,
  input  addr_4,
  input  in_4,
  input  addr_5,
  input  in_5,
  input  addr_6,
  input  in_6,
  input  addr_7,
  input  in_7,
  input  addr_8,
  input  addr_9,
  input  en,
  input  ld_str,
  input  [7:0] mem0_in,
  input  [7:0] mem1_in,
  input  [7:0] mem2_in,
  input  [7:0] mem3_in,
  input  clk,
  input  rst,
  output out_0,
  output out_1,
  output out_2,
  output out_3,
  output out_4,
  output out_5,
  output out_6,
  output out_7,
  output [7:0] mem0_addr,
  output [7:0] mem0_out,
  output mem0_en,
  output mem0_ld,
  output mem0_str,
  output mem0_clk,
  output mem0_rst,
  output [7:0] mem1_addr,
  output [7:0] mem1_out,
  output mem1_en,
  output mem1_ld,
  output mem1_str,
  output mem1_clk,
  output mem1_rst,
  output [7:0] mem2_addr,
  output [7:0] mem2_out,
  output mem2_en,
  output mem2_ld,
  output mem2_str,
  output mem2_clk,
  output mem2_rst,
  output [7:0] mem3_addr,
  output [7:0] mem3_out,
  output mem3_en,
  output mem3_ld,
  output mem3_str,
  output mem3_clk,
  output mem3_rst
);

  wire and_1_out, decoder_1_out0, decoder_1_out1, decoder_1_out2, decoder_1_out3, not_1_out, not_2_out,
       not_3_out, not_4_out;

  Decoder #(.select(2), .enable("false")) decoder_1 (
    .out0(decoder_1_out0), .out1(decoder_1_out1), .out2(decoder_1_out2), .out3(decoder_1_out3),
    .sel({addr_9, addr_8}));
  not not_1 (not_1_out, ld_str);
  not not_2 (not_2_out, ld_str);
  not not_3 (not_3_out, ld_str);
  not not_4 (not_4_out, ld_str);
  and and_1 (and_1_out, en, ~ld_str);  // AND_Gate
  and and_2 (mem0_en, en, decoder_1_out0);
  and and_3 (mem1_en, en, decoder_1_out1);
  and and_4 (mem2_en, en, decoder_1_out2);
  and and_5 (mem3_en, en, decoder_1_out3);
  and and_6 (mem0_ld, mem0_en, not_1_out);
  and and_7 (mem0_str, mem0_en, ld_str);
  and and_8 (mem0_clk, mem0_en, clk);
  and and_9 (mem1_ld, mem1_en, not_2_out);
  and and_10 (mem1_str, mem1_en, ld_str);
  and and_11 (mem1_clk, mem1_en, clk);
  and and_12 (mem2_ld, mem2_en, not_3_out);
  and and_13 (mem2_str, mem2_en, ld_str);
  and and_14 (mem2_clk, mem2_en, clk);
  and and_15 (mem3_ld, mem3_en, not_4_out);
  and and_16 (mem3_str, mem3_en, ld_str);
  and and_17 (mem3_clk, mem3_en, clk);
  Multiplexer #(.select(2), .width(8)) multiplexer_1 (
    .in0(mem0_in), .in1(mem1_in), .in2(mem2_in), .in3(mem3_in),
    .out({out_7, out_6, out_5, out_4, out_3, out_2, out_1, out_0}), .sel({addr_9, addr_8}), .en(and_1_out));
  assign mem0_addr = mem0_en ? {addr_7, addr_6, addr_5, addr_4, addr_3, addr_2, addr_1, addr_0} : 8'bz;  // Controlled_Buffer controlled_buffer_1
  assign mem1_addr = mem1_en ? {addr_7, addr_6, addr_5, addr_4, addr_3, addr_2, addr_1, addr_0} : 8'bz;  // Controlled_Buffer controlled_buffer_2
  assign mem2_addr = mem2_en ? {addr_7, addr_6, addr_5, addr_4, addr_3, addr_2, addr_1, addr_0} : 8'bz;  // Controlled_Buffer controlled_buffer_3
  assign mem3_addr = mem3_en ? {addr_7, addr_6, addr_5, addr_4, addr_3, addr_2, addr_1, addr_0} : 8'bz;  // Controlled_Buffer controlled_buffer_4
  assign mem0_out = mem0_str ? {in_7, in_6, in_5, in_4, in_3, in_2, in_1, in_0} : 8'bz;  // Controlled_Buffer controlled_buffer_5
  assign mem1_out = mem1_str ? {in_7, in_6, in_5, in_4, in_3, in_2, in_1, in_0} : 8'bz;  // Controlled_Buffer controlled_buffer_6
  assign mem2_out = mem2_str ? {in_7, in_6, in_5, in_4, in_3, in_2, in_1, in_0} : 8'bz;  // Controlled_Buffer controlled_buffer_7
  assign mem3_out = mem3_str ? {in_7, in_6, in_5, in_4, in_3, in_2, in_1, in_0} : 8'bz;  // Controlled_Buffer controlled_buffer_8

  assign mem0_rst = rst;
  assign mem1_rst = rst;
  assign mem2_rst = rst;
  assign mem3_rst = rst;
endmodule

module RegFile (
  input  [7:0] rd,
  input  reg_w,
  input  selRD0,
  input  selRD1,
  input  clk,
  input  rst,
  input  selRA0,
  input  selRA1,
  input  selRB0,
  input  selRB1,
  output [7:0] dbgR0,
  output [7:0] dbgR1,
  output [7:0] dbgR2,
  output [7:0] dbgR3,
  output [7:0] ra,
  output [7:0] rb
);

  wire and_1_out, and_2_out, and_3_out, and_4_out, decoder_1_out0, decoder_1_out1, decoder_1_out2,
       decoder_1_out3;
  wire [7:0] reg8_1_out, reg8_2_out, reg8_3_out, reg8_4_out;

  Decoder #(.select(2), .enable("false")) decoder_1 (
    .out0(decoder_1_out0), .out1(decoder_1_out1), .out2(decoder_1_out2), .out3(decoder_1_out3),
    .sel({selRD1, selRD0}));
  and and_1 (and_1_out, reg_w, decoder_1_out0);
  Reg8 reg8_1 (.in(rd), .dbg(dbgR0), .r(1'b1), .w(and_1_out), .en(1'b1), .clk(clk), .rst(rst), .out(reg8_1_out));
  and and_2 (and_2_out, reg_w, decoder_1_out1);
  Reg8 reg8_2 (.in(rd), .dbg(dbgR1), .r(1'b1), .w(and_2_out), .en(1'b1), .clk(clk), .rst(rst), .out(reg8_2_out));
  Reg8 reg8_3 (.in(rd), .dbg(dbgR2), .r(1'b1), .w(and_3_out), .en(1'b1), .clk(clk), .rst(rst), .out(reg8_3_out));
  and and_3 (and_3_out, reg_w, decoder_1_out2);
  Reg8 reg8_4 (.in(rd), .dbg(dbgR3), .r(1'b1), .w(and_4_out), .en(1'b1), .clk(clk), .rst(rst), .out(reg8_4_out));
  and and_4 (and_4_out, reg_w, decoder_1_out3);
  Multiplexer #(.select(2), .width(8), .enable("false")) multiplexer_1 (
    .in0(reg8_4_out), .in1(reg8_3_out), .in2(reg8_2_out), .in3(reg8_1_out), .out(ra), .sel({selRA1, selRA0}));
  Multiplexer #(.select(2), .width(8), .enable("false")) multiplexer_2 (
    .in0(reg8_4_out), .in1(reg8_3_out), .in2(reg8_2_out), .in3(reg8_1_out), .out(rb), .sel({selRB1, selRB0}));
endmodule

module RegMux (
  input  muxRA,
  input  [7:0] RAin0,
  input  [7:0] RAin1,
  input  muxRB,
  input  [7:0] RBin0,
  input  [7:0] RBin1,
  input  muxRD1,
  input  muxRD0,
  input  [7:0] RDin0,
  input  [7:0] RDin1,
  input  [7:0] RDin2,
  output [7:0] RAout,
  output [7:0] RBout,
  output [7:0] RDout
);

  wire [7:0] multiplexer_3_out;

  Multiplexer #(.width(8), .enable("false")) multiplexer_1 (.in0(RAin0), .in1(RAin1), .out(RAout), .sel(muxRA));
  Multiplexer #(.width(8), .enable("false")) multiplexer_2 (.in0(RBin0), .in1(RBin1), .out(RBout), .sel(muxRB));
  Multiplexer #(.width(8), .enable("false")) multiplexer_3 (
    .in0(RDin0), .in1(RDin1), .out(multiplexer_3_out), .sel(muxRD0));
  Multiplexer #(.width(8), .enable("false")) multiplexer_4 (
    .in0(multiplexer_3_out), .in1(RDin2), .out(RDout), .sel(muxRD1));
endmodule

module Reg4 (
  input  [3:0] in_3__0,
  input  r,
  input  w,
  input  en,
  input  clk,
  input  rst,
  output [3:0] dbg_3__0,
  output [3:0] out_3__0
);

  wire and_1_out, and_2_out, and_3_out, and_4_out, multiplexer_1_out, multiplexer_2_out, multiplexer_3_out,
       multiplexer_4_out, nand_1_out, nand_2_out, nand_3_out, nand_4_out;

  Multiplexer #(.enable("false")) multiplexer_1 (
    .in0(in_3__0[3]), .in1(dbg_3__0[3]), .out(multiplexer_1_out), .sel(nand_1_out));
  nand nand_1 (nand_1_out, w, en);
  D_Flip_Flop d_ff_1 (
    .clk(clk), .D(multiplexer_1_out), .Q(dbg_3__0[3]), .preset(1'b0), .en(en), .reset(rst));  // open: Qn
  assign out_3__0[3] = and_1_out ? dbg_3__0[3] : 1'bz;  // Controlled_Buffer controlled_buffer_1
  nand nand_2 (nand_2_out, w, en);
  and and_1 (and_1_out, r, en);
  Multiplexer #(.enable("false")) multiplexer_2 (
    .in0(in_3__0[2]), .in1(dbg_3__0[2]), .out(multiplexer_2_out), .sel(nand_2_out));
  D_Flip_Flop d_ff_2 (
    .clk(clk), .D(multiplexer_2_out), .Q(dbg_3__0[2]), .preset(1'b0), .en(en), .reset(rst));  // open: Qn
  assign out_3__0[2] = and_2_out ? dbg_3__0[2] : 1'bz;  // Controlled_Buffer controlled_buffer_2
  nand nand_3 (nand_3_out, w, en);
  and and_2 (and_2_out, r, en);
  Multiplexer #(.enable("false")) multiplexer_3 (
    .in0(in_3__0[1]), .in1(dbg_3__0[1]), .out(multiplexer_3_out), .sel(nand_3_out));
  D_Flip_Flop d_ff_3 (
    .clk(clk), .D(multiplexer_3_out), .Q(dbg_3__0[1]), .preset(1'b0), .en(en), .reset(rst));  // open: Qn
  assign out_3__0[1] = and_3_out ? dbg_3__0[1] : 1'bz;  // Controlled_Buffer controlled_buffer_3
  and and_3 (and_3_out, r, en);
  Multiplexer #(.enable("false")) multiplexer_4 (
    .in0(in_3__0[0]), .in1(dbg_3__0[0]), .out(multiplexer_4_out), .sel(nand_4_out));
  nand nand_4 (nand_4_out, w, en);
  assign out_3__0[0] = and_4_out ? dbg_3__0[0] : 1'bz;  // Controlled_Buffer controlled_buffer_4
  D_Flip_Flop d_ff_4 (
    .clk(clk), .D(multiplexer_4_out), .Q(dbg_3__0[0]), .preset(1'b0), .en(en), .reset(rst));  // open: Qn
  and and_4 (and_4_out, r, en);
endmodule

module Reg8 (
  input  [7:0] in,
  input  r,
  input  w,
  input  en,
  input  clk,
  input  rst,
  output [7:0] dbg,
  output [7:0] out
);

  wire and_1_out, and_2_out, and_3_out, and_4_out, and_5_out, and_6_out, and_7_out, and_8_out,
       multiplexer_1_out, multiplexer_2_out, multiplexer_3_out, multiplexer_4_out, multiplexer_5_out,
       multiplexer_6_out, multiplexer_7_out, multiplexer_8_out, nand_1_out, nand_2_out, nand_3_out,
       nand_4_out, nand_5_out, nand_6_out, nand_7_out, nand_8_out;

  nand nand_1 (nand_1_out, w, en);
  Multiplexer #(.enable("false")) multiplexer_1 (.in0(in[7]), .in1(dbg[7]), .out(multiplexer_1_out), .sel(nand_1_out));
  D_Flip_Flop d_ff_1 (.clk(clk), .D(multiplexer_1_out), .Q(dbg[7]), .preset(1'b0), .en(en), .reset(rst));  // open: Qn
  assign out[7] = and_1_out ? dbg[7] : 1'bz;  // Controlled_Buffer controlled_buffer_1
  nand nand_2 (nand_2_out, w, en);
  and and_1 (and_1_out, r, en);
  Multiplexer #(.enable("false")) multiplexer_2 (.in0(in[6]), .in1(dbg[6]), .out(multiplexer_2_out), .sel(nand_2_out));
  D_Flip_Flop d_ff_2 (.clk(clk), .D(multiplexer_2_out), .Q(dbg[6]), .preset(1'b0), .en(en), .reset(rst));  // open: Qn
  assign out[6] = and_2_out ? dbg[6] : 1'bz;  // Controlled_Buffer controlled_buffer_2
  and and_2 (and_2_out, r, en);
  Multiplexer #(.enable("false")) multiplexer_3 (.in0(in[5]), .in1(dbg[5]), .out(multiplexer_3_out), .sel(nand_3_out));
  nand nand_3 (nand_3_out, w, en);
  D_Flip_Flop d_ff_3 (.clk(clk), .D(multiplexer_3_out), .Q(dbg[5]), .preset(1'b0), .en(en), .reset(rst));  // open: Qn
  assign out[5] = and_3_out ? dbg[5] : 1'bz;  // Controlled_Buffer controlled_buffer_3
  and and_3 (and_3_out, r, en);
  Multiplexer #(.enable("false")) multiplexer_4 (.in0(in[4]), .in1(dbg[4]), .out(multiplexer_4_out), .sel(nand_4_out));
  nand nand_4 (nand_4_out, w, en);
  D_Flip_Flop d_ff_4 (.clk(clk), .D(multiplexer_4_out), .Q(dbg[4]), .preset(1'b0), .en(en), .reset(rst));  // open: Qn
  assign out[4] = and_4_out ? dbg[4] : 1'bz;  // Controlled_Buffer controlled_buffer_4
  and and_4 (and_4_out, r, en);
  Multiplexer #(.enable("false")) multiplexer_5 (.in0(in[3]), .in1(dbg[3]), .out(multiplexer_5_out), .sel(nand_5_out));
  nand nand_5 (nand_5_out, w, en);
  D_Flip_Flop d_ff_5 (.clk(clk), .D(multiplexer_5_out), .Q(dbg[3]), .preset(1'b0), .en(en), .reset(rst));  // open: Qn
  assign out[3] = and_5_out ? dbg[3] : 1'bz;  // Controlled_Buffer controlled_buffer_5
  and and_5 (and_5_out, r, en);
  Multiplexer #(.enable("false")) multiplexer_6 (.in0(in[2]), .in1(dbg[2]), .out(multiplexer_6_out), .sel(nand_6_out));
  nand nand_6 (nand_6_out, w, en);
  assign out[2] = and_6_out ? dbg[2] : 1'bz;  // Controlled_Buffer controlled_buffer_6
  D_Flip_Flop d_ff_6 (.clk(clk), .D(multiplexer_6_out), .Q(dbg[2]), .preset(1'b0), .en(en), .reset(rst));  // open: Qn
  and and_6 (and_6_out, r, en);
  Multiplexer #(.enable("false")) multiplexer_7 (.in0(in[1]), .in1(dbg[1]), .out(multiplexer_7_out), .sel(nand_7_out));
  nand nand_7 (nand_7_out, w, en);
  D_Flip_Flop d_ff_7 (.clk(clk), .D(multiplexer_7_out), .Q(dbg[1]), .preset(1'b0), .en(en), .reset(rst));  // open: Qn
  and and_7 (and_7_out, r, en);
  Multiplexer #(.enable("false")) multiplexer_8 (.in0(in[0]), .in1(dbg[0]), .out(multiplexer_8_out), .sel(nand_8_out));
  assign out[1] = and_7_out ? dbg[1] : 1'bz;  // Controlled_Buffer controlled_buffer_7
  nand nand_8 (nand_8_out, w, en);
  D_Flip_Flop d_ff_8 (.clk(clk), .D(multiplexer_8_out), .Q(dbg[0]), .preset(1'b0), .en(en), .reset(rst));  // open: Qn
  assign out[0] = and_8_out ? dbg[0] : 1'bz;  // Controlled_Buffer controlled_buffer_8
  and and_8 (and_8_out, r, en);
endmodule

module ALU_2 (
  input  [7:0] a,
  input  [7:0] b,
  input  op2,
  input  op1,
  input  op0,
  input  cin,
  output [7:0] out,
  output overflow,
  output carry,
  output sign,
  output zero
);

  wire addsub8_1_carry, addsub8_1_out0, addsub8_1_out1, addsub8_1_out2, addsub8_1_out3, addsub8_1_out4,
       addsub8_1_out5, addsub8_1_out6, addsub8_1_out7, addsub8_1_overflow, ander8_1_out0, ander8_1_out1,
       ander8_1_out2, ander8_1_out3, ander8_1_out4, ander8_1_out5, ander8_1_out6, ander8_1_out7,
       leftshifter8_1_cout, leftshifter8_1_out0, leftshifter8_1_out1, leftshifter8_1_out2,
       leftshifter8_1_out3, leftshifter8_1_out4, leftshifter8_1_out6, leftshifter8_1_out6_2,
       leftshifter8_1_out7, nor_2_out, or_1_out, orer8_1_out0, orer8_1_out1, orer8_1_out2, orer8_1_out3,
       orer8_1_out4, orer8_1_out5, orer8_1_out6, orer8_1_out7, rightshifter8_1_cout, rightshifter8_1_out0,
       rightshifter8_1_out1, rightshifter8_1_out2, rightshifter8_1_out3, rightshifter8_1_out4,
       rightshifter8_1_out6, rightshifter8_1_out6_2, rightshifter8_1_out7, xorer8_1_out0, xorer8_1_out1,
       xorer8_1_out2, xorer8_1_out3, xorer8_1_out4, xorer8_1_out5, xorer8_1_out6, xorer8_1_out7;
  wire [7:0] decoder_1_out0;

  Ander8 ander8_1 (
    .a0(a[0]), .b0(b[0]), .a1(a[1]), .b1(b[1]), .a2(a[2]), .b2(b[2]), .a3(a[3]), .b3(b[3]), .a4(a[4]),
    .b4(b[4]), .a5(a[5]), .b5(b[5]), .a6(a[6]), .b6(b[6]), .a7(a[7]), .b7(b[7]), .out0(ander8_1_out0),
    .out1(ander8_1_out1), .out2(ander8_1_out2), .out3(ander8_1_out3), .out4(ander8_1_out4),
    .out5(ander8_1_out5), .out6(ander8_1_out6), .out7(ander8_1_out7));
  Orer8 orer8_1 (
    .a0(a[0]), .b0(b[0]), .a1(a[1]), .b1(b[1]), .a2(a[2]), .b2(b[2]), .a3(a[3]), .b3(b[3]), .a4(a[4]),
    .b4(b[4]), .a5(a[5]), .b5(b[5]), .a6(a[6]), .b6(b[6]), .a7(a[7]), .b7(b[7]), .out0(orer8_1_out0),
    .out1(orer8_1_out1), .out2(orer8_1_out2), .out3(orer8_1_out3), .out4(orer8_1_out4), .out5(orer8_1_out5),
    .out6(orer8_1_out6), .out7(orer8_1_out7));
  Xorer8 xorer8_1 (
    .a0(a[0]), .b0(b[0]), .a1(a[1]), .b1(b[1]), .a2(a[2]), .b2(b[2]), .a3(a[3]), .b3(b[3]), .a4(a[4]),
    .b4(b[4]), .a5(a[5]), .b5(b[5]), .a6(a[6]), .b6(b[6]), .a7(a[7]), .b7(b[7]), .out0(xorer8_1_out0),
    .out1(xorer8_1_out1), .out2(xorer8_1_out2), .out3(xorer8_1_out3), .out4(xorer8_1_out4),
    .out5(xorer8_1_out5), .out6(xorer8_1_out6), .out7(xorer8_1_out7));
  AddSub8 addsub8_1 (
    .cin(cin), .a0(a[0]), .b0(b[0]), .a1(a[1]), .b1(b[1]), .a2(a[2]), .b2(b[2]), .a3(a[3]), .b3(b[3]),
    .a4(a[4]), .b4(b[4]), .a5(a[5]), .b5(b[5]), .a6(a[6]), .b6(b[6]), .a7(a[7]), .b7(b[7]),
    .out0(addsub8_1_out0), .out1(addsub8_1_out1), .out2(addsub8_1_out2), .out3(addsub8_1_out3),
    .out4(addsub8_1_out4), .out5(addsub8_1_out5), .out6(addsub8_1_out6), .out7(addsub8_1_out7),
    .carry(addsub8_1_carry), .sub(decoder_1_out0[5]), .overflow(addsub8_1_overflow));
  LeftShifter8 leftshifter8_1 (
    .cin(cin), .in0(b[0]), .in1(b[1]), .in2(b[2]), .in3(b[3]), .in4(b[4]), .in5(b[5]), .in6(b[6]),
    .in7(b[7]), .out0(leftshifter8_1_out0), .out1(leftshifter8_1_out1), .out2(leftshifter8_1_out2),
    .out3(leftshifter8_1_out3), .out4(leftshifter8_1_out4), .out6(leftshifter8_1_out6),
    .out6_2(leftshifter8_1_out6_2), .out7(leftshifter8_1_out7), .cout(leftshifter8_1_cout));
  RightShifter8 rightshifter8_1 (
    .in0(b[0]), .in1(b[1]), .in2(b[2]), .in3(b[3]), .in4(b[4]), .in5(b[5]), .in6(b[6]), .in7(b[7]),
    .cin(cin), .cout(rightshifter8_1_cout), .out0(rightshifter8_1_out0), .out1(rightshifter8_1_out1),
    .out2(rightshifter8_1_out2), .out3(rightshifter8_1_out3), .out4(rightshifter8_1_out4),
    .out6(rightshifter8_1_out6), .out6_2(rightshifter8_1_out6_2), .out7(rightshifter8_1_out7));
  Decoder #(.select(3), .enable("false")) decoder_1 (
    .out0(decoder_1_out0[0]), .out1(decoder_1_out0[1]), .out2(decoder_1_out0[2]), .out3(decoder_1_out0[3]),
    .out4(decoder_1_out0[4]), .out5(decoder_1_out0[5]), .out6(decoder_1_out0[6]), .out7(decoder_1_out0[7]),
    .sel({op2, op1, op0}));
  Enabler8 enabler8_1 (
    .in0(b[0]), .in1(b[1]), .in2(b[2]), .in3(b[3]), .in4(b[4]), .in5(b[5]), .in6(b[6]), .in7(b[7]),
    .enable(decoder_1_out0[0]), .out0(out[0]), .out1(out[1]), .out2(out[2]), .out3(out[3]), .out4(out[4]),
    .out6(out[5]), .out6_2(out[6]), .out7(out[7]));
  Enabler8 enabler8_2 (
    .in0(ander8_1_out0), .in1(ander8_1_out1), .in2(ander8_1_out2), .in3(ander8_1_out3), .in4(ander8_1_out4),
    .in5(ander8_1_out5), .in6(ander8_1_out6), .in7(ander8_1_out7), .enable(decoder_1_out0[1]), .out0(out[0]),
    .out1(out[1]), .out2(out[2]), .out3(out[3]), .out4(out[4]), .out6(out[5]), .out6_2(out[6]), .out7(out[7]));
  Enabler8 enabler8_3 (
    .in0(orer8_1_out0), .in1(orer8_1_out1), .in2(orer8_1_out2), .in3(orer8_1_out3), .in4(orer8_1_out4),
    .in5(orer8_1_out5), .in6(orer8_1_out6), .in7(orer8_1_out7), .enable(decoder_1_out0[2]), .out0(out[0]),
    .out1(out[1]), .out2(out[2]), .out3(out[3]), .out4(out[4]), .out6(out[5]), .out6_2(out[6]), .out7(out[7]));
  Enabler8 enabler8_4 (
    .in0(xorer8_1_out0), .in1(xorer8_1_out1), .in2(xorer8_1_out2), .in3(xorer8_1_out3), .in4(xorer8_1_out4),
    .in5(xorer8_1_out5), .in6(xorer8_1_out6), .in7(xorer8_1_out7), .enable(decoder_1_out0[3]), .out0(out[0]),
    .out1(out[1]), .out2(out[2]), .out3(out[3]), .out4(out[4]), .out6(out[5]), .out6_2(out[6]), .out7(out[7]));
  or or_1 (or_1_out, decoder_1_out0[4], decoder_1_out0[5]);
  Enabler8 enabler8_5 (
    .in0(addsub8_1_out0), .in1(addsub8_1_out1), .in2(addsub8_1_out2), .in3(addsub8_1_out3),
    .in4(addsub8_1_out4), .in5(addsub8_1_out5), .in6(addsub8_1_out6), .in7(addsub8_1_out7),
    .enable(or_1_out), .out0(out[0]), .out1(out[1]), .out2(out[2]), .out3(out[3]), .out4(out[4]),
    .out6(out[5]), .out6_2(out[6]), .out7(out[7]));
  Enabler8 enabler8_6 (
    .in0(leftshifter8_1_out0), .in1(leftshifter8_1_out1), .in2(leftshifter8_1_out2),
    .in3(leftshifter8_1_out3), .in4(leftshifter8_1_out4), .in5(leftshifter8_1_out6),
    .in6(leftshifter8_1_out6_2), .in7(leftshifter8_1_out7), .enable(decoder_1_out0[6]), .out0(out[0]),
    .out1(out[1]), .out2(out[2]), .out3(out[3]), .out4(out[4]), .out6(out[5]), .out6_2(out[6]), .out7(out[7]));
  Enabler8 enabler8_7 (
    .in0(rightshifter8_1_out0), .in1(rightshifter8_1_out1), .in2(rightshifter8_1_out2),
    .in3(rightshifter8_1_out3), .in4(rightshifter8_1_out4), .in5(rightshifter8_1_out6),
    .in6(rightshifter8_1_out6_2), .in7(rightshifter8_1_out7), .enable(decoder_1_out0[7]), .out0(out[0]),
    .out1(out[1]), .out2(out[2]), .out3(out[3]), .out4(out[4]), .out6(out[5]), .out6_2(out[6]), .out7(out[7]));
  nor nor_1 (zero, out[7], out[6], out[5], out[4], out[3], out[2], out[1], out[0]);
  Multiplexer #(.enable("false")) multiplexer_1 (.in0(1'b0), .in1(addsub8_1_overflow), .out(overflow), .sel(or_1_out));
  nor nor_2 (nor_2_out, or_1_out, decoder_1_out0[6], decoder_1_out0[7]);
  assign carry = nor_2_out ? 1'b0 : 1'bz;  // Controlled_Buffer controlled_buffer_1
  assign carry = or_1_out ? addsub8_1_carry : 1'bz;  // Controlled_Buffer controlled_buffer_2
  assign carry = decoder_1_out0[6] ? leftshifter8_1_cout : 1'bz;  // Controlled_Buffer controlled_buffer_3
  assign carry = decoder_1_out0[7] ? rightshifter8_1_cout : 1'bz;  // Controlled_Buffer controlled_buffer_4

  assign sign = out[7];
endmodule

module Enabler8 (
  input  enable,
  input  in0,
  input  in1,
  input  in2,
  input  in3,
  input  in4,
  input  in5,
  input  in6,
  input  in7,
  output out0,
  output out1,
  output out2,
  output out3,
  output out4,
  output out6,
  output out6_2,
  output out7
);

  assign out0 = enable ? in0 : 1'bz;  // Controlled_Buffer controlled_buffer_1
  assign out1 = enable ? in1 : 1'bz;  // Controlled_Buffer controlled_buffer_2
  assign out2 = enable ? in2 : 1'bz;  // Controlled_Buffer controlled_buffer_3
  assign out3 = enable ? in3 : 1'bz;  // Controlled_Buffer controlled_buffer_4
  assign out4 = enable ? in4 : 1'bz;  // Controlled_Buffer controlled_buffer_5
  assign out6 = enable ? in5 : 1'bz;  // Controlled_Buffer controlled_buffer_6
  assign out6_2 = enable ? in6 : 1'bz;  // Controlled_Buffer controlled_buffer_7
  assign out7 = enable ? in7 : 1'bz;  // Controlled_Buffer controlled_buffer_8
endmodule

module LeftShifter8 (
  input  cin,
  input  in0,
  input  in1,
  input  in2,
  input  in3,
  input  in4,
  input  in5,
  input  in6,
  input  in7,
  output out0,
  output out1,
  output out2,
  output out3,
  output out4,
  output out6,
  output out6_2,
  output out7,
  output cout
);


  assign cout = in7;
  assign out0 = cin;
  assign out1 = in0;
  assign out2 = in1;
  assign out3 = in2;
  assign out4 = in3;
  assign out6 = in4;
  assign out6_2 = in5;
  assign out7 = in6;
endmodule

module RightShifter8 (
  input  in0,
  input  in1,
  input  in2,
  input  in3,
  input  in4,
  input  in5,
  input  in6,
  input  in7,
  input  cin,
  output cout,
  output out0,
  output out1,
  output out2,
  output out3,
  output out4,
  output out6,
  output out6_2,
  output out7
);


  assign cout = in0;
  assign out0 = in1;
  assign out1 = in2;
  assign out2 = in3;
  assign out3 = in4;
  assign out4 = in5;
  assign out6 = in6;
  assign out6_2 = in7;
  assign out7 = cin;
endmodule

module Notter8 (
  input  in0,
  input  in1,
  input  in2,
  input  in3,
  input  in4,
  input  in5,
  input  in6,
  input  in7,
  output out0,
  output out1,
  output out2,
  output out3,
  output out4,
  output out6,
  output out6_2,
  output out7
);

  not not_1 (out0, in0);
  not not_2 (out1, in1);
  not not_3 (out2, in2);
  not not_4 (out3, in3);
  not not_5 (out4, in4);
  not not_6 (out6, in5);
  not not_7 (out6_2, in6);
  not not_8 (out7, in7);
endmodule

module Ander8 (
  input  a0,
  input  b0,
  input  a1,
  input  b1,
  input  a2,
  input  b2,
  input  a3,
  input  b3,
  input  a4,
  input  b4,
  input  a5,
  input  b5,
  input  a6,
  input  b6,
  input  a7,
  input  b7,
  output out0,
  output out1,
  output out2,
  output out3,
  output out4,
  output out5,
  output out6,
  output out7
);

  and and_1 (out0, a0, b0);
  and and_2 (out1, a1, b1);
  and and_3 (out2, a2, b2);
  and and_4 (out3, a3, b3);
  and and_5 (out4, a4, b4);
  and and_6 (out5, a5, b5);
  and and_7 (out6, a6, b6);
  and and_8 (out7, a7, b7);
endmodule

module Orer8 (
  input  a0,
  input  b0,
  input  a1,
  input  b1,
  input  a2,
  input  b2,
  input  a3,
  input  b3,
  input  a4,
  input  b4,
  input  a5,
  input  b5,
  input  a6,
  input  b6,
  input  a7,
  input  b7,
  output out0,
  output out1,
  output out2,
  output out3,
  output out4,
  output out5,
  output out6,
  output out7
);

  or or_1 (out0, a0, b0);
  or or_2 (out1, a1, b1);
  or or_3 (out2, a2, b2);
  or or_4 (out3, a3, b3);
  or or_5 (out4, a4, b4);
  or or_6 (out5, a5, b5);
  or or_7 (out6, a6, b6);
  or or_8 (out7, a7, b7);
endmodule

module Xorer8 (
  input  a0,
  input  b0,
  input  a1,
  input  b1,
  input  a2,
  input  b2,
  input  a3,
  input  b3,
  input  a4,
  input  b4,
  input  a5,
  input  b5,
  input  a6,
  input  b6,
  input  a7,
  input  b7,
  output out0,
  output out1,
  output out2,
  output out3,
  output out4,
  output out5,
  output out6,
  output out7
);

  xor xor_1 (out0, a0, b0);
  xor xor_2 (out1, a1, b1);
  xor xor_3 (out2, a2, b2);
  xor xor_4 (out3, a3, b3);
  xor xor_5 (out4, a4, b4);
  xor xor_6 (out5, a5, b5);
  xor xor_7 (out6, a6, b6);
  xor xor_8 (out7, a7, b7);
endmodule

module FullAdder (
  input  a,
  input  b,
  input  cin,
  output sum,
  output cout
);

  wire and_1_out, and_2_out, xor_1_out;

  xor xor_1 (xor_1_out, a, b);
  xor xor_2 (sum, xor_1_out, cin);
  and and_1 (and_1_out, xor_1_out, cin);
  and and_2 (and_2_out, a, b);
  or or_1 (cout, and_1_out, and_2_out);
endmodule

module Adder8 (
  input  cin,
  input  a0,
  input  b0,
  input  a1,
  input  b1,
  input  a2,
  input  b2,
  input  a3,
  input  b3,
  input  a4,
  input  b4,
  input  a5,
  input  b5,
  input  a6,
  input  b6,
  input  a7,
  input  b7,
  output out0,
  output out1,
  output out2,
  output out3,
  output out4,
  output out5,
  output out6,
  output out7,
  output ovcarry,
  output cout
);

  wire fulladder_1_cout, fulladder_2_cout, fulladder_3_cout, fulladder_4_cout, fulladder_5_cout,
       fulladder_6_cout;

  FullAdder fulladder_1 (.a(a0), .b(b0), .cin(cin), .sum(out0), .cout(fulladder_1_cout));
  FullAdder fulladder_2 (.a(a1), .b(b1), .cin(fulladder_1_cout), .sum(out1), .cout(fulladder_2_cout));
  FullAdder fulladder_3 (.a(a2), .b(b2), .cin(fulladder_2_cout), .sum(out2), .cout(fulladder_3_cout));
  FullAdder fulladder_4 (.a(a3), .b(b3), .cin(fulladder_3_cout), .sum(out3), .cout(fulladder_4_cout));
  FullAdder fulladder_5 (.a(a4), .b(b4), .cin(fulladder_4_cout), .sum(out4), .cout(fulladder_5_cout));
  FullAdder fulladder_6 (.a(a5), .b(b5), .cin(fulladder_5_cout), .sum(out5), .cout(fulladder_6_cout));
  FullAdder fulladder_7 (.a(a6), .b(b6), .cin(fulladder_6_cout), .sum(out6), .cout(ovcarry));
  FullAdder fulladder_8 (.a(a7), .b(b7), .cin(ovcarry), .sum(out7), .cout(cout));
endmodule

module AddSub8 (
  input  sub,
  input  a0,
  input  b0,
  input  a1,
  input  b1,
  input  a2,
  input  b2,
  input  a3,
  input  b3,
  input  a4,
  input  b4,
  input  a5,
  input  b5,
  input  a6,
  input  b6,
  input  a7,
  input  b7,
  input  cin,
  output carry,
  output overflow,
  output out7,
  output out6,
  output out5,
  output out4,
  output out3,
  output out2,
  output out1,
  output out0
);

  wire adder8_1_cout, adder8_1_ovcarry, xor_3_out, xor_4_out, xor_5_out, xor_6_out, xor_7_out, xor_8_out,
       xor_9_out, xor_10_out, xor_11_out;

  xor xor_1 (carry, sub, adder8_1_cout);
  xor xor_2 (overflow, adder8_1_ovcarry, adder8_1_cout);
  xor xor_3 (xor_3_out, sub, b0);
  xor xor_4 (xor_4_out, sub, b1);
  xor xor_5 (xor_5_out, sub, b2);
  xor xor_6 (xor_6_out, sub, b3);
  xor xor_7 (xor_7_out, sub, b4);
  xor xor_8 (xor_8_out, sub, b5);
  xor xor_9 (xor_9_out, sub, b6);
  xor xor_10 (xor_10_out, sub, b7);
  Adder8 adder8_1 (
    .cin(xor_11_out), .a0(a0), .b0(xor_3_out), .a1(a1), .b1(xor_4_out), .a2(a2), .b2(xor_5_out), .a3(a3),
    .b3(xor_6_out), .a4(a4), .b4(xor_7_out), .a5(a5), .b5(xor_8_out), .a6(a6), .b6(xor_9_out), .a7(a7),
    .b7(xor_10_out), .out0(out0), .out1(out1), .out2(out2), .out3(out3), .out4(out4), .out5(out5),
    .out6(out6), .out7(out7), .ovcarry(adder8_1_ovcarry), .cout(adder8_1_cout));
  xor xor_11 (xor_11_out, sub, cin);
endmodule

module Inc8 (
  input  cin,
  input  [7:0] in,
  input  add_sub,
  output [7:0] out,
  output cout
);

  wire inc4_1_cout;

  Inc4 inc4_1 (
    .cin(cin), .add_sub(add_sub), .out0(out[0]), .in0(in[0]), .out1(out[1]), .in1(in[1]), .out2(out[2]),
    .in2(in[2]), .out3(out[3]), .in3(in[3]), .cout(inc4_1_cout));
  Inc4 inc4_2 (
    .cin(inc4_1_cout), .add_sub(add_sub), .out0(out[4]), .in0(in[4]), .out1(out[5]), .in1(in[5]),
    .out2(out[6]), .in2(in[6]), .out3(out[7]), .in3(in[7]), .cout(cout));
endmodule

module Inc4 (
  input  cin,
  input  in0,
  input  in1,
  input  in2,
  input  in3,
  input  add_sub,
  output out0,
  output out1,
  output out2,
  output out3,
  output cout
);

  wire and_1_out, and_2_out, and_3_out, and_4_out, and_5_out, and_6_out, and_7_out, and_8_out, or_1_out,
       or_2_out, or_3_out;

  xor xor_1 (out0, cin, in0);
  and and_1 (and_1_out, cin, in0, ~add_sub);  // AND_Gate
  and and_2 (and_2_out, cin, ~in0, add_sub);  // AND_Gate
  xor xor_2 (out1, or_1_out, in1);
  and and_3 (and_3_out, or_1_out, in1, ~add_sub);  // AND_Gate
  and and_4 (and_4_out, or_1_out, ~in1, add_sub);  // AND_Gate
  xor xor_3 (out2, or_2_out, in2);
  and and_5 (and_5_out, or_2_out, in2, ~add_sub);  // AND_Gate
  and and_6 (and_6_out, or_2_out, ~in2, add_sub);  // AND_Gate
  xor xor_4 (out3, or_3_out, in3);
  and and_7 (and_7_out, or_3_out, in3, ~add_sub);  // AND_Gate
  and and_8 (and_8_out, or_3_out, ~in3, add_sub);  // AND_Gate
  or or_1 (or_1_out, and_2_out, and_1_out);
  or or_2 (or_2_out, and_4_out, and_3_out);
  or or_3 (or_3_out, and_6_out, and_5_out);
  or or_4 (cout, and_8_out, and_7_out);
endmodule

module BranchChecker (
  input  zero,
  input  sign,
  input  carry,
  input  overflow,
  input  op2,
  input  op1,
  input  op0,
  output result
);

  wire and_1_out, and_2_out, and_3_out, and_4_out, and_5_out, and_6_out, and_7_out, decoder_1_out0,
       decoder_1_out1, decoder_1_out2, decoder_1_out3, decoder_1_out4, decoder_1_out5, decoder_1_out6,
       decoder_1_out7, or_1_out, or_2_out, xor_1_out;

  Decoder #(.select(3), .enable("false")) decoder_1 (
    .out0(decoder_1_out0), .out1(decoder_1_out1), .out2(decoder_1_out2), .out3(decoder_1_out3),
    .out4(decoder_1_out4), .out5(decoder_1_out5), .out6(decoder_1_out6), .out7(decoder_1_out7),
    .sel({op2, op1, op0}));
  or or_1 (or_1_out, zero, xor_1_out);
  or or_2 (or_2_out, carry, zero);
  xor xor_1 (xor_1_out, overflow, sign);
  and and_1 (and_1_out, decoder_1_out1, zero);
  and and_2 (and_2_out, decoder_1_out2, sign);
  and and_3 (and_3_out, decoder_1_out3, overflow);
  and and_4 (and_4_out, decoder_1_out4, carry);
  and and_5 (and_5_out, decoder_1_out5, or_2_out);
  and and_6 (and_6_out, decoder_1_out6, xor_1_out);
  and and_7 (and_7_out, decoder_1_out7, or_1_out);
  or or_3 (result, and_7_out, and_6_out, and_5_out, and_4_out, and_3_out, and_2_out, and_1_out, decoder_1_out0);
endmodule
